// Logisim project Mostafa_Mushsharat_1931298042(L5 Onward).circ as structural Verilog
module _1_bit_ALU (
  input  A,
  input  B,
  input  Cin,
  input  B_Invert,
  input  [1:0] Operation,
  output Result0,
  output Carry0
);

  wire adder_1_out, and_1_out, multiplexer_1_out, multiplier_1_out, not_1_out, or_1_out;

  not not_1 (not_1_out, B);
  Multiplier #(.width(1)) multiplier_1 (.a(B), .b(A), .out(multiplier_1_out));  // open: cin, cout
  and and_1 (and_1_out, B, A);
  or or_1 (or_1_out, B, A);
  Multiplexer multiplexer_1 (.in0(B), .in1(not_1_out), .out(multiplexer_1_out), .sel(B_Invert));  // open: en
  Adder #(.width(1)) adder_1 (.a(A), .b(multiplexer_1_out), .out(adder_1_out), .cin(Cin), .cout(Carry0));
  Multiplexer #(.select(2)) multiplexer_2 (
    .in0(and_1_out), .in1(or_1_out), .in2(adder_1_out), .in3(multiplier_1_out), .out(Result0), .sel(Operation));  // open: en

  // Notes on the sheet:
  //   Name: Mostafa Mushsharat
  //   ID: 1931298042
endmodule

module _16_bit_ALU (
  input  Binvert,
  input  Cin,
  input  [1:0] Operation,
  input  [15:0] A,
  input  [15:0] B,
  output [15:0] Result,
  output Zero_Flag,
  output Overflow,
  output Cout
);

  wire n1_bit_alu_1_carry0, n1_bit_alu_2_carry0, n1_bit_alu_3_carry0, n1_bit_alu_4_carry0,
       n1_bit_alu_5_carry0, n1_bit_alu_6_carry0, n1_bit_alu_7_carry0, n1_bit_alu_8_carry0,
       n1_bit_alu_9_carry0, n1_bit_alu_10_carry0, n1_bit_alu_11_carry0, n1_bit_alu_12_carry0,
       n1_bit_alu_13_carry0, n1_bit_alu_14_carry0, n1_bit_alu_15_carry0;

  _1_bit_ALU u_1_bit_alu_1 (
    .Result0(Result[0]), .Carry0(n1_bit_alu_1_carry0), .A(A[0]), .B(B[0]), .Cin(Cin), .B_Invert(Binvert),
    .Operation(Operation));
  _1_bit_ALU u_1_bit_alu_2 (
    .Result0(Result[1]), .Carry0(n1_bit_alu_2_carry0), .A(A[1]), .B(B[1]), .Cin(n1_bit_alu_1_carry0),
    .B_Invert(Binvert), .Operation(Operation));
  _1_bit_ALU u_1_bit_alu_3 (
    .Result0(Result[2]), .Carry0(n1_bit_alu_3_carry0), .A(A[2]), .B(B[2]), .Cin(n1_bit_alu_2_carry0),
    .B_Invert(Binvert), .Operation(Operation));
  _1_bit_ALU u_1_bit_alu_4 (
    .Result0(Result[3]), .Carry0(n1_bit_alu_4_carry0), .A(A[3]), .B(B[4]), .Cin(n1_bit_alu_3_carry0),
    .B_Invert(Binvert), .Operation(Operation));
  _1_bit_ALU u_1_bit_alu_5 (
    .Result0(Result[4]), .Carry0(n1_bit_alu_5_carry0), .A(A[4]), .B(B[3]), .Cin(n1_bit_alu_4_carry0),
    .B_Invert(Binvert), .Operation(Operation));
  _1_bit_ALU u_1_bit_alu_6 (
    .Result0(Result[5]), .Carry0(n1_bit_alu_6_carry0), .A(A[5]), .B(B[5]), .Cin(n1_bit_alu_5_carry0),
    .B_Invert(Binvert), .Operation(Operation));
  _1_bit_ALU u_1_bit_alu_7 (
    .Result0(Result[6]), .Carry0(n1_bit_alu_7_carry0), .A(A[6]), .B(B[6]), .Cin(n1_bit_alu_6_carry0),
    .B_Invert(Binvert), .Operation(Operation));
  _1_bit_ALU u_1_bit_alu_8 (
    .Result0(Result[7]), .Carry0(n1_bit_alu_8_carry0), .A(A[7]), .B(B[7]), .Cin(n1_bit_alu_7_carry0),
    .B_Invert(Binvert), .Operation(Operation));
  _1_bit_ALU u_1_bit_alu_9 (
    .Result0(Result[8]), .Carry0(n1_bit_alu_9_carry0), .A(A[8]), .B(B[8]), .Cin(n1_bit_alu_8_carry0),
    .B_Invert(Binvert), .Operation(Operation));
  _1_bit_ALU u_1_bit_alu_10 (
    .Result0(Result[9]), .Carry0(n1_bit_alu_10_carry0), .A(A[9]), .B(B[9]), .Cin(n1_bit_alu_9_carry0),
    .B_Invert(Binvert), .Operation(Operation));
  _1_bit_ALU u_1_bit_alu_11 (
    .Result0(Result[10]), .Carry0(n1_bit_alu_11_carry0), .A(A[10]), .B(B[10]), .Cin(n1_bit_alu_10_carry0),
    .B_Invert(Binvert), .Operation(Operation));
  _1_bit_ALU u_1_bit_alu_12 (
    .Result0(Result[11]), .Carry0(n1_bit_alu_12_carry0), .A(A[11]), .B(B[11]), .Cin(n1_bit_alu_11_carry0),
    .B_Invert(Binvert), .Operation(Operation));
  _1_bit_ALU u_1_bit_alu_13 (
    .Result0(Result[12]), .Carry0(n1_bit_alu_13_carry0), .A(A[12]), .B(B[12]), .Cin(n1_bit_alu_12_carry0),
    .B_Invert(Binvert), .Operation(Operation));
  _1_bit_ALU u_1_bit_alu_14 (
    .Result0(Result[13]), .Carry0(n1_bit_alu_14_carry0), .A(A[13]), .B(B[13]), .Cin(n1_bit_alu_13_carry0),
    .B_Invert(Binvert), .Operation(Operation));
  _1_bit_ALU u_1_bit_alu_15 (
    .Result0(Result[14]), .Carry0(n1_bit_alu_15_carry0), .A(A[14]), .B(B[14]), .Cin(n1_bit_alu_14_carry0),
    .B_Invert(Binvert), .Operation(Operation));
  _1_bit_ALU u_1_bit_alu_16 (
    .Result0(Result[15]), .Carry0(Cout), .A(A[15]), .B(B[15]), .Cin(n1_bit_alu_15_carry0),
    .B_Invert(Binvert), .Operation(Operation));
  xor xor_1 (Overflow, Result[15], Cout);
  nor nor_1 (Zero_Flag, Result[0], Result[1], Result[2], Result[3], Result[4], Result[5], Result[6], Result[7], Result[8], Result[9], Result[10], Result[11], Result[12], Result[13], Result[14], Result[15], Cout);

  // Notes on the sheet:
  //   ID: 1931298042
  //   Name: Mostafa Mushsharat
endmodule

module _16_bit_Register_File (
  input  [15:0] Data_Input,
  input  [3:0] RS,
  input  R_W,
  input  [3:0] RD,
  input  [3:0] RT,
  input  Clock,
  output [15:0] out_7,
  output [15:0] out_8
);

  wire demultiplexer_1_out0, demultiplexer_1_out1, demultiplexer_1_out2, demultiplexer_1_out3,
       demultiplexer_1_out4, demultiplexer_1_out5, demultiplexer_1_out6, demultiplexer_1_out7,
       demultiplexer_1_out8, demultiplexer_1_out9, demultiplexer_1_out10, demultiplexer_1_out11,
       demultiplexer_1_out12, demultiplexer_1_out13, demultiplexer_1_out14, demultiplexer_1_out15;
  wire [15:0] register_1_q, register_2_q, register_3_q, register_4_q, register_5_q, register_6_q,
       register_7_q, register_8_q, register_9_q, register_10_q, register_12_q, register_13_q, register_14_q,
       register_15_q, register_16_q;

  Demultiplexer #(.select(4)) demultiplexer_1 (
    .out0(demultiplexer_1_out0), .out1(demultiplexer_1_out1), .out2(demultiplexer_1_out2),
    .out3(demultiplexer_1_out3), .out4(demultiplexer_1_out4), .out5(demultiplexer_1_out5),
    .out6(demultiplexer_1_out6), .out7(demultiplexer_1_out7), .out8(demultiplexer_1_out8),
    .out9(demultiplexer_1_out9), .out10(demultiplexer_1_out10), .out11(demultiplexer_1_out11),
    .out12(demultiplexer_1_out12), .out13(demultiplexer_1_out13), .out14(demultiplexer_1_out14),
    .out15(demultiplexer_1_out15), .in(R_W), .sel(RD));  // open: en
  Register #(.width(16)) register_1 (
    .D(Data_Input), .en(demultiplexer_1_out0), .Q(register_1_q), .clk(Clock));  // open: clr
  Register #(.width(16)) register_2 (
    .D(Data_Input), .en(demultiplexer_1_out1), .Q(register_2_q), .clk(Clock));  // open: clr
  Register #(.width(16)) register_3 (
    .D(Data_Input), .en(demultiplexer_1_out2), .Q(register_3_q), .clk(Clock));  // open: clr
  Register #(.width(16)) register_4 (
    .D(Data_Input), .en(demultiplexer_1_out3), .Q(register_4_q), .clk(Clock));  // open: clr
  Register #(.width(16)) register_5 (
    .D(Data_Input), .en(demultiplexer_1_out4), .Q(register_5_q), .clk(Clock));  // open: clr
  Register #(.width(16)) register_6 (
    .D(Data_Input), .en(demultiplexer_1_out5), .Q(register_6_q), .clk(Clock));  // open: clr
  Register #(.width(16)) register_7 (
    .D(Data_Input), .en(demultiplexer_1_out6), .Q(register_7_q), .clk(Clock));  // open: clr
  Register #(.width(16)) register_8 (
    .D(Data_Input), .en(demultiplexer_1_out7), .Q(register_8_q), .clk(Clock));  // open: clr
  Register #(.width(16)) register_9 (
    .D(Data_Input), .en(demultiplexer_1_out8), .Q(register_9_q), .clk(Clock));  // open: clr
  Register #(.width(16)) register_10 (
    .D(Data_Input), .en(demultiplexer_1_out9), .Q(register_10_q), .clk(Clock));  // open: clr
  Register #(.width(16)) register_11 (
    .D(Data_Input), .en(demultiplexer_1_out10), .Q(register_10_q), .clk(Clock));  // open: clr
  Register #(.width(16)) register_12 (
    .D(Data_Input), .en(demultiplexer_1_out11), .Q(register_12_q), .clk(Clock));  // open: clr
  Register #(.width(16)) register_13 (
    .D(Data_Input), .en(demultiplexer_1_out12), .Q(register_13_q), .clk(Clock));  // open: clr
  Register #(.width(16)) register_14 (
    .D(Data_Input), .en(demultiplexer_1_out13), .Q(register_14_q), .clk(Clock));  // open: clr
  Register #(.width(16)) register_15 (
    .D(Data_Input), .en(demultiplexer_1_out14), .Q(register_15_q), .clk(Clock));  // open: clr
  Register #(.width(16)) register_16 (
    .D(Data_Input), .en(demultiplexer_1_out15), .Q(register_16_q), .clk(Clock));  // open: clr
  Multiplexer #(.select(4), .width(16)) multiplexer_1 (
    .in0(register_1_q), .in1(register_2_q), .in2(register_3_q), .in3(register_4_q), .in4(register_5_q),
    .in5(register_6_q), .in6(register_7_q), .in7(register_8_q), .in8(register_9_q), .in9(register_10_q),
    .in10(register_10_q), .in11(register_12_q), .in12(register_13_q), .in13(register_14_q),
    .in14(register_15_q), .in15(register_16_q), .out(out_7), .sel(RS));  // open: en
  Multiplexer #(.select(4), .width(16)) multiplexer_2 (
    .in0(register_1_q), .in1(register_2_q), .in2(register_3_q), .in3(register_4_q), .in4(register_5_q),
    .in5(register_6_q), .in6(register_7_q), .in7(register_8_q), .in8(register_9_q), .in9(register_10_q),
    .in10(register_10_q), .in11(register_12_q), .in12(register_13_q), .in13(register_14_q),
    .in14(register_15_q), .in15(register_16_q), .out(out_8), .sel(RT));  // open: en

  // Notes on the sheet:
  //   Name: Mostafa Mushsharat
  //   ID: 1931298042
endmodule

module _16_bit_Single_Cycle_Datapath (
  input  Clear,
  input  C_K,
  output Jump,
  output [3:0] Opcode,
  output [3:0] Jump_Value,
  output [15:0] A,
  output [3:0] RS,
  output Branch,
  output [3:0] RT,
  output [15:0] B,
  output [3:0] RD_Immediate,
  output Cin_Sub,
  output Zero_Flag,
  output Write_Enable,
  output RD_RT,
  output Res_mem_ALU,
  output R_I,
  output [1:0] ALU_Op
);

  wire and_1_out, control_unit_1_lw, control_unit_1_mem_en, control_unit_1_sw;
  wire [3:0] adder_1_out, adder_2_out, bit_extender_1_out, multiplexer_1_out, multiplexer_2_out,
       multiplexer_3_out, register_1_q;
  wire [15:0] multiplexer_4_out, multiplexer_5_out, n16_bit_alu_1_result, n16_bit_register_file_1_out_8,
       ram_1_data;

  Multiplexer #(.width(4)) multiplexer_1 (
    .in0(adder_1_out), .in1(adder_2_out), .out(multiplexer_1_out), .sel(and_1_out));  // open: en
  Register #(.width(4)) register_1 (.D(multiplexer_2_out), .Q(register_1_q), .clk(C_K));  // open: en, clr
  Multiplexer #(.width(4)) multiplexer_2 (
    .in0(multiplexer_1_out), .in1(Jump_Value), .out(multiplexer_2_out), .sel(Jump));  // open: en
  Control_Unit control_unit_1 (
    .RD_RT_MUX(RD_RT), .Write_Enable(Write_Enable), .R_I_Type_MUX(R_I), .B_inv_Sub(Cin_Sub),
    .lw(control_unit_1_lw), .sw(control_unit_1_sw), .Mem_En(control_unit_1_mem_en),
    .Res_Mem_ALU_MUX(Res_mem_ALU), .beq(Branch), .jump(Jump), .Opcode(Opcode), .ALU_OP_MUX(ALU_Op));
  Adder #(.width(4)) adder_1 (.a(register_1_q), .b(4'b0001), .out(adder_1_out));  // open: cin, cout
  ROM #(.addrWidth(4), .dataWidth(16)) rom_1 (.addr(register_1_q), .data({Opcode, RS, RT, RD_Immediate}));  // open: sel
  Adder #(.width(4)) adder_2 (.a(adder_1_out), .b(RD_Immediate), .out(adder_2_out));  // open: cin, cout
  Multiplexer #(.width(4)) multiplexer_3 (
    .in0(RD_Immediate), .in1(RT), .out(multiplexer_3_out), .sel(RD_RT));  // open: en
  Bit_Extender #(.in_width(12), .out_width(4)) bit_extender_1 (.in({RS, RT, RD_Immediate}), .out(bit_extender_1_out));
  _16_bit_Register_File u_16_bit_register_file_1 (
    .Data_Input(multiplexer_5_out), .R_W(Write_Enable), .RS(RS), .RD(multiplexer_3_out), .RT(RT),
    .Clock(C_K), .out_7(A), .out_8(n16_bit_register_file_1_out_8));
  assign B = {{12{1'b0}}, RD_Immediate};  // Bit_Extender bit_extender_2
  Adder #(.width(4)) adder_3 (.a(adder_1_out), .b(bit_extender_1_out), .out(Jump_Value));  // open: cin, cout
  Multiplexer #(.width(16)) multiplexer_4 (
    .in0(n16_bit_register_file_1_out_8), .in1(B), .out(multiplexer_4_out), .sel(R_I));  // open: en
  _16_bit_ALU u_16_bit_alu_1 (
    .Binvert(Cin_Sub), .Operation(ALU_Op), .Result(n16_bit_alu_1_result), .A(A), .B(multiplexer_4_out),
    .Cin(Cin_Sub), .Zero_Flag(Zero_Flag));  // open: Cout, Overflow
  and and_1 (and_1_out, Branch, Zero_Flag);
  Multiplexer #(.width(16)) multiplexer_5 (
    .in0(n16_bit_alu_1_result), .in1(ram_1_data), .out(multiplexer_5_out), .sel(Res_mem_ALU));  // open: en
  RAM #(.addrWidth(16), .dataWidth(16), .bus("separate")) ram_1 (
    .addr(n16_bit_alu_1_result), .din(n16_bit_register_file_1_out_8), .data(ram_1_data),
    .str(control_unit_1_sw), .sel(control_unit_1_mem_en), .clk(C_K), .ld(control_unit_1_lw), .clr(Clear));

  // Notes on the sheet:
  //   ID: 1931298042
  //   Name: Mostafa Mushsharat
endmodule

module _16_bit_Pipeline_DataPath (
  input  Clear,
  input  C_K,
  output [3:0] Jump_Value,
  output [3:0] Opcode,
  output [3:0] RS,
  output Branch,
  output [15:0] A,
  output [3:0] RT,
  output [3:0] RD_Immediate,
  output [15:0] B,
  output Cin_Sub,
  output Zero_Flag,
  output RD_RT,
  output Write_Enable,
  output Res_mem_ALU,
  output R_I,
  output [1:0] ALU_Op,
  output [15:0] out_18
);

  wire and_1_out, ex_mem_1_zero_flag_2;
  wire [1:0] control_unit_1_alu_op_mux;
  wire [3:0] adder_1_out, adder_2_out, ex_mem_1_rd_2, id_ex_1_immediate_2, id_ex_1_pc_output,
       if_id_1_pc_output, mem_wb_1_rd_2, multiplexer_1_out, multiplexer_2_out, multiplexer_3_out,
       register_1_q;
  wire [11:0] ex_mem_1_control_2, id_ex_1_control_2;
  wire [11:2] control_unit_1_r_i_type_mux;
  wire [15:0] ex_mem_1_a, ex_mem_1_d, id_ex_1_data2_2, mem_wb_1_a, mem_wb_1_d, multiplexer_4_out,
       multiplexer_5_out, n16_bit_register_file_1_out_7, n16_bit_register_file_1_out_8, ram_1_data,
       rom_1_data;

  Multiplexer #(.width(4)) multiplexer_1 (
    .in0(adder_1_out), .in1(adder_2_out), .out(multiplexer_1_out), .sel(and_1_out));  // open: en
  Register #(.width(4)) register_1 (.D(multiplexer_2_out), .Q(register_1_q), .clk(C_K));  // open: en, clr
  Multiplexer #(.width(4)) multiplexer_2 (
    .in0(multiplexer_1_out), .in1(Jump_Value), .out(multiplexer_2_out), .sel(id_ex_1_control_2[11]));  // open: en
  Adder #(.width(4)) adder_1 (.a(register_1_q), .b(4'b0001), .out(adder_1_out));  // open: cin, cout
  ROM #(.addrWidth(4), .dataWidth(16)) rom_1 (.addr(register_1_q), .data(rom_1_data));  // open: sel
  IF_ID if_id_1 (
    .Instruction(rom_1_data), .PC_output(if_id_1_pc_output),
    .Instruction_Output({Opcode, RS, RT, RD_Immediate}), .C_K(C_K), .PC_in(adder_1_out));
  Control_Unit control_unit_1 (
    .RD_RT_MUX(RD_RT), .Write_Enable(Write_Enable), .R_I_Type_MUX(control_unit_1_r_i_type_mux[2]),
    .B_inv_Sub(control_unit_1_r_i_type_mux[5]), .lw(control_unit_1_r_i_type_mux[6]),
    .sw(control_unit_1_r_i_type_mux[7]), .Mem_En(control_unit_1_r_i_type_mux[8]),
    .Res_Mem_ALU_MUX(control_unit_1_r_i_type_mux[9]), .beq(control_unit_1_r_i_type_mux[10]),
    .jump(control_unit_1_r_i_type_mux[11]), .Opcode(Opcode), .ALU_OP_MUX(control_unit_1_alu_op_mux));
  Multiplexer #(.width(4)) multiplexer_3 (
    .in0(mem_wb_1_rd_2), .in1(RT), .out(multiplexer_3_out), .sel(RD_RT));  // open: en
  _16_bit_Register_File u_16_bit_register_file_1 (
    .Data_Input(multiplexer_5_out), .R_W(Write_Enable), .RS(RS), .RD(multiplexer_3_out), .RT(RT),
    .Clock(C_K), .out_7(n16_bit_register_file_1_out_7), .out_8(n16_bit_register_file_1_out_8));
  ID_EX id_ex_1 (
    .PC_in(if_id_1_pc_output), .Immediate(RD_Immediate),
    .Control({control_unit_1_r_i_type_mux[11:5], control_unit_1_alu_op_mux, control_unit_1_r_i_type_mux[2], Write_Enable, RD_RT}),
    .Data1(n16_bit_register_file_1_out_7), .Data2(n16_bit_register_file_1_out_8),
    .PC_output(id_ex_1_pc_output), .Immediate_2(id_ex_1_immediate_2),
    .Control_2({id_ex_1_control_2[11:6], Cin_Sub, ALU_Op, R_I, id_ex_1_control_2[1:0]}), .Data1_2(A),
    .Data2_2(id_ex_1_data2_2), .C_K(C_K));
  assign B = {{12{1'b0}}, id_ex_1_immediate_2};  // Bit_Extender bit_extender_1
  Adder #(.width(4)) adder_2 (.a(id_ex_1_pc_output), .b(id_ex_1_immediate_2), .out(adder_2_out));  // open: cin, cout
  Multiplexer #(.width(16)) multiplexer_4 (
    .in0(id_ex_1_data2_2), .in1(B), .out(multiplexer_4_out), .sel(R_I));  // open: en
  Adder #(.width(4)) adder_3 (.a(id_ex_1_pc_output), .b(id_ex_1_immediate_2), .out(Jump_Value));  // open: cin, cout
  _16_bit_ALU u_16_bit_alu_1 (
    .Binvert(Cin_Sub), .Operation(ALU_Op), .Result(out_18), .A(A), .B(multiplexer_4_out), .Cin(Cin_Sub),
    .Zero_Flag(Zero_Flag));  // open: Cout, Overflow
  EX_MEM ex_mem_1 (
    .Zero_Flag(Zero_Flag), .Control({id_ex_1_control_2[11:6], Cin_Sub, ALU_Op, R_I, id_ex_1_control_2[1:0]}),
    .Result(out_18), .Data2(id_ex_1_data2_2), .Zero_Flag_2(ex_mem_1_zero_flag_2),
    .Control_2({ex_mem_1_control_2[11], Branch, ex_mem_1_control_2[9:0]}), .A(ex_mem_1_a), .D(ex_mem_1_d),
    .C_K(C_K), .RD(id_ex_1_immediate_2), .RD_2(ex_mem_1_rd_2));
  and and_1 (and_1_out, Branch, ex_mem_1_zero_flag_2);
  RAM #(.addrWidth(16), .dataWidth(16), .bus("separate")) ram_1 (
    .addr(ex_mem_1_a), .din(ex_mem_1_d), .data(ram_1_data), .str(ex_mem_1_control_2[7]),
    .sel(ex_mem_1_control_2[8]), .clk(C_K), .ld(ex_mem_1_control_2[6]), .clr(Clear));
  MEM_WB mem_wb_1 (
    .ResMem_MUX(ex_mem_1_control_2[9]), .Result(ex_mem_1_a), .Data2(ram_1_data), .ResMem_MUX_2(Res_mem_ALU),
    .A(mem_wb_1_a), .D(mem_wb_1_d), .RD(ex_mem_1_rd_2), .RD_2(mem_wb_1_rd_2));  // open: C_K
  Multiplexer #(.width(16)) multiplexer_5 (
    .in0(mem_wb_1_a), .in1(mem_wb_1_d), .out(multiplexer_5_out), .sel(Res_mem_ALU));  // open: en

  // Notes on the sheet:
  //   contents of rom_1 (hex, n*v repeats v):
  //   1
  //   Name: Mostafa Mushsharat
  //   ID: 1931298042
endmodule

module R_Type_Datapath (
  input  in_1,
  input  C_K,
  input  [1:0] ALU_Op,
  output [15:0] A,
  output [3:0] Opcode,
  output [3:0] RS,
  output [15:0] B,
  output [3:0] RT,
  output [3:0] RD_Immediate
);

  wire [3:0] adder_1_out, register_1_q;
  wire [15:0] n16_bit_alu_1_result;

  Register #(.width(4)) register_1 (.D(adder_1_out), .Q(register_1_q), .clk(C_K));  // open: en, clr
  Adder #(.width(4)) adder_1 (.a(register_1_q), .b(4'b0001), .out(adder_1_out));  // open: cin, cout
  ROM #(.addrWidth(4), .dataWidth(16)) rom_1 (.addr(register_1_q), .data({Opcode, RS, RT, RD_Immediate}));  // open: sel
  _16_bit_Register_File u_16_bit_register_file_1 (
    .Data_Input(n16_bit_alu_1_result), .R_W(in_1), .RS(RS), .RD(RD_Immediate), .RT(RT), .Clock(C_K),
    .out_7(A), .out_8(B));
  _16_bit_ALU u_16_bit_alu_1 (
    .Operation(ALU_Op), .Result(n16_bit_alu_1_result), .A(A), .B(B));  // open: Binvert, Cout, Cin, Overflow, Zero_Flag

  // Notes on the sheet:
  //   Name: Mostafa Mushsharat
  //   ID: 1931298042
endmodule

module I_Type_Datapath (
  input  Cin,
  input  SW,
  input  Enable,
  input  LW,
  input  Clear,
  input  in_6,
  input  C_K,
  input  Reg_ALU,
  input  [1:0] ALU_Op,
  output [15:0] A,
  output [3:0] Opcode,
  output [3:0] RS,
  output [15:0] B,
  output [3:0] RT,
  output [3:0] RD_Immediate
);

  wire [3:0] adder_1_out, register_1_q;
  wire [15:0] multiplexer_1_out, n16_bit_alu_1_result, n16_bit_register_file_1_out_8, ram_1_data;

  Register #(.width(4)) register_1 (.D(adder_1_out), .Q(register_1_q), .clk(C_K));  // open: en, clr
  Adder #(.width(4)) adder_1 (.a(register_1_q), .b(4'b0001), .out(adder_1_out));  // open: cin, cout
  ROM #(.addrWidth(4), .dataWidth(16)) rom_1 (.addr(register_1_q), .data({Opcode, RS, RT, RD_Immediate}));  // open: sel
  assign B = {{12{1'b0}}, RD_Immediate};  // Bit_Extender bit_extender_1
  _16_bit_Register_File u_16_bit_register_file_1 (
    .Data_Input(multiplexer_1_out), .R_W(in_6), .RS(RS), .RD(RT), .RT(RT), .Clock(C_K), .out_7(A),
    .out_8(n16_bit_register_file_1_out_8));
  _16_bit_ALU u_16_bit_alu_1 (
    .Operation(ALU_Op), .Result(n16_bit_alu_1_result), .A(A), .B(B), .Cin(Cin));  // open: Binvert, Cout, Overflow, Zero_Flag
  Multiplexer #(.width(16)) multiplexer_1 (
    .in0(n16_bit_alu_1_result), .in1(ram_1_data), .out(multiplexer_1_out), .sel(Reg_ALU));  // open: en
  RAM #(.addrWidth(16), .dataWidth(16), .bus("separate")) ram_1 (
    .addr(n16_bit_alu_1_result), .din(n16_bit_register_file_1_out_8), .data(ram_1_data), .str(SW),
    .sel(Enable), .clk(C_K), .ld(LW), .clr(Clear));

  // Notes on the sheet:
  //   Name: Mostafa Mushsharat
  //   ID: 1931298042
endmodule

module R_I_Type_DataPath (
  input  Clear,
  input  C_K,
  output Jump,
  output [3:0] Opcode,
  output [3:0] Jump_Value,
  output [15:0] A,
  output [3:0] RS,
  output Branch,
  output [3:0] RT,
  output [15:0] B,
  output [3:0] RD_Immediate,
  output Cin_Sub,
  output Zero_Flag,
  output Write_Enable,
  output RD_RT,
  output Res_mem_ALU,
  output R_I,
  output [1:0] ALU_Op
);

  wire and_1_out, control_unit_1_lw, control_unit_1_mem_en, control_unit_1_sw;
  wire [3:0] adder_1_out, adder_2_out, bit_extender_1_out, multiplexer_1_out, multiplexer_2_out,
       multiplexer_3_out, register_1_q;
  wire [15:0] multiplexer_4_out, multiplexer_5_out, n16_bit_alu_1_result, n16_bit_register_file_1_out_8,
       ram_1_data;

  Multiplexer #(.width(4)) multiplexer_1 (
    .in0(adder_1_out), .in1(adder_2_out), .out(multiplexer_1_out), .sel(and_1_out));  // open: en
  Register #(.width(4)) register_1 (.D(multiplexer_2_out), .Q(register_1_q), .clk(C_K));  // open: en, clr
  Multiplexer #(.width(4)) multiplexer_2 (
    .in0(multiplexer_1_out), .in1(Jump_Value), .out(multiplexer_2_out), .sel(Jump));  // open: en
  Control_Unit control_unit_1 (
    .RD_RT_MUX(RD_RT), .Write_Enable(Write_Enable), .R_I_Type_MUX(R_I), .B_inv_Sub(Cin_Sub),
    .lw(control_unit_1_lw), .sw(control_unit_1_sw), .Mem_En(control_unit_1_mem_en),
    .Res_Mem_ALU_MUX(Res_mem_ALU), .beq(Branch), .jump(Jump), .Opcode(Opcode), .ALU_OP_MUX(ALU_Op));
  Adder #(.width(4)) adder_1 (.a(register_1_q), .b(4'b0001), .out(adder_1_out));  // open: cin, cout
  ROM #(.addrWidth(4), .dataWidth(16)) rom_1 (.addr(register_1_q), .data({Opcode, RS, RT, RD_Immediate}));  // open: sel
  Adder #(.width(4)) adder_2 (.a(adder_1_out), .b(RD_Immediate), .out(adder_2_out));  // open: cin, cout
  Multiplexer #(.width(4)) multiplexer_3 (
    .in0(RD_Immediate), .in1(RT), .out(multiplexer_3_out), .sel(RD_RT));  // open: en
  Bit_Extender #(.in_width(12), .out_width(4)) bit_extender_1 (.in({RS, RT, RD_Immediate}), .out(bit_extender_1_out));
  _16_bit_Register_File u_16_bit_register_file_1 (
    .Data_Input(multiplexer_5_out), .R_W(Write_Enable), .RS(RS), .RD(multiplexer_3_out), .RT(RT),
    .Clock(C_K), .out_7(A), .out_8(n16_bit_register_file_1_out_8));
  assign B = {{12{1'b0}}, RD_Immediate};  // Bit_Extender bit_extender_2
  Adder #(.width(4)) adder_3 (.a(adder_1_out), .b(bit_extender_1_out), .out(Jump_Value));  // open: cin, cout
  Multiplexer #(.width(16)) multiplexer_4 (
    .in0(n16_bit_register_file_1_out_8), .in1(B), .out(multiplexer_4_out), .sel(R_I));  // open: en
  _16_bit_ALU u_16_bit_alu_1 (
    .Binvert(Cin_Sub), .Operation(ALU_Op), .Result(n16_bit_alu_1_result), .A(A), .B(multiplexer_4_out),
    .Cin(Cin_Sub), .Zero_Flag(Zero_Flag));  // open: Cout, Overflow
  and and_1 (and_1_out, Branch, Zero_Flag);
  Multiplexer #(.width(16)) multiplexer_5 (
    .in0(n16_bit_alu_1_result), .in1(ram_1_data), .out(multiplexer_5_out), .sel(Res_mem_ALU));  // open: en
  RAM #(.addrWidth(16), .dataWidth(16), .bus("separate")) ram_1 (
    .addr(n16_bit_alu_1_result), .din(n16_bit_register_file_1_out_8), .data(ram_1_data),
    .str(control_unit_1_sw), .sel(control_unit_1_mem_en), .clk(C_K), .ld(control_unit_1_lw), .clr(Clear));

  // Notes on the sheet:
  //   contents of rom_1 (hex, n*v repeats v):
  //   2000
  //   ID: 1931298042
  //   Name: Mostafa Mushsharat
endmodule

module Control_Unit (
  input  [3:0] Opcode,
  output RD_RT_MUX,
  output Write_Enable,
  output R_I_Type_MUX,
  output [1:0] ALU_OP_MUX,
  output B_inv_Sub,
  output lw,
  output sw,
  output Mem_En,
  output Res_Mem_ALU_MUX,
  output beq,
  output jump
);

  wire and_1_out, and_2_out, and_3_out, and_4_out, and_5_out, and_6_out, and_7_out, and_8_out, and_9_out,
       and_10_out, and_11_out, and_12_out, and_13_out, and_14_out, and_15_out, and_16_out, and_17_out,
       and_18_out, and_19_out, and_20_out, and_21_out, and_22_out, and_23_out, and_24_out, and_25_out,
       and_26_out, and_27_out, and_28_out, and_29_out, not_1_out, not_2_out, not_3_out, not_4_out, not_5_out,
       not_6_out, not_7_out, not_8_out, not_9_out, not_10_out, not_11_out, not_12_out, not_13_out,
       not_14_out, not_15_out, not_16_out, not_17_out, not_18_out, not_19_out, not_20_out, not_21_out,
       not_22_out, not_23_out, not_24_out, not_25_out, not_26_out, not_27_out, not_28_out, not_29_out,
       not_30_out, not_31_out, not_32_out, not_33_out, not_34_out, not_35_out, not_36_out;

  not not_1 (not_1_out, Opcode[3]);
  not not_2 (not_2_out, Opcode[0]);
  not not_3 (not_3_out, Opcode[2]);
  not not_4 (not_4_out, Opcode[1]);
  not not_5 (not_5_out, Opcode[2]);
  not not_6 (not_6_out, Opcode[3]);
  not not_7 (not_7_out, Opcode[1]);
  not not_8 (not_8_out, Opcode[3]);
  not not_9 (not_9_out, Opcode[0]);
  not not_10 (not_10_out, Opcode[3]);
  not not_11 (not_11_out, Opcode[2]);
  not not_12 (not_12_out, Opcode[3]);
  not not_13 (not_13_out, Opcode[2]);
  not not_14 (not_14_out, Opcode[1]);
  not not_15 (not_15_out, Opcode[3]);
  not not_16 (not_16_out, Opcode[2]);
  not not_17 (not_17_out, Opcode[0]);
  not not_18 (not_18_out, Opcode[3]);
  not not_19 (not_19_out, Opcode[1]);
  not not_20 (not_20_out, Opcode[2]);
  not not_21 (not_21_out, Opcode[0]);
  not not_22 (not_22_out, Opcode[3]);
  not not_23 (not_23_out, Opcode[2]);
  not not_24 (not_24_out, Opcode[1]);
  not not_25 (not_25_out, Opcode[0]);
  not not_26 (not_26_out, Opcode[3]);
  not not_27 (not_27_out, Opcode[2]);
  not not_28 (not_28_out, Opcode[0]);
  not not_29 (not_29_out, Opcode[3]);
  not not_30 (not_30_out, Opcode[2]);
  not not_31 (not_31_out, Opcode[3]);
  not not_32 (not_32_out, Opcode[2]);
  not not_33 (not_33_out, Opcode[3]);
  not not_34 (not_34_out, Opcode[2]);
  not not_35 (not_35_out, Opcode[0]);
  not not_36 (not_36_out, Opcode[0]);
  and and_1 (and_1_out, Opcode[3], Opcode[2], Opcode[0]);
  and and_2 (and_2_out, Opcode[3], Opcode[2], Opcode[1]);
  and and_3 (and_3_out, not_1_out, Opcode[1], not_2_out);
  and and_4 (and_4_out, Opcode[2], Opcode[1]);
  and and_5 (and_5_out, Opcode[3], not_3_out, not_4_out);
  and and_6 (and_6_out, Opcode[3], not_5_out, Opcode[0]);
  and and_7 (and_7_out, not_6_out, not_7_out);
  and and_8 (and_8_out, not_8_out, not_9_out);
  and and_9 (and_9_out, not_10_out, Opcode[2]);
  and and_10 (and_10_out, Opcode[3], not_11_out);
  and and_11 (and_11_out, not_12_out, Opcode[1]);
  and and_12 (and_12_out, Opcode[1], Opcode[0]);
  and and_13 (and_13_out, Opcode[3], not_13_out, not_14_out);
  and and_14 (and_14_out, not_15_out, not_16_out);
  and and_15 (and_15_out, Opcode[3], Opcode[2], not_17_out);
  and and_16 (and_16_out, not_18_out, Opcode[2], not_19_out, Opcode[0]);
  and and_17 (and_17_out, Opcode[3], not_20_out, not_21_out);
  and and_18 (and_18_out, Opcode[3], Opcode[1]);
  and and_19 (and_19_out, not_22_out, not_23_out, not_24_out, Opcode[0]);
  and and_20 (and_20_out, Opcode[2], Opcode[1], Opcode[0]);
  and and_21 (and_21_out, Opcode[3], Opcode[2], not_25_out);
  and and_22 (and_22_out, not_26_out, not_27_out, Opcode[1], not_28_out);
  and and_23 (and_23_out, Opcode[3], Opcode[2], Opcode[1]);
  and and_24 (and_24_out, not_29_out, not_30_out, Opcode[1], Opcode[0]);
  and and_25 (and_25_out, Opcode[3], Opcode[2], Opcode[1]);
  and and_26 (and_26_out, not_31_out, not_32_out, Opcode[1]);
  and and_27 (and_27_out, Opcode[3], Opcode[2], Opcode[1]);
  and and_28 (and_28_out, not_33_out, not_34_out, Opcode[1], not_35_out);
  and and_29 (and_29_out, Opcode[3], Opcode[2], Opcode[1]);
  and and_30 (beq, Opcode[3], Opcode[2], not_36_out);
  or or_1 (jump, and_1_out, and_2_out);
  or or_2 (RD_RT_MUX, and_3_out, and_4_out, and_5_out, and_6_out);
  or or_3 (Write_Enable, and_7_out, and_8_out, and_9_out, and_10_out);
  or or_4 (R_I_Type_MUX, and_11_out, and_12_out, and_13_out);
  or or_5 (ALU_OP_MUX[1], and_14_out, Opcode[1], and_15_out);
  or or_6 (ALU_OP_MUX[0], and_16_out, and_17_out, and_18_out);
  or or_7 (B_inv_Sub, and_19_out, and_20_out, and_21_out);
  or or_8 (lw, and_22_out, and_23_out);
  or or_9 (sw, and_24_out, and_25_out);
  or or_10 (Mem_En, and_26_out, and_27_out);
  or or_11 (Res_Mem_ALU_MUX, and_28_out, and_29_out);
endmodule

module IF_ID (
  input  [3:0] PC_in,
  input  [15:0] Instruction,
  input  C_K,
  output [3:0] PC_output,
  output [15:0] Instruction_Output
);

  D_Flip_Flop d_ff_1 (.clk(C_K), .D(PC_in[0]), .Q(PC_output[0]));  // open: Qn, preset, en, reset
  D_Flip_Flop d_ff_2 (.clk(C_K), .D(PC_in[1]), .Q(PC_output[1]));  // open: Qn, preset, en, reset
  D_Flip_Flop d_ff_3 (.clk(C_K), .D(PC_in[2]), .Q(PC_output[2]));  // open: Qn, preset, en, reset
  D_Flip_Flop d_ff_4 (.clk(C_K), .D(PC_in[3]), .Q(PC_output[3]));  // open: Qn, preset, en, reset
  D_Flip_Flop d_ff_5 (.clk(C_K), .D(Instruction[0]), .Q(Instruction_Output[0]));  // open: Qn, preset, en, reset
  D_Flip_Flop d_ff_6 (.clk(C_K), .D(Instruction[1]), .Q(Instruction_Output[1]));  // open: Qn, preset, en, reset
  D_Flip_Flop d_ff_7 (.clk(C_K), .D(Instruction[2]), .Q(Instruction_Output[2]));  // open: Qn, preset, en, reset
  D_Flip_Flop d_ff_8 (.clk(C_K), .D(Instruction[3]), .Q(Instruction_Output[3]));  // open: Qn, preset, en, reset
  D_Flip_Flop d_ff_9 (.clk(C_K), .D(Instruction[4]), .Q(Instruction_Output[4]));  // open: Qn, preset, en, reset
  D_Flip_Flop d_ff_10 (.clk(C_K), .D(Instruction[5]), .Q(Instruction_Output[5]));  // open: Qn, preset, en, reset
  D_Flip_Flop d_ff_11 (.clk(C_K), .D(Instruction[6]), .Q(Instruction_Output[6]));  // open: Qn, preset, en, reset
  D_Flip_Flop d_ff_12 (.clk(C_K), .D(Instruction[7]), .Q(Instruction_Output[7]));  // open: Qn, preset, en, reset
  D_Flip_Flop d_ff_13 (.clk(C_K), .D(Instruction[8]), .Q(Instruction_Output[8]));  // open: Qn, preset, en, reset
  D_Flip_Flop d_ff_14 (.clk(C_K), .D(Instruction[9]), .Q(Instruction_Output[9]));  // open: Qn, preset, en, reset
  D_Flip_Flop d_ff_15 (.clk(C_K), .D(Instruction[10]), .Q(Instruction_Output[10]));  // open: Qn, preset, en, reset
  D_Flip_Flop d_ff_16 (.clk(C_K), .D(Instruction[11]), .Q(Instruction_Output[11]));  // open: Qn, preset, en, reset
  D_Flip_Flop d_ff_17 (.clk(C_K), .D(Instruction[12]), .Q(Instruction_Output[12]));  // open: Qn, preset, en, reset
  D_Flip_Flop d_ff_18 (.clk(C_K), .D(Instruction[13]), .Q(Instruction_Output[13]));  // open: Qn, preset, en, reset
  D_Flip_Flop d_ff_19 (.clk(C_K), .D(Instruction[14]), .Q(Instruction_Output[14]));  // open: Qn, preset, en, reset
  D_Flip_Flop d_ff_20 (.clk(C_K), .D(Instruction[15]), .Q(Instruction_Output[15]));  // open: Qn, preset, en, reset
endmodule

module ID_EX (
  input  [3:0] PC_in,
  input  [3:0] Immediate,
  input  [11:0] Control,
  input  [15:0] Data1,
  input  [15:0] Data2,
  input  C_K,
  output [3:0] PC_output,
  output [3:0] Immediate_2,
  output [11:0] Control_2,
  output [15:0] Data1_2,
  output [15:0] Data2_2
);

  D_Flip_Flop d_ff_1 (.clk(C_K), .D(PC_in[0]), .Q(PC_output[0]));  // open: Qn, preset, en, reset
  D_Flip_Flop d_ff_2 (.clk(C_K), .D(PC_in[1]), .Q(PC_output[1]));  // open: Qn, preset, en, reset
  D_Flip_Flop d_ff_3 (.clk(C_K), .D(PC_in[2]), .Q(PC_output[2]));  // open: Qn, preset, en, reset
  D_Flip_Flop d_ff_4 (.clk(C_K), .D(PC_in[3]), .Q(PC_output[3]));  // open: Qn, preset, en, reset
  D_Flip_Flop d_ff_5 (.clk(C_K), .D(Immediate[0]), .Q(Immediate_2[0]));  // open: Qn, preset, en, reset
  D_Flip_Flop d_ff_6 (.clk(C_K), .D(Immediate[1]), .Q(Immediate_2[1]));  // open: Qn, preset, en, reset
  D_Flip_Flop d_ff_7 (.clk(C_K), .D(Immediate[2]), .Q(Immediate_2[2]));  // open: Qn, preset, en, reset
  D_Flip_Flop d_ff_8 (.clk(C_K), .D(Immediate[3]), .Q(Immediate_2[3]));  // open: Qn, preset, en, reset
  D_Flip_Flop d_ff_9 (.clk(C_K), .D(Control[0]), .Q(Control_2[0]));  // open: Qn, preset, en, reset
  D_Flip_Flop d_ff_10 (.clk(C_K), .D(Control[1]), .Q(Control_2[1]));  // open: Qn, preset, en, reset
  D_Flip_Flop d_ff_11 (.clk(C_K), .D(Control[2]), .Q(Control_2[2]));  // open: Qn, preset, en, reset
  D_Flip_Flop d_ff_12 (.clk(C_K), .D(Control[3]), .Q(Control_2[3]));  // open: Qn, preset, en, reset
  D_Flip_Flop d_ff_13 (.clk(C_K), .D(Control[4]), .Q(Control_2[4]));  // open: Qn, preset, en, reset
  D_Flip_Flop d_ff_14 (.clk(C_K), .D(Control[5]), .Q(Control_2[5]));  // open: Qn, preset, en, reset
  D_Flip_Flop d_ff_15 (.clk(C_K), .D(Control[6]), .Q(Control_2[6]));  // open: Qn, preset, en, reset
  D_Flip_Flop d_ff_16 (.clk(C_K), .D(Control[7]), .Q(Control_2[7]));  // open: Qn, preset, en, reset
  D_Flip_Flop d_ff_17 (.clk(C_K), .D(Control[8]), .Q(Control_2[8]));  // open: Qn, preset, en, reset
  D_Flip_Flop d_ff_18 (.clk(C_K), .D(Control[9]), .Q(Control_2[9]));  // open: Qn, preset, en, reset
  D_Flip_Flop d_ff_19 (.clk(C_K), .D(Control[10]), .Q(Control_2[10]));  // open: Qn, preset, en, reset
  D_Flip_Flop d_ff_20 (.clk(C_K), .D(Control[11]), .Q(Control_2[11]));  // open: Qn, preset, en, reset
  D_Flip_Flop d_ff_21 (.clk(C_K), .D(Data1[0]), .Q(Data1_2[0]));  // open: Qn, preset, en, reset
  D_Flip_Flop d_ff_22 (.clk(C_K), .D(Data1[1]), .Q(Data1_2[1]));  // open: Qn, preset, en, reset
  D_Flip_Flop d_ff_23 (.clk(C_K), .D(Data1[2]), .Q(Data1_2[2]));  // open: Qn, preset, en, reset
  D_Flip_Flop d_ff_24 (.clk(C_K), .D(Data1[3]), .Q(Data1_2[3]));  // open: Qn, preset, en, reset
  D_Flip_Flop d_ff_25 (.clk(C_K), .D(Data1[4]), .Q(Data1_2[4]));  // open: Qn, preset, en, reset
  D_Flip_Flop d_ff_26 (.clk(C_K), .D(Data1[5]), .Q(Data1_2[5]));  // open: Qn, preset, en, reset
  D_Flip_Flop d_ff_27 (.clk(C_K), .D(Data1[6]), .Q(Data1_2[6]));  // open: Qn, preset, en, reset
  D_Flip_Flop d_ff_28 (.clk(C_K), .D(Data1[7]), .Q(Data1_2[7]));  // open: Qn, preset, en, reset
  D_Flip_Flop d_ff_29 (.clk(C_K), .D(Data1[8]), .Q(Data1_2[8]));  // open: Qn, preset, en, reset
  D_Flip_Flop d_ff_30 (.clk(C_K), .D(Data1[9]), .Q(Data1_2[9]));  // open: Qn, preset, en, reset
  D_Flip_Flop d_ff_31 (.clk(C_K), .D(Data1[10]), .Q(Data1_2[10]));  // open: Qn, preset, en, reset
  D_Flip_Flop d_ff_32 (.clk(C_K), .D(Data1[11]), .Q(Data1_2[11]));  // open: Qn, preset, en, reset
  D_Flip_Flop d_ff_33 (.clk(C_K), .D(Data1[12]), .Q(Data1_2[12]));  // open: Qn, preset, en, reset
  D_Flip_Flop d_ff_34 (.clk(C_K), .D(Data1[13]), .Q(Data1_2[13]));  // open: Qn, preset, en, reset
  D_Flip_Flop d_ff_35 (.clk(C_K), .D(Data1[14]), .Q(Data1_2[14]));  // open: Qn, preset, en, reset
  D_Flip_Flop d_ff_36 (.clk(C_K), .D(Data1[15]), .Q(Data1_2[15]));  // open: Qn, preset, en, reset
  D_Flip_Flop d_ff_37 (.clk(C_K), .D(Data2[0]), .Q(Data2_2[0]));  // open: Qn, preset, en, reset
  D_Flip_Flop d_ff_38 (.clk(C_K), .D(Data2[1]), .Q(Data2_2[1]));  // open: Qn, preset, en, reset
  D_Flip_Flop d_ff_39 (.clk(C_K), .D(Data2[2]), .Q(Data2_2[2]));  // open: Qn, preset, en, reset
  D_Flip_Flop d_ff_40 (.clk(C_K), .D(Data2[3]), .Q(Data2_2[3]));  // open: Qn, preset, en, reset
  D_Flip_Flop d_ff_41 (.clk(C_K), .D(Data2[4]), .Q(Data2_2[4]));  // open: Qn, preset, en, reset
  D_Flip_Flop d_ff_42 (.clk(C_K), .D(Data2[5]), .Q(Data2_2[5]));  // open: Qn, preset, en, reset
  D_Flip_Flop d_ff_43 (.clk(C_K), .D(Data2[6]), .Q(Data2_2[6]));  // open: Qn, preset, en, reset
  D_Flip_Flop d_ff_44 (.clk(C_K), .D(Data2[7]), .Q(Data2_2[7]));  // open: Qn, preset, en, reset
  D_Flip_Flop d_ff_45 (.clk(C_K), .D(Data2[8]), .Q(Data2_2[8]));  // open: Qn, preset, en, reset
  D_Flip_Flop d_ff_46 (.clk(C_K), .D(Data2[9]), .Q(Data2_2[9]));  // open: Qn, preset, en, reset
  D_Flip_Flop d_ff_47 (.clk(C_K), .D(Data2[10]), .Q(Data2_2[10]));  // open: Qn, preset, en, reset
  D_Flip_Flop d_ff_48 (.clk(C_K), .D(Data2[11]), .Q(Data2_2[11]));  // open: Qn, preset, en, reset
  D_Flip_Flop d_ff_49 (.clk(C_K), .D(Data2[12]), .Q(Data2_2[12]));  // open: Qn, preset, en, reset
  D_Flip_Flop d_ff_50 (.clk(C_K), .D(Data2[13]), .Q(Data2_2[13]));  // open: Qn, preset, en, reset
  D_Flip_Flop d_ff_51 (.clk(C_K), .D(Data2[14]), .Q(Data2_2[14]));  // open: Qn, preset, en, reset
  D_Flip_Flop d_ff_52 (.clk(C_K), .D(Data2[15]), .Q(Data2_2[15]));  // open: Qn, preset, en, reset
endmodule

module EX_MEM (
  input  Zero_Flag,
  input  [3:0] RD,
  input  [11:0] Control,
  input  [15:0] Result,
  input  [15:0] Data2,
  input  C_K,
  output Zero_Flag_2,
  output [3:0] RD_2,
  output [11:0] Control_2,
  output [15:0] A,
  output [15:0] D
);

  wire d_ff_6_qn;

  D_Flip_Flop d_ff_1 (.clk(C_K), .D(Zero_Flag), .Q(Zero_Flag_2));  // open: Qn, preset, en, reset
  D_Flip_Flop d_ff_2 (.clk(C_K), .D(RD[0]), .Q(RD_2[0]));  // open: Qn, preset, en, reset
  D_Flip_Flop d_ff_3 (.clk(C_K), .D(RD[1]), .Q(RD_2[1]));  // open: Qn, preset, en, reset
  D_Flip_Flop d_ff_4 (.clk(C_K), .D(RD[2]), .Q(RD_2[2]));  // open: Qn, preset, en, reset
  D_Flip_Flop d_ff_5 (.clk(C_K), .D(RD[3]), .Q(RD_2[3]));  // open: Qn, preset, en, reset
  D_Flip_Flop d_ff_6 (.clk(C_K), .D(Control[0]), .Q(Control_2[0]), .Qn(d_ff_6_qn));  // open: preset, en, reset
  D_Flip_Flop d_ff_7 (.clk(C_K), .D(Control[1]), .Q(Control_2[1]));  // open: Qn, preset, en, reset
  D_Flip_Flop d_ff_8 (.clk(C_K), .D(Control[2]), .Q(Control_2[2]));  // open: Qn, preset, en, reset
  D_Flip_Flop d_ff_9 (.clk(C_K), .D(Control[3]), .Q(Control_2[3]));  // open: Qn, preset, en, reset
  D_Flip_Flop d_ff_10 (.clk(C_K), .D(Control[4]), .Q(Control_2[4]));  // open: Qn, preset, en, reset
  D_Flip_Flop d_ff_11 (.clk(C_K), .D(Control[5]), .Q(Control_2[5]));  // open: Qn, preset, en, reset
  D_Flip_Flop d_ff_12 (.clk(C_K), .D(Control[6]), .Q(Control_2[6]));  // open: Qn, preset, en, reset
  D_Flip_Flop d_ff_13 (.clk(C_K), .D(Control[7]), .Q(Control_2[7]));  // open: Qn, preset, en, reset
  D_Flip_Flop d_ff_14 (.clk(C_K), .D(Control[8]), .Q(Control_2[8]));  // open: Qn, preset, en, reset
  D_Flip_Flop d_ff_15 (.clk(C_K), .D(Control[9]), .Q(Control_2[9]));  // open: Qn, preset, en, reset
  D_Flip_Flop d_ff_16 (.clk(C_K), .D(Control[10]), .Q(Control_2[10]));  // open: Qn, preset, en, reset
  D_Flip_Flop d_ff_17 (.clk(C_K), .D(Control[11]), .Q(Control_2[11]));  // open: Qn, preset, en, reset
  D_Flip_Flop d_ff_18 (.clk(C_K), .D(Result[0]), .Q(A[0]));  // open: Qn, preset, en, reset
  D_Flip_Flop d_ff_19 (.clk(C_K), .D(Result[1]), .Q(A[1]));  // open: Qn, preset, en, reset
  D_Flip_Flop d_ff_20 (.clk(C_K), .D(Result[2]), .Q(A[2]));  // open: Qn, preset, en, reset
  D_Flip_Flop d_ff_21 (.clk(C_K), .D(Result[3]), .Q(A[3]));  // open: Qn, preset, en, reset
  D_Flip_Flop d_ff_22 (.clk(C_K), .D(Result[4]), .Q(A[4]));  // open: Qn, preset, en, reset
  D_Flip_Flop d_ff_23 (.clk(C_K), .D(Result[5]), .Q(A[5]));  // open: Qn, preset, en, reset
  D_Flip_Flop d_ff_24 (.clk(C_K), .D(Result[6]), .Q(A[6]));  // open: Qn, preset, en, reset
  D_Flip_Flop d_ff_25 (.clk(C_K), .D(Result[7]), .Q(A[7]));  // open: Qn, preset, en, reset
  D_Flip_Flop d_ff_26 (.clk(C_K), .D(Result[8]), .Q(A[8]));  // open: Qn, preset, en, reset
  D_Flip_Flop d_ff_27 (.clk(C_K), .D(Result[9]), .Q(A[9]));  // open: Qn, preset, en, reset
  D_Flip_Flop d_ff_28 (.clk(C_K), .D(Result[10]), .Q(A[10]));  // open: Qn, preset, en, reset
  D_Flip_Flop d_ff_29 (.clk(C_K), .D(Result[11]), .Q(A[11]));  // open: Qn, preset, en, reset
  D_Flip_Flop d_ff_30 (.clk(C_K), .D(Result[12]), .Q(A[12]));  // open: Qn, preset, en, reset
  D_Flip_Flop d_ff_31 (.clk(C_K), .D(Result[13]), .Q(A[13]));  // open: Qn, preset, en, reset
  D_Flip_Flop d_ff_32 (.clk(C_K), .D(Result[14]), .Q(A[14]));  // open: Qn, preset, en, reset
  D_Flip_Flop d_ff_33 (.clk(C_K), .D(Result[15]), .Q(A[15]));  // open: Qn, preset, en, reset
  D_Flip_Flop d_ff_34 (.clk(C_K), .D(Data2[0]), .Q(D[0]));  // open: Qn, preset, en, reset
  D_Flip_Flop d_ff_35 (.clk(C_K), .D(Data2[1]), .Q(D[1]));  // open: Qn, preset, en, reset
  D_Flip_Flop d_ff_36 (.clk(C_K), .D(Data2[2]), .Q(D[2]));  // open: Qn, preset, en, reset
  D_Flip_Flop d_ff_37 (.clk(C_K), .D(Data2[3]), .Q(D[3]));  // open: Qn, preset, en, reset
  D_Flip_Flop d_ff_38 (.clk(C_K), .D(Data2[4]), .Q(D[4]));  // open: Qn, preset, en, reset
  D_Flip_Flop d_ff_39 (.clk(C_K), .D(Data2[5]), .Q(D[5]));  // open: Qn, preset, en, reset
  D_Flip_Flop d_ff_40 (.clk(C_K), .D(Data2[6]), .Q(D[6]));  // open: Qn, preset, en, reset
  D_Flip_Flop d_ff_41 (.clk(C_K), .D(Data2[7]), .Q(D[7]));  // open: Qn, preset, en, reset
  D_Flip_Flop d_ff_42 (.clk(C_K), .D(Data2[8]), .Q(D[8]));  // open: Qn, preset, en, reset
  D_Flip_Flop d_ff_43 (.clk(C_K), .D(Data2[9]), .Q(D[9]));  // open: Qn, preset, en, reset
  D_Flip_Flop d_ff_44 (.clk(C_K), .D(Data2[10]), .Q(D[10]));  // open: Qn, preset, en, reset
  D_Flip_Flop d_ff_45 (.clk(C_K), .D(Data2[11]), .Q(D[11]));  // open: Qn, preset, en, reset
  D_Flip_Flop d_ff_46 (.clk(C_K), .D(Data2[12]), .Q(D[12]));  // open: Qn, preset, en, reset
  D_Flip_Flop d_ff_47 (.clk(C_K), .D(Data2[13]), .Q(D[13]));  // open: Qn, preset, en, reset
  D_Flip_Flop d_ff_48 (.clk(C_K), .D(Data2[14]), .Q(D[14]));  // open: Qn, preset, en, reset
  D_Flip_Flop d_ff_49 (.clk(C_K), .D(Data2[15]), .Q(D[15]));  // open: Qn, preset, en, reset
endmodule

module MEM_WB (
  input  ResMem_MUX,
  input  [3:0] RD,
  input  [15:0] Result,
  input  [15:0] Data2,
  input  C_K,
  output ResMem_MUX_2,
  output [3:0] RD_2,
  output [15:0] A,
  output [15:0] D
);

  D_Flip_Flop d_ff_1 (.clk(C_K), .D(C_K), .Q(ResMem_MUX_2));  // open: Qn, preset, en, reset
  D_Flip_Flop d_ff_2 (.clk(C_K), .D(RD[0]), .Q(RD_2[0]));  // open: Qn, preset, en, reset
  D_Flip_Flop d_ff_3 (.clk(C_K), .D(RD[1]), .Q(RD_2[1]));  // open: Qn, preset, en, reset
  D_Flip_Flop d_ff_4 (.clk(C_K), .D(RD[2]), .Q(RD_2[2]));  // open: Qn, preset, en, reset
  D_Flip_Flop d_ff_5 (.clk(C_K), .D(RD[3]), .Q(RD_2[3]));  // open: Qn, preset, en, reset
  D_Flip_Flop d_ff_6 (.clk(C_K), .D(C_K), .Q(A[0]));  // open: Qn, preset, en, reset
  D_Flip_Flop d_ff_7 (.clk(C_K), .D(Result[1]), .Q(A[1]));  // open: Qn, preset, en, reset
  D_Flip_Flop d_ff_8 (.clk(C_K), .D(Result[2]), .Q(A[2]));  // open: Qn, preset, en, reset
  D_Flip_Flop d_ff_9 (.clk(C_K), .D(Result[3]), .Q(A[3]));  // open: Qn, preset, en, reset
  D_Flip_Flop d_ff_10 (.clk(C_K), .D(Result[4]), .Q(A[4]));  // open: Qn, preset, en, reset
  D_Flip_Flop d_ff_11 (.clk(C_K), .D(Result[5]), .Q(A[5]));  // open: Qn, preset, en, reset
  D_Flip_Flop d_ff_12 (.clk(C_K), .D(Result[6]), .Q(A[6]));  // open: Qn, preset, en, reset
  D_Flip_Flop d_ff_13 (.clk(C_K), .D(Result[7]), .Q(A[7]));  // open: Qn, preset, en, reset
  D_Flip_Flop d_ff_14 (.clk(C_K), .D(Result[8]), .Q(A[8]));  // open: Qn, preset, en, reset
  D_Flip_Flop d_ff_15 (.clk(C_K), .D(Result[9]), .Q(A[9]));  // open: Qn, preset, en, reset
  D_Flip_Flop d_ff_16 (.clk(C_K), .D(Result[10]), .Q(A[10]));  // open: Qn, preset, en, reset
  D_Flip_Flop d_ff_17 (.clk(C_K), .D(Result[11]), .Q(A[11]));  // open: Qn, preset, en, reset
  D_Flip_Flop d_ff_18 (.clk(C_K), .D(Result[12]), .Q(A[12]));  // open: Qn, preset, en, reset
  D_Flip_Flop d_ff_19 (.clk(C_K), .D(Result[13]), .Q(A[13]));  // open: Qn, preset, en, reset
  D_Flip_Flop d_ff_20 (.clk(C_K), .D(Result[14]), .Q(A[14]));  // open: Qn, preset, en, reset
  D_Flip_Flop d_ff_21 (.clk(C_K), .D(Result[15]), .Q(A[15]));  // open: Qn, preset, en, reset
  D_Flip_Flop d_ff_22 (.clk(C_K), .D(Data2[0]), .Q(D[0]));  // open: Qn, preset, en, reset
  D_Flip_Flop d_ff_23 (.clk(C_K), .D(Data2[1]), .Q(D[1]));  // open: Qn, preset, en, reset
  D_Flip_Flop d_ff_24 (.clk(C_K), .D(Data2[2]), .Q(D[2]));  // open: Qn, preset, en, reset
  D_Flip_Flop d_ff_25 (.clk(C_K), .D(Data2[3]), .Q(D[3]));  // open: Qn, preset, en, reset
  D_Flip_Flop d_ff_26 (.clk(C_K), .D(Data2[4]), .Q(D[4]));  // open: Qn, preset, en, reset
  D_Flip_Flop d_ff_27 (.clk(C_K), .D(Data2[5]), .Q(D[5]));  // open: Qn, preset, en, reset
  D_Flip_Flop d_ff_28 (.clk(C_K), .D(Data2[6]), .Q(D[6]));  // open: Qn, preset, en, reset
  D_Flip_Flop d_ff_29 (.clk(C_K), .D(Data2[7]), .Q(D[7]));  // open: Qn, preset, en, reset
  D_Flip_Flop d_ff_30 (.clk(C_K), .D(Data2[8]), .Q(D[8]));  // open: Qn, preset, en, reset
  D_Flip_Flop d_ff_31 (.clk(C_K), .D(Data2[9]), .Q(D[9]));  // open: Qn, preset, en, reset
  D_Flip_Flop d_ff_32 (.clk(C_K), .D(Data2[10]), .Q(D[10]));  // open: Qn, preset, en, reset
  D_Flip_Flop d_ff_33 (.clk(C_K), .D(Data2[11]), .Q(D[11]));  // open: Qn, preset, en, reset
  D_Flip_Flop d_ff_34 (.clk(C_K), .D(Data2[12]), .Q(D[12]));  // open: Qn, preset, en, reset
  D_Flip_Flop d_ff_35 (.clk(C_K), .D(Data2[13]), .Q(D[13]));  // open: Qn, preset, en, reset
  D_Flip_Flop d_ff_36 (.clk(C_K), .D(Data2[14]), .Q(D[14]));  // open: Qn, preset, en, reset
  D_Flip_Flop d_ff_37 (.clk(C_K), .D(Data2[15]), .Q(D[15]));  // open: Qn, preset, en, reset

  assign ResMem_MUX = C_K;
  assign Result[0] = C_K;
endmodule
