// Logisim project Mostafa_Mushsharat_1931298042.circ as structural Verilog: 17 circuits, main circuit AND IC
module AND_IC (
  input  in_1,
  input  in_2,
  input  in_3,
  input  in_4,
  input  in_5,
  input  in_6,
  input  in_7,
  input  in_8,
  input  in_9,
  input  in_10,
  output out_11,
  output out_12,
  output out_13,
  output out_14
);

  and and_1 (out_11, in_2, in_3);
  and and_2 (out_12, in_4, in_5);
  and and_3 (out_13, in_6, in_7);
  and and_4 (out_14, in_8, in_9);
endmodule

module OR_IC (
  input  in_1,
  input  in_2,
  input  in_3,
  input  in_4,
  input  in_5,
  input  in_6,
  input  in_7,
  input  in_8,
  input  in_9,
  input  in_10,
  output out_11,
  output out_12,
  output out_13,
  output out_14
);

  or or_1 (out_11, in_2, in_3);
  or or_2 (out_12, in_4, in_5);
  or or_3 (out_13, in_6, in_7);
  or or_4 (out_14, in_8, in_9);
endmodule

module NOT_IC (
  input  in_1,
  input  in_2,
  input  in_3,
  input  in_4,
  input  in_5,
  input  in_6,
  input  in_7,
  input  in_8,
  output out_9,
  output out_10,
  output out_11,
  output out_12,
  output out_13,
  output out_14
);

  not not_1 (out_9, in_2);
  not not_2 (out_10, in_3);
  not not_3 (out_11, in_4);
  not not_4 (out_12, in_5);
  not not_5 (out_13, in_6);
  not not_6 (out_14, in_7);
endmodule

module XOR_IC (
  input  in_1,
  input  in_2,
  input  in_3,
  input  in_4,
  input  in_5,
  input  in_6,
  input  in_7,
  input  in_8,
  input  in_9,
  input  in_10,
  output out_11,
  output out_12,
  output out_13,
  output out_14
);

  xor xor_1 (out_11, in_2, in_3);
  xor xor_2 (out_12, in_4, in_5);
  xor xor_3 (out_13, in_6, in_7);
  xor xor_4 (out_14, in_8, in_9);
endmodule

module _4_1_MUX_IC (
  input  S0,
  input  S1,
  input  A,
  input  B,
  input  C,
  input  D,
  output Q
);

  wire and_1_out, and_2_out, and_3_out, and_4_out, not_1_out, not_2_out;

  not not_1 (not_1_out, S0);
  not not_2 (not_2_out, S1);
  and and_1 (and_1_out, A, not_2_out, not_1_out);
  and and_2 (and_2_out, B, not_2_out, S0);
  and and_3 (and_3_out, C, S1, not_1_out);
  and and_4 (and_4_out, D, S1, S0);
  or or_1 (Q, and_1_out, and_2_out, and_3_out, and_4_out);
endmodule

module _4_Bit_Adder_IC (
  input  B4,
  input  B3,
  input  B2,
  input  B1,
  input  A4,
  input  A3,
  input  A1,
  input  in_8,
  input  Cin,
  output C,
  output S4,
  output S3,
  output S2,
  output S1
);

  wire and_1_out, and_2_out, and_3_out, and_4_out, and_5_out, and_6_out, and_7_out, and_8_out, or_1_out,
       or_3_out, or_4_out, xor_1_out, xor_2_out, xor_3_out, xor_4_out;

  and and_1 (and_1_out, A3, B3);
  xor xor_1 (xor_1_out, A4, B4);
  and and_2 (and_2_out, A4, B4);
  xor xor_2 (xor_2_out, in_8, B1);
  and and_3 (and_3_out, in_8, B1);
  xor xor_3 (xor_3_out, A1, B2);
  and and_4 (and_4_out, A1, B2);
  xor xor_4 (xor_4_out, A3, B3);
  xor xor_5 (S1, xor_2_out, Cin);
  and and_5 (and_5_out, xor_2_out, Cin);
  xor xor_6 (S2, xor_3_out, or_3_out);
  and and_6 (and_6_out, xor_3_out, or_3_out);
  xor xor_7 (S3, xor_4_out, or_4_out);
  and and_7 (and_7_out, xor_4_out, or_4_out);
  or or_1 (or_1_out, and_7_out, and_1_out);
  xor xor_8 (S4, xor_1_out, or_1_out);
  and and_8 (and_8_out, xor_1_out, or_1_out);
  or or_2 (C, and_8_out, and_2_out);
  or or_3 (or_3_out, and_5_out, and_3_out);
  or or_4 (or_4_out, and_6_out, and_4_out);

  // Notes on the sheet:
  //   A2
endmodule

module D_FF_IC (
  input  Set,
  input  Clock,
  input  Data,
  input  Reset,
  output Q,
  output nQ
);

  wire nand_1_out, nand_2_out, nand_3_out, nand_4_out, not_1_out, not_2_out;

  not not_1 (not_1_out, Set);
  not not_2 (not_2_out, Reset);
  nand nand_1 (nand_1_out, not_1_out, nand_4_out, nand_2_out);
  nand nand_2 (nand_2_out, nand_1_out, Clock, not_2_out);
  nand nand_3 (nand_3_out, nand_2_out, Clock, nand_4_out);
  nand nand_4 (nand_4_out, nand_3_out, Data, not_2_out);
  nand nand_5 (Q, not_1_out, nand_2_out, nQ);
  nand nand_6 (nQ, Q, nand_3_out, not_2_out);
endmodule

module Lab2 (
  input  S1,
  input  S0,
  input  Cin,
  input  A3,
  input  A2,
  input  A1,
  input  A0,
  input  B3,
  input  B2,
  input  B1,
  input  B0,
  output Cout,
  output D3,
  output D2,
  output D1,
  output D0
);

  wire n4_1_mux_ic_1_q, n4_1_mux_ic_2_q, n4_1_mux_ic_3_q, n4_1_mux_ic_4_q, not_ic_1_out_9, not_ic_1_out_10,
       not_ic_1_out_11, not_ic_1_out_12, not_ic_1_out_13;

  NOT_IC not_ic_1 (
    .in_2(B0), .in_3(B1), .in_4(B2), .in_5(B3), .in_6(1'b0), .out_9(not_ic_1_out_9),
    .out_10(not_ic_1_out_10), .out_11(not_ic_1_out_11), .out_12(not_ic_1_out_12), .out_13(not_ic_1_out_13));  // open: in_1, in_7, in_8, out_14
  _4_1_MUX_IC u_4_1_mux_ic_1 (
    .S0(S0), .S1(S1), .A(B0), .B(not_ic_1_out_9), .C(1'b0), .D(not_ic_1_out_13), .Q(n4_1_mux_ic_1_q));
  _4_1_MUX_IC u_4_1_mux_ic_2 (
    .S0(S0), .S1(S1), .A(B1), .B(not_ic_1_out_10), .C(1'b0), .D(not_ic_1_out_13), .Q(n4_1_mux_ic_2_q));
  _4_1_MUX_IC u_4_1_mux_ic_3 (
    .S0(S0), .S1(S1), .A(B2), .B(not_ic_1_out_11), .C(1'b0), .D(not_ic_1_out_13), .Q(n4_1_mux_ic_3_q));
  _4_1_MUX_IC u_4_1_mux_ic_4 (
    .S0(S0), .S1(S1), .A(B3), .B(not_ic_1_out_12), .C(1'b0), .D(not_ic_1_out_13), .Q(n4_1_mux_ic_4_q));
  _4_Bit_Adder_IC u_4_bit_adder_ic_1 (
    .B4(n4_1_mux_ic_4_q), .B3(n4_1_mux_ic_3_q), .B2(n4_1_mux_ic_2_q), .B1(n4_1_mux_ic_1_q), .A4(A3), .A3(A2),
    .A1(A1), .in_8(A0), .Cin(Cin), .C(Cout), .S4(D3), .S3(D2), .S2(D1), .S1(D0));

  // Notes on the sheet:
  //   Name: Mostafa Mushsharat
  //   ID: 1931298042
endmodule

module Lab1 (
  input  A1,
  input  B1,
  input  A2,
  input  B2,
  input  S1,
  input  S2
);

  wire and_ic_1_out_11, and_ic_1_out_12, n4_1_mux_ic_1_q, n4_1_mux_ic_2_q, not_ic_1_out_9, not_ic_1_out_12,
       or_ic_1_out_11, or_ic_1_out_12, xor_ic_1_out_11, xor_ic_1_out_12;

  NOT_IC not_ic_1 (
    .in_2(A1), .in_5(A2), .out_9(not_ic_1_out_9), .out_12(not_ic_1_out_12));  // open: in_1, in_3, in_4, in_6, in_7, in_8, out_10, out_11, out_13, out_14
  AND_IC and_ic_1 (
    .in_2(A1), .in_3(B1), .in_4(A2), .in_5(B2), .out_11(and_ic_1_out_11), .out_12(and_ic_1_out_12));  // open: in_1, in_6, in_7, in_8, in_9, in_10, out_13, out_14
  OR_IC or_ic_1 (
    .in_2(A1), .in_3(B1), .in_4(A2), .in_5(B2), .out_11(or_ic_1_out_11), .out_12(or_ic_1_out_12));  // open: in_1, in_6, in_7, in_8, in_9, in_10, out_13, out_14
  XOR_IC xor_ic_1 (
    .in_2(A1), .in_3(B1), .in_4(A2), .in_5(B2), .out_11(xor_ic_1_out_11), .out_12(xor_ic_1_out_12));  // open: in_1, in_6, in_7, in_8, in_9, in_10, out_13, out_14
  _4_1_MUX_IC u_4_1_mux_ic_1 (
    .S0(S2), .S1(S1), .A(and_ic_1_out_11), .B(or_ic_1_out_11), .C(xor_ic_1_out_11), .D(not_ic_1_out_9),
    .Q(n4_1_mux_ic_1_q));
  LED led_1 (.in(n4_1_mux_ic_1_q));
  _4_1_MUX_IC u_4_1_mux_ic_2 (
    .S0(S2), .S1(S1), .A(and_ic_1_out_12), .B(or_ic_1_out_12), .C(xor_ic_1_out_12), .D(not_ic_1_out_12),
    .Q(n4_1_mux_ic_2_q));
  LED led_2 (.in(n4_1_mux_ic_2_q));

  // Notes on the sheet:
  //   Name: Mostafa Mushsharat
  //   ID: 1931298042
  //   F1
  //   F2
endmodule

module Lab3 (
  input  A4,
  input  A2,
  input  A1,
  input  in_4,
  input  B3,
  input  B2,
  input  B1,
  input  in_8,
  output out_9,
  output S7,
  output S6,
  output S5,
  output S4,
  output S3,
  output S2,
  output S1
);

  wire and_ic_1_out_11, and_ic_1_out_12, and_ic_1_out_13, and_ic_1_out_14, and_ic_2_out_11, and_ic_2_out_12,
       and_ic_2_out_13, and_ic_2_out_14, and_ic_3_out_11, and_ic_3_out_12, and_ic_3_out_13, and_ic_3_out_14,
       and_ic_4_out_11, and_ic_4_out_12, and_ic_4_out_13, n4_bit_adder_ic_2_c, n4_bit_adder_ic_2_s2,
       n4_bit_adder_ic_2_s3, n4_bit_adder_ic_2_s4, n4_bit_adder_ic_3_c, n4_bit_adder_ic_3_s2,
       n4_bit_adder_ic_3_s3, n4_bit_adder_ic_3_s4;

  AND_IC and_ic_1 (
    .in_2(A4), .in_3(B3), .in_4(A4), .in_5(B2), .in_6(A4), .in_7(in_8), .in_8(A4), .in_9(B1),
    .out_11(and_ic_1_out_11), .out_12(and_ic_1_out_12), .out_13(and_ic_1_out_13), .out_14(and_ic_1_out_14));  // open: in_1, in_10
  AND_IC and_ic_2 (
    .in_2(A2), .in_3(B3), .in_4(A2), .in_5(B2), .in_6(A2), .in_7(in_8), .in_8(A2), .in_9(B1),
    .out_11(and_ic_2_out_11), .out_12(and_ic_2_out_12), .out_13(and_ic_2_out_13), .out_14(and_ic_2_out_14));  // open: in_1, in_10
  _4_Bit_Adder_IC u_4_bit_adder_ic_1 (
    .B4(n4_bit_adder_ic_2_c), .B3(n4_bit_adder_ic_2_s4), .B2(n4_bit_adder_ic_2_s3),
    .B1(n4_bit_adder_ic_2_s2), .A4(and_ic_1_out_11), .A3(and_ic_1_out_12), .A1(and_ic_1_out_14),
    .in_8(and_ic_1_out_13), .Cin(1'b0), .C(out_9), .S4(S7), .S3(S6), .S2(S5), .S1(S4));
  AND_IC and_ic_3 (
    .in_2(A1), .in_3(B3), .in_4(A1), .in_5(B2), .in_6(A1), .in_7(in_8), .in_8(B1), .in_9(A1),
    .out_11(and_ic_3_out_11), .out_12(and_ic_3_out_12), .out_13(and_ic_3_out_13), .out_14(and_ic_3_out_14));  // open: in_1, in_10
  _4_Bit_Adder_IC u_4_bit_adder_ic_2 (
    .B4(n4_bit_adder_ic_3_c), .B3(n4_bit_adder_ic_3_s4), .B2(n4_bit_adder_ic_3_s3),
    .B1(n4_bit_adder_ic_3_s2), .A4(and_ic_2_out_11), .A3(and_ic_2_out_12), .A1(and_ic_2_out_14),
    .in_8(and_ic_2_out_13), .Cin(1'b0), .C(n4_bit_adder_ic_2_c), .S4(n4_bit_adder_ic_2_s4),
    .S3(n4_bit_adder_ic_2_s3), .S2(n4_bit_adder_ic_2_s2), .S1(S3));
  _4_Bit_Adder_IC u_4_bit_adder_ic_3 (
    .B4(1'b0), .B3(and_ic_4_out_11), .B2(and_ic_4_out_12), .B1(and_ic_4_out_13), .A4(and_ic_3_out_11),
    .A3(and_ic_3_out_12), .A1(and_ic_3_out_14), .in_8(and_ic_3_out_13), .Cin(1'b0), .C(n4_bit_adder_ic_3_c),
    .S4(n4_bit_adder_ic_3_s4), .S3(n4_bit_adder_ic_3_s3), .S2(n4_bit_adder_ic_3_s2), .S1(S2));
  AND_IC and_ic_4 (
    .in_2(in_4), .in_3(B3), .in_4(in_4), .in_5(B2), .in_6(in_4), .in_7(B1), .in_8(in_4), .in_9(in_8),
    .out_11(and_ic_4_out_11), .out_12(and_ic_4_out_12), .out_13(and_ic_4_out_13), .out_14(S1));  // open: in_1, in_10

  // Notes on the sheet:
  //   A3
  //   B4
  //   S8
  //   ID: 1931298042
  //   Name: Mostafa Mushsharat
endmodule

module lab4 (
  input  Up,
  input  in_2,
  input  Down,
  input  in_4,
  input  in_5,
  input  in_6,
  input  Reset,
  input  Clock,
  output A,
  output B,
  output C,
  output D
);

  wire and_ic_1_out_11, and_ic_1_out_12, and_ic_1_out_13, and_ic_1_out_14, and_ic_2_out_11, and_ic_2_out_12,
       and_ic_2_out_13, d_ff_ic_1_nq, d_ff_ic_2_nq, d_ff_ic_3_nq, not_1_out, or_ic_1_out_11, or_ic_1_out_12,
       or_ic_1_out_13, or_ic_1_out_14, xor_ic_1_out_11, xor_ic_1_out_12, xor_ic_1_out_13, xor_ic_1_out_14;

  not not_1 (not_1_out, Up);
  AND_IC and_ic_1 (
    .in_2(not_1_out), .in_3(Down), .in_4(and_ic_1_out_11), .in_5(d_ff_ic_1_nq), .in_6(Up), .in_7(D),
    .in_8(and_ic_1_out_12), .in_9(d_ff_ic_2_nq), .out_11(and_ic_1_out_11), .out_12(and_ic_1_out_12),
    .out_13(and_ic_1_out_13), .out_14(and_ic_1_out_14));  // open: in_1, in_10
  AND_IC and_ic_2 (
    .in_2(and_ic_1_out_13), .in_3(C), .in_4(and_ic_1_out_14), .in_5(d_ff_ic_3_nq), .in_6(and_ic_2_out_11),
    .in_7(B), .out_11(and_ic_2_out_11), .out_12(and_ic_2_out_12), .out_13(and_ic_2_out_13));  // open: in_1, in_8, in_9, in_10, out_14
  OR_IC or_ic_1 (
    .in_2(Up), .in_3(and_ic_1_out_11), .in_4(and_ic_1_out_13), .in_5(and_ic_1_out_12),
    .in_6(and_ic_2_out_11), .in_7(and_ic_1_out_14), .in_8(and_ic_2_out_12), .in_9(and_ic_2_out_13),
    .out_11(or_ic_1_out_11), .out_12(or_ic_1_out_12), .out_13(or_ic_1_out_13), .out_14(or_ic_1_out_14));  // open: in_1, in_10
  XOR_IC xor_ic_1 (
    .in_2(or_ic_1_out_11), .in_3(D), .in_4(or_ic_1_out_12), .in_5(C), .in_6(or_ic_1_out_13), .in_7(B),
    .in_8(or_ic_1_out_14), .in_9(A), .out_11(xor_ic_1_out_11), .out_12(xor_ic_1_out_12),
    .out_13(xor_ic_1_out_13), .out_14(xor_ic_1_out_14));  // open: in_1, in_10
  D_FF_IC d_ff_ic_1 (.Set(in_2), .Clock(Clock), .Data(xor_ic_1_out_11), .Reset(Reset), .Q(D), .nQ(d_ff_ic_1_nq));
  D_FF_IC d_ff_ic_2 (.Set(in_4), .Clock(Clock), .Data(xor_ic_1_out_12), .Reset(Reset), .Q(C), .nQ(d_ff_ic_2_nq));
  D_FF_IC d_ff_ic_3 (.Set(in_5), .Clock(Clock), .Data(xor_ic_1_out_13), .Reset(Reset), .Q(B), .nQ(d_ff_ic_3_nq));
  D_FF_IC d_ff_ic_4 (.Set(in_6), .Clock(Clock), .Data(xor_ic_1_out_14), .Reset(Reset), .Q(A));  // open: nQ

  // Notes on the sheet:
  //   A
  //   B
  //   E
  //   F
  //   D
  //   C
  //   G
  //   H
  //   I
  //   K
  //   J
  //   ID: 1931290842
  //   Name: Mostafa Mushsharat
  //   L
  //   M
  //   O
  //   N
endmodule

module Task1 (
  input  B4,
  input  B3,
  input  B2,
  input  B1,
  input  A4,
  input  A3,
  input  A2,
  input  A1,
  input  S3,
  input  S2,
  input  S1,
  input  Cin,
  output Cout,
  output D4,
  output D3,
  output D2,
  output D1
);

  wire and_ic_1_out_11, and_ic_1_out_12, and_ic_1_out_13, and_ic_1_out_14, n1bit_full_adder_1_cout,
       n1bit_full_adder_2_cout, n1bit_full_adder_3_cout, n8_1_mux_ic_1_o, n8_1_mux_ic_2_o, n8_1_mux_ic_3_o,
       n8_1_mux_ic_4_o, not_1_out, not_ic_1_out_9, not_ic_1_out_10, not_ic_1_out_11, not_ic_1_out_12,
       not_ic_1_out_13, not_ic_1_out_14, not_ic_2_out_9, not_ic_2_out_10, not_ic_2_out_11, not_ic_2_out_12,
       not_ic_2_out_13, not_ic_2_out_14, or_ic_1_out_11, or_ic_1_out_12, or_ic_1_out_13, or_ic_1_out_14;

  AND_IC and_ic_1 (
    .in_2(A3), .in_3(B3), .in_4(A4), .in_5(B4), .in_6(A2), .in_7(B2), .in_8(A1), .in_9(B1),
    .out_11(and_ic_1_out_11), .out_12(and_ic_1_out_12), .out_13(and_ic_1_out_13), .out_14(and_ic_1_out_14));  // open: in_1, in_10
  OR_IC or_ic_1 (
    .in_2(A3), .in_3(B3), .in_4(A4), .in_5(B4), .in_6(B2), .in_7(A2), .in_8(A1), .in_9(B1),
    .out_11(or_ic_1_out_11), .out_12(or_ic_1_out_12), .out_13(or_ic_1_out_13), .out_14(or_ic_1_out_14));  // open: in_1, in_10
  NOT_IC not_ic_1 (
    .in_2(A3), .in_3(or_ic_1_out_12), .in_4(A4), .in_5(or_ic_1_out_11), .in_6(A2), .in_7(or_ic_1_out_13),
    .out_9(not_ic_1_out_9), .out_10(not_ic_1_out_10), .out_11(not_ic_1_out_11), .out_12(not_ic_1_out_12),
    .out_13(not_ic_1_out_13), .out_14(not_ic_1_out_14));  // open: in_1, in_8
  NOT_IC not_ic_2 (
    .in_2(B4), .in_3(or_ic_1_out_14), .in_4(A1), .in_5(B3), .in_6(B2), .in_7(B1), .out_9(not_ic_2_out_9),
    .out_10(not_ic_2_out_10), .out_11(not_ic_2_out_11), .out_12(not_ic_2_out_12), .out_13(not_ic_2_out_13),
    .out_14(not_ic_2_out_14));  // open: in_1, in_8
  not not_1 (not_1_out, 1'b0);
  _8_1_MUX_IC u_8_1_mux_ic_1 (
    .I1(B1), .I2(not_ic_2_out_14), .I3(1'b0), .I4(not_1_out), .S0(S1), .S1(S2), .S2(S3),
    .I5(and_ic_1_out_14), .I6(or_ic_1_out_14), .I7(not_ic_2_out_10), .I8(not_ic_2_out_11), .O(n8_1_mux_ic_1_o));
  _8_1_MUX_IC u_8_1_mux_ic_2 (
    .I1(B2), .I2(not_ic_2_out_13), .I3(1'b0), .I4(not_1_out), .S0(S1), .S1(S2), .S2(S3),
    .I5(and_ic_1_out_13), .I6(or_ic_1_out_13), .I7(not_ic_1_out_14), .I8(not_ic_1_out_13), .O(n8_1_mux_ic_2_o));
  _8_1_MUX_IC u_8_1_mux_ic_3 (
    .I1(B3), .I2(not_ic_2_out_12), .I3(1'b0), .I4(not_1_out), .S0(S1), .S1(S2), .S2(S3),
    .I5(and_ic_1_out_11), .I6(or_ic_1_out_11), .I7(not_ic_1_out_12), .I8(not_ic_1_out_9), .O(n8_1_mux_ic_3_o));
  _8_1_MUX_IC u_8_1_mux_ic_4 (
    .I1(B4), .I2(not_ic_2_out_9), .I3(1'b0), .I4(not_1_out), .S0(S1), .S1(S2), .S2(S3), .I5(and_ic_1_out_12),
    .I6(or_ic_1_out_12), .I7(not_ic_1_out_10), .I8(not_ic_1_out_11), .O(n8_1_mux_ic_4_o));
  _1Bit_Full_Adder u_1bit_full_adder_1 (.A(A1), .B(n8_1_mux_ic_1_o), .Cin(Cin), .S(D1), .Cout(n1bit_full_adder_1_cout));
  _1Bit_Full_Adder u_1bit_full_adder_2 (
    .A(A2), .B(n8_1_mux_ic_2_o), .Cin(n1bit_full_adder_1_cout), .S(D2), .Cout(n1bit_full_adder_2_cout));
  _1Bit_Full_Adder u_1bit_full_adder_3 (
    .A(A3), .B(n8_1_mux_ic_3_o), .Cin(n1bit_full_adder_2_cout), .S(D3), .Cout(n1bit_full_adder_3_cout));
  _1Bit_Full_Adder u_1bit_full_adder_4 (
    .A(A4), .B(n8_1_mux_ic_4_o), .Cin(n1bit_full_adder_3_cout), .S(D4), .Cout(Cout));

  // Notes on the sheet:
  //   ID: 1931298042
  //   Name: Mostafa Mushsharat
endmodule

module _8_1_MUX_IC (
  input  I1,
  input  I2,
  input  I3,
  input  I4,
  input  S0,
  input  S1,
  input  S2,
  input  I5,
  input  I6,
  input  I7,
  input  I8,
  output O
);

  wire n4_1_mux_ic_1_q, n4_1_mux_ic_2_q;

  _4_1_MUX_IC u_4_1_mux_ic_1 (.S0(S0), .S1(S1), .A(I1), .B(I2), .C(I3), .D(I4), .Q(n4_1_mux_ic_1_q));
  _4_1_MUX_IC u_4_1_mux_ic_2 (.S0(S0), .S1(S1), .A(I5), .B(I6), .C(I7), .D(I8), .Q(n4_1_mux_ic_2_q));
  or or_1 (O, n4_1_mux_ic_1_q, S2, n4_1_mux_ic_2_q);
endmodule

module _1Bit_Full_Adder (
  input  A,
  input  B,
  input  Cin,
  output S,
  output Cout
);

  wire and_1_out, and_2_out, xor_1_out;

  xor xor_1 (xor_1_out, A, B);
  and and_1 (and_1_out, Cin, xor_1_out);
  and and_2 (and_2_out, A, B);
  xor xor_2 (S, xor_1_out, Cin);
  or or_1 (Cout, and_1_out, and_2_out);
endmodule

module Task2 (
  input  D1,
  input  D2,
  input  U2,
  input  U1,
  input  [3:0] Pre_Set,
  input  [3:0] Pre_Set_2,
  output out_7,
  output out_8,
  output out_9,
  output out_10,
  output out_11,
  output out_12,
  output out_13,
  output out_14
);

  wire button_1_out, clock_1_out, lab4_1_a, lab4_1_b, lab4_1_c, lab4_1_d, lab4_2_a, lab4_2_b, lab4_2_c,
       lab4_2_d;

  Clock clock_1 (.out(clock_1_out));
  Button button_1 (.out(button_1_out));
  lab4 lab4_1 (
    .Up(U1), .in_2(Pre_Set[0]), .Down(D2), .in_4(Pre_Set[1]), .in_5(Pre_Set[2]), .in_6(Pre_Set[3]),
    .Reset(button_1_out), .A(lab4_1_a), .B(lab4_1_b), .C(lab4_1_c), .D(lab4_1_d), .Clock(clock_1_out));
  lab4 lab4_2 (
    .Up(U2), .in_2(Pre_Set_2[0]), .Down(D1), .in_4(Pre_Set_2[1]), .in_5(Pre_Set_2[2]), .in_6(Pre_Set_2[3]),
    .Reset(button_1_out), .A(lab4_2_a), .B(lab4_2_b), .C(lab4_2_c), .D(lab4_2_d), .Clock(clock_1_out));
  Lab3 lab3_1 (
    .A4(lab4_1_a), .A2(lab4_1_b), .A1(lab4_1_c), .in_4(lab4_1_d), .B3(lab4_2_a), .B2(lab4_2_b),
    .B1(lab4_2_c), .in_8(lab4_2_d), .out_9(out_7), .S7(out_8), .S6(out_9), .S5(out_10), .S4(out_11),
    .S3(out_12), .S2(out_13), .S1(out_14));
  // Probe on {out_7, out_8, out_9, out_10, out_11, out_12, out_13, out_14}

  // Notes on the sheet:
  //   A
  //   B
  //   Clear
  //   Decimal Result
  //   Results(Decimal)
  //   40
  //   126
  //   104
  //   0
  //   120
  //   180
  //   0
  //   ID: 1931298042
  //   Name: Mostafa Mushsharat
endmodule

module Task3 (
  input  A8,
  input  A7,
  input  A6,
  input  A5,
  input  A4,
  input  A3,
  input  A2,
  input  A1,
  input  B8,
  input  B7,
  input  B6,
  input  B5,
  input  B4,
  input  B3,
  input  B2,
  input  B1,
  output S16,
  output S15,
  output S14,
  output S13,
  output S12,
  output S11,
  output S10,
  output S9,
  output S8,
  output S7,
  output S6,
  output S5,
  output S4,
  output S3,
  output S2,
  output S1
);

  wire lab3_1_out_9, lab3_1_s1, lab3_1_s2, lab3_1_s3, lab3_1_s4, lab3_1_s5, lab3_1_s6, lab3_1_s7,
       lab3_2_out_9, lab3_2_s1, lab3_2_s2, lab3_2_s3, lab3_2_s4, lab3_2_s5, lab3_2_s6, lab3_2_s7,
       lab3_3_out_9, lab3_3_s1, lab3_3_s2, lab3_3_s3, lab3_3_s4, lab3_3_s5, lab3_3_s6, lab3_3_s7,
       lab3_4_out_9, lab3_4_s5, lab3_4_s6, lab3_4_s7, n8bit_carrysaveadder_2_out_26,
       n8bit_carrysaveadder_2_out_27, n8bit_carrysaveadder_2_out_28, n8bit_carrysaveadder_2_out_29,
       n8bit_carrysaveadder_2_out_30;

  _8bit_CarrySaveAdder u_8bit_carrysaveadder_1 (
    .out_27(S16), .out_28(S15), .out_29(S14), .out_30(S13), .out_31(S12), .out_32(S11), .out_33(S10),
    .out_34(S9), .A8(lab3_1_out_9), .A7(lab3_1_s7), .A6(lab3_1_s6), .A5(lab3_1_s5), .A4(lab3_1_s4),
    .A3(lab3_1_s3), .A2(lab3_1_s2), .A1(lab3_1_s1), .B8(1'b0), .B7(1'b0), .B6(1'b0), .B5(1'b0), .B4(1'b0),
    .B3(1'b0), .B2(1'b0), .B1(1'b0), .C8(1'b0), .C7(1'b0), .C6(1'b0), .C5(n8bit_carrysaveadder_2_out_26),
    .C4(n8bit_carrysaveadder_2_out_27), .C3(n8bit_carrysaveadder_2_out_28),
    .C2(n8bit_carrysaveadder_2_out_29), .C1(n8bit_carrysaveadder_2_out_30));  // open: out_25, out_26
  Lab3 lab3_1 (
    .A4(A8), .A2(A7), .A1(A6), .in_4(A5), .B3(B8), .B2(B7), .B1(B6), .in_8(B5), .out_9(lab3_1_out_9),
    .S7(lab3_1_s7), .S6(lab3_1_s6), .S5(lab3_1_s5), .S4(lab3_1_s4), .S3(lab3_1_s3), .S2(lab3_1_s2),
    .S1(lab3_1_s1));
  Lab3 lab3_2 (
    .A4(A8), .A2(A7), .A1(A6), .in_4(A5), .B3(B4), .B2(B3), .B1(B2), .in_8(B1), .out_9(lab3_2_out_9),
    .S7(lab3_2_s7), .S6(lab3_2_s6), .S5(lab3_2_s5), .S4(lab3_2_s4), .S3(lab3_2_s3), .S2(lab3_2_s2),
    .S1(lab3_2_s1));
  _8bit_CarrySaveAdder u_8bit_carrysaveadder_2 (
    .out_26(n8bit_carrysaveadder_2_out_26), .out_27(n8bit_carrysaveadder_2_out_27),
    .out_28(n8bit_carrysaveadder_2_out_28), .out_29(n8bit_carrysaveadder_2_out_29),
    .out_30(n8bit_carrysaveadder_2_out_30), .out_31(S8), .out_32(S7), .out_33(S6), .out_34(S5),
    .A8(lab3_2_out_9), .A7(lab3_2_s7), .A6(lab3_2_s6), .A5(lab3_2_s5), .A4(lab3_2_s4), .A3(lab3_2_s3),
    .A2(lab3_2_s2), .A1(lab3_2_s1), .B8(lab3_3_out_9), .B7(lab3_3_s7), .B6(lab3_3_s6), .B5(lab3_3_s5),
    .B4(lab3_3_s4), .B3(lab3_3_s3), .B2(lab3_3_s2), .B1(lab3_3_s1), .C8(1'b0), .C7(1'b0), .C6(1'b0),
    .C5(1'b0), .C4(lab3_4_out_9), .C3(lab3_4_s7), .C2(lab3_4_s6), .C1(lab3_4_s5));  // open: out_25
  Lab3 lab3_3 (
    .A4(A4), .A2(A3), .A1(A2), .in_4(A1), .B3(B8), .B2(B7), .B1(B6), .in_8(B5), .out_9(lab3_3_out_9),
    .S7(lab3_3_s7), .S6(lab3_3_s6), .S5(lab3_3_s5), .S4(lab3_3_s4), .S3(lab3_3_s3), .S2(lab3_3_s2),
    .S1(lab3_3_s1));
  Lab3 lab3_4 (
    .A4(A4), .A2(A3), .A1(A2), .in_4(A1), .B3(B4), .B2(B3), .B1(B2), .in_8(B1), .out_9(lab3_4_out_9),
    .S7(lab3_4_s7), .S6(lab3_4_s6), .S5(lab3_4_s5), .S4(S4), .S3(S3), .S2(S2), .S1(S1));
  // Probe on {S16, S15, S14, S13, S12, S11, S10, S9, S8, S7, S6, S5, S4, S3, S2, S1}

  // Notes on the sheet:
  //   Decimal Output
  //   Name: Mostafa Mushsharat
  //   ID: 1931298042
endmodule

module _8bit_CarrySaveAdder (
  input  A8,
  input  A7,
  input  A6,
  input  A5,
  input  A4,
  input  A3,
  input  A2,
  input  A1,
  input  B8,
  input  B7,
  input  B6,
  input  B5,
  input  B4,
  input  B3,
  input  B2,
  input  B1,
  input  C8,
  input  C7,
  input  C6,
  input  C5,
  input  C4,
  input  C3,
  input  C2,
  input  C1,
  output out_25,
  output out_26,
  output out_27,
  output out_28,
  output out_29,
  output out_30,
  output out_31,
  output out_32,
  output out_33,
  output out_34
);

  wire n1bit_full_adder_2_cout, n1bit_full_adder_2_s, n1bit_full_adder_3_cout, n1bit_full_adder_4_cout,
       n1bit_full_adder_5_cout, n1bit_full_adder_5_s, n1bit_full_adder_6_cout, n1bit_full_adder_6_s,
       n1bit_full_adder_7_cout, n1bit_full_adder_8_cout, n1bit_full_adder_8_s, n1bit_full_adder_9_cout,
       n1bit_full_adder_10_cout, n1bit_full_adder_10_s, n1bit_full_adder_11_cout, n1bit_full_adder_12_cout,
       n1bit_full_adder_12_s, n1bit_full_adder_13_cout, n1bit_full_adder_14_cout, n1bit_full_adder_14_s,
       n1bit_full_adder_15_cout, n1bit_full_adder_16_cout;

  _1Bit_Full_Adder u_1bit_full_adder_1 (
    .A(n1bit_full_adder_2_cout), .B(1'b0), .Cin(n1bit_full_adder_3_cout), .S(out_26), .Cout(out_25));
  _1Bit_Full_Adder u_1bit_full_adder_2 (
    .A(A8), .B(B8), .Cin(C8), .S(n1bit_full_adder_2_s), .Cout(n1bit_full_adder_2_cout));
  _1Bit_Full_Adder u_1bit_full_adder_3 (
    .A(n1bit_full_adder_5_cout), .B(n1bit_full_adder_2_s), .Cin(n1bit_full_adder_4_cout), .S(out_27),
    .Cout(n1bit_full_adder_3_cout));
  _1Bit_Full_Adder u_1bit_full_adder_4 (
    .A(n1bit_full_adder_6_cout), .B(n1bit_full_adder_5_s), .Cin(n1bit_full_adder_7_cout), .S(out_28),
    .Cout(n1bit_full_adder_4_cout));
  _1Bit_Full_Adder u_1bit_full_adder_5 (
    .A(A7), .B(B7), .Cin(C7), .S(n1bit_full_adder_5_s), .Cout(n1bit_full_adder_5_cout));
  _1Bit_Full_Adder u_1bit_full_adder_6 (
    .A(A6), .B(B6), .Cin(C6), .S(n1bit_full_adder_6_s), .Cout(n1bit_full_adder_6_cout));
  _1Bit_Full_Adder u_1bit_full_adder_7 (
    .A(n1bit_full_adder_8_cout), .B(n1bit_full_adder_6_s), .Cin(n1bit_full_adder_9_cout), .S(out_29),
    .Cout(n1bit_full_adder_7_cout));
  _1Bit_Full_Adder u_1bit_full_adder_8 (
    .A(A5), .B(B5), .Cin(C5), .S(n1bit_full_adder_8_s), .Cout(n1bit_full_adder_8_cout));
  _1Bit_Full_Adder u_1bit_full_adder_9 (
    .A(n1bit_full_adder_10_cout), .B(n1bit_full_adder_8_s), .Cin(n1bit_full_adder_11_cout), .S(out_30),
    .Cout(n1bit_full_adder_9_cout));
  _1Bit_Full_Adder u_1bit_full_adder_10 (
    .A(A4), .B(B4), .Cin(C4), .S(n1bit_full_adder_10_s), .Cout(n1bit_full_adder_10_cout));
  _1Bit_Full_Adder u_1bit_full_adder_11 (
    .A(n1bit_full_adder_12_cout), .B(n1bit_full_adder_10_s), .Cin(n1bit_full_adder_13_cout), .S(out_31),
    .Cout(n1bit_full_adder_11_cout));
  _1Bit_Full_Adder u_1bit_full_adder_12 (
    .A(A3), .B(B3), .Cin(C3), .S(n1bit_full_adder_12_s), .Cout(n1bit_full_adder_12_cout));
  _1Bit_Full_Adder u_1bit_full_adder_13 (
    .A(n1bit_full_adder_14_cout), .B(n1bit_full_adder_12_s), .Cin(n1bit_full_adder_15_cout), .S(out_32),
    .Cout(n1bit_full_adder_13_cout));
  _1Bit_Full_Adder u_1bit_full_adder_14 (
    .A(A2), .B(B2), .Cin(C2), .S(n1bit_full_adder_14_s), .Cout(n1bit_full_adder_14_cout));
  _1Bit_Full_Adder u_1bit_full_adder_15 (
    .A(n1bit_full_adder_16_cout), .B(n1bit_full_adder_14_s), .Cin(1'b0), .S(out_33),
    .Cout(n1bit_full_adder_15_cout));
  _1Bit_Full_Adder u_1bit_full_adder_16 (.A(A1), .B(B1), .Cin(C1), .S(out_34), .Cout(n1bit_full_adder_16_cout));
endmodule
