// Logisim project Team_8_Datapath_1.circ as structural Verilog
module _1_bit_ALU (
  input  A,
  input  B,
  input  Cin,
  input  [1:0] Operation,
  input  A_invert,
  input  in_6,
  output Result_0,
  output Carry0
);

  wire adder_1_out, and_1_out, multiplexer_1_out, multiplexer_2_out, not_1_out, not_2_out, not_3_out,
       or_1_out, or_2_out;

  not not_1 (not_1_out, A);
  or or_1 (or_1_out, B, A);
  not not_2 (not_2_out, or_1_out);
  not not_3 (not_3_out, B);
  Multiplexer multiplexer_1 (.in0(A), .in1(not_1_out), .out(multiplexer_1_out), .sel(A_invert));  // open: en
  and and_1 (and_1_out, B, A);
  or or_2 (or_2_out, B, A);
  Multiplexer multiplexer_2 (.in0(B), .in1(not_3_out), .out(multiplexer_2_out), .sel(in_6));  // open: en
  Adder #(.width(1)) adder_1 (
    .a(multiplexer_1_out), .b(multiplexer_2_out), .out(adder_1_out), .cin(Cin), .cout(Carry0));
  Multiplexer #(.select(2)) multiplexer_3 (
    .in0(and_1_out), .in1(or_2_out), .in2(adder_1_out), .in3(not_2_out), .out(Result_0), .sel(Operation));  // open: en

  // Notes on the sheet:
  //   B-invert
endmodule

module register (
  input  in_1,
  input  [15:0] in_2,
  input  RegWrite,
  input  [3:0] RS,
  input  [3:0] RD,
  input  [3:0] RT,
  output [15:0] out_7,
  output [15:0] out_8
);

  wire and_1_out, and_2_out, and_3_out, and_4_out, and_5_out, and_6_out, and_7_out, and_8_out, and_9_out,
       and_10_out, and_11_out, and_12_out, and_13_out, and_14_out, and_15_out, and_16_out, decoder_1_out0,
       decoder_1_out1, decoder_1_out2, decoder_1_out3, decoder_1_out4, decoder_1_out5, decoder_1_out6,
       decoder_1_out7, decoder_1_out8, decoder_1_out9, decoder_1_out10, decoder_1_out11, decoder_1_out12,
       decoder_1_out13, decoder_1_out14, decoder_1_out15;
  wire [15:0] register_1_q, register_2_q, register_3_q, register_4_q, register_5_q, register_6_q,
       register_7_q, register_8_q, register_9_q, register_10_q, register_11_q, register_12_q, register_13_q,
       register_14_q, register_15_q, register_16_q;

  Decoder #(.select(4)) decoder_1 (
    .out0(decoder_1_out0), .out1(decoder_1_out1), .out2(decoder_1_out2), .out3(decoder_1_out3),
    .out4(decoder_1_out4), .out5(decoder_1_out5), .out6(decoder_1_out6), .out7(decoder_1_out7),
    .out8(decoder_1_out8), .out9(decoder_1_out9), .out10(decoder_1_out10), .out11(decoder_1_out11),
    .out12(decoder_1_out12), .out13(decoder_1_out13), .out14(decoder_1_out14), .out15(decoder_1_out15),
    .sel(RD));  // open: en
  and and_1 (and_1_out, RegWrite, decoder_1_out0);
  and and_2 (and_2_out, RegWrite, decoder_1_out1);
  and and_3 (and_3_out, RegWrite, decoder_1_out2);
  and and_4 (and_4_out, RegWrite, decoder_1_out3);
  and and_5 (and_5_out, RegWrite, decoder_1_out4);
  and and_6 (and_6_out, RegWrite, decoder_1_out5);
  and and_7 (and_7_out, RegWrite, decoder_1_out6);
  and and_8 (and_8_out, RegWrite, decoder_1_out7);
  and and_9 (and_9_out, RegWrite, decoder_1_out8);
  and and_10 (and_10_out, RegWrite, decoder_1_out9);
  and and_11 (and_11_out, RegWrite, decoder_1_out10);
  and and_12 (and_12_out, RegWrite, decoder_1_out11);
  and and_13 (and_13_out, RegWrite, decoder_1_out12);
  and and_14 (and_14_out, RegWrite, decoder_1_out13);
  and and_15 (and_15_out, RegWrite, decoder_1_out14);
  and and_16 (and_16_out, RegWrite, decoder_1_out15);
  Register #(.width(16)) register_1 (.D(in_2), .en(and_1_out), .Q(register_1_q), .clk(in_1));  // open: clr
  Register #(.width(16)) register_2 (.D(in_2), .en(and_2_out), .Q(register_2_q), .clk(in_1));  // open: clr
  Register #(.width(16)) register_3 (.D(in_2), .en(and_3_out), .Q(register_3_q), .clk(in_1));  // open: clr
  Register #(.width(16)) register_4 (.D(in_2), .en(and_4_out), .Q(register_4_q), .clk(in_1));  // open: clr
  Register #(.width(16)) register_5 (.D(in_2), .en(and_5_out), .Q(register_5_q), .clk(in_1));  // open: clr
  Register #(.width(16)) register_6 (.D(in_2), .en(and_6_out), .Q(register_6_q), .clk(in_1));  // open: clr
  Register #(.width(16)) register_7 (.D(in_2), .en(and_7_out), .Q(register_7_q), .clk(in_1));  // open: clr
  Register #(.width(16)) register_8 (.D(in_2), .en(and_8_out), .Q(register_8_q), .clk(in_1));  // open: clr
  Register #(.width(16)) register_9 (.D(in_2), .en(and_9_out), .Q(register_9_q), .clk(in_1));  // open: clr
  Register #(.width(16)) register_10 (.D(in_2), .en(and_10_out), .Q(register_10_q), .clk(in_1));  // open: clr
  Register #(.width(16)) register_11 (.D(in_2), .en(and_11_out), .Q(register_11_q), .clk(in_1));  // open: clr
  Register #(.width(16)) register_12 (.D(in_2), .en(and_12_out), .Q(register_12_q), .clk(in_1));  // open: clr
  Register #(.width(16)) register_13 (.D(in_2), .en(and_13_out), .Q(register_13_q), .clk(in_1));  // open: clr
  Register #(.width(16)) register_14 (.D(in_2), .en(and_14_out), .Q(register_14_q), .clk(in_1));  // open: clr
  Register #(.width(16)) register_15 (.D(in_2), .en(and_15_out), .Q(register_15_q), .clk(in_1));  // open: clr
  Register #(.width(16)) register_16 (.D(in_2), .en(and_16_out), .Q(register_16_q), .clk(in_1));  // open: clr
  Multiplexer #(.select(4), .width(16)) multiplexer_1 (
    .in0(register_1_q), .in1(register_2_q), .in2(register_3_q), .in3(register_4_q), .in4(register_5_q),
    .in5(register_6_q), .in6(register_7_q), .in7(register_8_q), .in8(register_9_q), .in9(register_10_q),
    .in10(register_11_q), .in11(register_12_q), .in12(register_13_q), .in13(register_14_q),
    .in14(register_15_q), .in15(register_16_q), .out(out_7), .sel(RS));  // open: en
  Multiplexer #(.select(4), .width(16)) multiplexer_2 (
    .in0(register_1_q), .in1(register_2_q), .in2(register_3_q), .in3(register_4_q), .in4(register_5_q),
    .in5(register_6_q), .in6(register_7_q), .in7(register_8_q), .in8(register_9_q), .in9(register_10_q),
    .in10(register_11_q), .in11(register_12_q), .in12(register_13_q), .in13(register_14_q),
    .in14(register_15_q), .in15(register_16_q), .out(out_8), .sel(RT));  // open: en

  // Notes on the sheet:
  //   Data In
  //   $ZERO
  //   $s0
  //   $s1
  //   $s2
  //   $s3
  //   $s4
  //   $s5
  //   $s6
  //   $s7
  //   $t0
  //   $t1
  //   $t2
  //   $t3
  //   $t4
  //   $t5
  //   $t6
  //   data_1
  //   data_2
endmodule

module _16_bit_ALU (
  input  A_invert,
  input  B_invert,
  input  Cin,
  input  [15:0] in_4,
  input  [15:0] in_5,
  input  [1:0] Operation,
  output [15:0] Result,
  output out_8,
  output out_9
);

  wire n1_bit_alu_1_carry0, n1_bit_alu_2_carry0, n1_bit_alu_3_carry0, n1_bit_alu_4_carry0,
       n1_bit_alu_5_carry0, n1_bit_alu_6_carry0, n1_bit_alu_7_carry0, n1_bit_alu_8_carry0,
       n1_bit_alu_9_carry0, n1_bit_alu_10_carry0, n1_bit_alu_11_carry0, n1_bit_alu_12_carry0,
       n1_bit_alu_13_carry0, n1_bit_alu_14_carry0, n1_bit_alu_15_carry0, n1_bit_alu_16_carry0;

  _1_bit_ALU u_1_bit_alu_1 (
    .A(in_4[0]), .B(in_5[0]), .Cin(Cin), .Carry0(n1_bit_alu_1_carry0), .Operation(Operation),
    .A_invert(A_invert), .in_6(B_invert), .Result_0(Result[0]));
  _1_bit_ALU u_1_bit_alu_2 (
    .A(in_4[1]), .B(in_5[1]), .Cin(n1_bit_alu_1_carry0), .Carry0(n1_bit_alu_2_carry0), .Operation(Operation),
    .A_invert(A_invert), .in_6(B_invert), .Result_0(Result[1]));
  _1_bit_ALU u_1_bit_alu_3 (
    .A(in_4[2]), .B(in_5[2]), .Cin(n1_bit_alu_2_carry0), .Carry0(n1_bit_alu_3_carry0), .Operation(Operation),
    .A_invert(A_invert), .in_6(B_invert), .Result_0(Result[2]));
  _1_bit_ALU u_1_bit_alu_4 (
    .A(in_4[3]), .B(in_5[3]), .Cin(n1_bit_alu_3_carry0), .Carry0(n1_bit_alu_4_carry0), .Operation(Operation),
    .A_invert(A_invert), .in_6(B_invert), .Result_0(Result[3]));
  _1_bit_ALU u_1_bit_alu_5 (
    .A(in_4[4]), .B(in_5[4]), .Cin(n1_bit_alu_4_carry0), .Carry0(n1_bit_alu_5_carry0), .Operation(Operation),
    .A_invert(A_invert), .in_6(B_invert), .Result_0(Result[4]));
  _1_bit_ALU u_1_bit_alu_6 (
    .A(in_4[5]), .B(in_5[5]), .Cin(n1_bit_alu_5_carry0), .Carry0(n1_bit_alu_6_carry0), .Operation(Operation),
    .A_invert(A_invert), .in_6(B_invert), .Result_0(Result[5]));
  _1_bit_ALU u_1_bit_alu_7 (
    .A(in_4[6]), .B(in_5[6]), .Cin(n1_bit_alu_6_carry0), .Carry0(n1_bit_alu_7_carry0), .Operation(Operation),
    .A_invert(A_invert), .in_6(B_invert), .Result_0(Result[6]));
  _1_bit_ALU u_1_bit_alu_8 (
    .A(in_4[7]), .B(in_5[7]), .Cin(n1_bit_alu_7_carry0), .Carry0(n1_bit_alu_8_carry0), .Operation(Operation),
    .A_invert(A_invert), .in_6(B_invert), .Result_0(Result[7]));
  _1_bit_ALU u_1_bit_alu_9 (
    .A(in_4[8]), .B(in_5[8]), .Cin(n1_bit_alu_8_carry0), .Carry0(n1_bit_alu_9_carry0), .Operation(Operation),
    .A_invert(A_invert), .in_6(B_invert), .Result_0(Result[8]));
  _1_bit_ALU u_1_bit_alu_10 (
    .A(in_4[9]), .B(in_5[9]), .Cin(n1_bit_alu_9_carry0), .Carry0(n1_bit_alu_10_carry0),
    .Operation(Operation), .A_invert(A_invert), .in_6(B_invert), .Result_0(Result[9]));
  _1_bit_ALU u_1_bit_alu_11 (
    .A(in_4[10]), .B(in_5[10]), .Cin(n1_bit_alu_10_carry0), .Carry0(n1_bit_alu_11_carry0),
    .Operation(Operation), .A_invert(A_invert), .in_6(B_invert), .Result_0(Result[10]));
  _1_bit_ALU u_1_bit_alu_12 (
    .A(in_4[11]), .B(in_5[11]), .Cin(n1_bit_alu_11_carry0), .Carry0(n1_bit_alu_12_carry0),
    .Operation(Operation), .A_invert(A_invert), .in_6(B_invert), .Result_0(Result[11]));
  _1_bit_ALU u_1_bit_alu_13 (
    .A(in_4[12]), .B(in_5[12]), .Cin(n1_bit_alu_12_carry0), .Carry0(n1_bit_alu_13_carry0),
    .Operation(Operation), .A_invert(A_invert), .in_6(B_invert), .Result_0(Result[12]));
  _1_bit_ALU u_1_bit_alu_14 (
    .A(in_4[13]), .B(in_5[13]), .Cin(n1_bit_alu_13_carry0), .Carry0(n1_bit_alu_14_carry0),
    .Operation(Operation), .A_invert(A_invert), .in_6(B_invert), .Result_0(Result[13]));
  _1_bit_ALU u_1_bit_alu_15 (
    .A(in_4[14]), .B(in_5[14]), .Cin(n1_bit_alu_14_carry0), .Carry0(n1_bit_alu_15_carry0),
    .Operation(Operation), .A_invert(A_invert), .in_6(B_invert), .Result_0(Result[14]));
  _1_bit_ALU u_1_bit_alu_16 (
    .A(in_4[15]), .B(in_5[15]), .Cin(n1_bit_alu_15_carry0), .Carry0(n1_bit_alu_16_carry0),
    .Operation(Operation), .A_invert(A_invert), .in_6(B_invert), .Result_0(Result[15]));
  xor xor_1 (out_9, n1_bit_alu_15_carry0, n1_bit_alu_16_carry0);
  nor nor_1 (out_8, Result[0], Result[1], Result[2], Result[3], Result[4], Result[5], Result[6], Result[7], Result[8], Result[9], Result[10], Result[11], Result[12], Result[13], Result[14], Result[15]);

  // Notes on the sheet:
  //   Input B
  //   Input A
endmodule

module R_Type_Datapath (
  input  in_1,
  input  in_2,
  input  ALU_op,
  input  [1:0] in_4,
  output [3:0] opcode,
  output [3:0] RS,
  output [3:0] RT,
  output [3:0] RD_Imm
);

  wire clock_1_out;
  wire [3:0] adder_1_out, register_1_q;
  wire [15:0] n16_bit_alu_1_p6, register_2_out_7, register_2_out_8;

  Register #(.width(4)) register_1 (.D(adder_1_out), .Q(register_1_q), .clk(clock_1_out));  // open: en, clr
  Clock clock_1 (.out(clock_1_out));
  Adder #(.width(4)) adder_1 (.a(register_1_q), .b(4'b0001), .out(adder_1_out));  // open: cin, cout
  ROM #(.addrWidth(4), .dataWidth(16)) rom_1 (.addr(register_1_q), .data({RD_Imm, RT, RS, opcode}));  // open: sel
  register register_2 (
    .in_1(clock_1_out), .in_2(n16_bit_alu_1_p6), .RegWrite(in_1), .out_7(register_2_out_7), .RS(RS),
    .RD(RD_Imm), .out_8(register_2_out_8), .RT(RT));
  // _16_bit_ALU 16_bit_alu_1: pin names not known; wires that end beside it: register_2_out_7, register_2_out_8, in_2, ALU_op, in_4, n16_bit_alu_1_p6
endmodule

module I_type_datapath (
  input  in_1,
  input  ALU_op,
  input  [1:0] in_3,
  input  LW,
  input  Clear,
  input  Enable,
  input  sw,
  output [3:0] opcode,
  output [3:0] RS,
  output [3:0] RT,
  output [3:0] RD_Imm,
  output [15:0] out_12,
  output [15:0] out_13
);

  wire clock_1_out;
  wire [3:0] adder_1_out, register_1_q;
  wire [15:0] n16_bit_alu_1_p5, ram_1_data, register_2_out_8;

  Register #(.width(4)) register_1 (.D(adder_1_out), .Q(register_1_q), .clk(clock_1_out));  // open: en, clr
  Clock clock_1 (.out(clock_1_out));
  Adder #(.width(4)) adder_1 (.a(register_1_q), .b(4'b0001), .out(adder_1_out));  // open: cin, cout
  ROM #(.addrWidth(4), .dataWidth(16)) rom_1 (.addr(register_1_q), .data({RD_Imm, RT, RS, opcode}));  // open: sel
  register register_2 (
    .in_1(clock_1_out), .in_2(ram_1_data), .RegWrite(in_1), .out_7(out_12), .RS(RS), .RD(RT),
    .out_8(register_2_out_8), .RT(RT));
  assign out_13 = {{12{1'b0}}, opcode};  // Bit_Extender bit_extender_1
  // _16_bit_ALU 16_bit_alu_1: pin names not known; wires that end beside it: out_12, out_13, ALU_op, in_3, n16_bit_alu_1_p5
  RAM #(.addrWidth(16), .dataWidth(16), .bus("separate")) ram_1 (
    .addr(n16_bit_alu_1_p5), .din(register_2_out_8), .data(ram_1_data), .str(sw), .sel(Enable),
    .clk(clock_1_out), .ld(LW), .clr(Clear));
endmodule

module Combined_Datapath (
  input  R_W,
  input  in_2,
  input  in_3,
  input  ALU_op,
  input  [1:0] in_5,
  input  LW,
  input  Clear,
  input  Enable,
  input  sw,
  input  in_10,
  output [3:0] opcode,
  output [3:0] RS,
  output [3:0] RT,
  output [3:0] RD_Imm,
  output [15:0] out_15,
  output [15:0] out_16
);

  wire clock_1_out;
  wire [3:0] adder_1_out, multiplexer_1_out, register_1_q;
  wire [15:0] multiplexer_3_out, n16_bit_alu_1_p2, n16_bit_alu_1_p6, ram_1_data, register_2_out_8;

  Register #(.width(4)) register_1 (.D(adder_1_out), .Q(register_1_q), .clk(clock_1_out));  // open: en, clr
  Clock clock_1 (.out(clock_1_out));
  Adder #(.width(4)) adder_1 (.a(register_1_q), .b(4'b0001), .out(adder_1_out));  // open: cin, cout
  ROM #(.addrWidth(4), .dataWidth(16)) rom_1 (.addr(register_1_q), .data({RD_Imm, RT, RS, opcode}));  // open: sel
  Multiplexer #(.width(4)) multiplexer_1 (.in0(RT), .in1(opcode), .out(multiplexer_1_out), .sel(in_3));  // open: en
  register register_2 (
    .in_1(clock_1_out), .in_2(multiplexer_3_out), .RegWrite(R_W), .out_7(out_15), .RS(RS),
    .RD(multiplexer_1_out), .out_8(register_2_out_8), .RT(RT));
  assign out_16 = {{12{1'b0}}, opcode};  // Bit_Extender bit_extender_1
  // _16_bit_ALU 16_bit_alu_1: pin names not known; wires that end beside it: out_15, n16_bit_alu_1_p2, ALU_op, ALU_op, in_5, n16_bit_alu_1_p6
  Multiplexer #(.width(16)) multiplexer_2 (
    .in0(register_2_out_8), .in1(out_16), .out(n16_bit_alu_1_p2), .sel(in_10));  // open: en
  RAM #(.addrWidth(16), .dataWidth(16), .bus("separate")) ram_1 (
    .addr(n16_bit_alu_1_p6), .din(register_2_out_8), .data(ram_1_data), .str(sw), .sel(Enable),
    .clk(clock_1_out), .ld(LW), .clr(Clear));
  Multiplexer #(.width(16)) multiplexer_3 (
    .in0(n16_bit_alu_1_p6), .in1(ram_1_data), .out(multiplexer_3_out), .sel(in_2));  // open: en
endmodule

module pipelined (
  input  Jump,
  input  in_2,
  input  R_W,
  input  ALU_Memory,
  input  RD_RT,
  input  Sub,
  input  [1:0] ALU_op,
  input  LW,
  input  Clear,
  input  Enable,
  input  sw,
  input  in_12,
  output [3:0] opcode,
  output [3:0] RS,
  output [3:0] RT,
  output [3:0] RD_Imm,
  output [15:0] out_17,
  output out_18,
  output [15:0] out_19
);

  wire and_1_out, clock_1_out;
  wire [3:0] multiplexer_3_out;
  wire [15:0] adder_1_out, adder_2_out, adder_3_out, bit_extender_2_out, multiplexer_1_out,
       multiplexer_2_out, multiplexer_4_out, multiplexer_5_out, n16_bit_alu_1_p6, ram_1_data, register_1_q,
       register_2_out_8;

  Register #(.width(16)) register_1 (.D(multiplexer_1_out), .Q(register_1_q), .clk(clock_1_out));  // open: en, clr
  Clock clock_1 (.out(clock_1_out));
  Multiplexer #(.width(16)) multiplexer_1 (
    .in0(multiplexer_2_out), .in1(adder_3_out), .out(multiplexer_1_out), .sel(Jump));  // open: en
  Multiplexer #(.width(16)) multiplexer_2 (
    .in0(adder_1_out), .in1(adder_2_out), .out(multiplexer_2_out), .sel(and_1_out));  // open: en
  Adder #(.width(16)) adder_1 (.a(register_1_q), .b(16'h1), .out(adder_1_out));  // open: cin, cout
  ROM #(.addrWidth(16), .dataWidth(16)) rom_1 (.addr(register_1_q), .data({opcode, RS, RT, RD_Imm}));  // open: sel
  Multiplexer #(.width(4)) multiplexer_3 (.in0(RD_Imm), .in1(RT), .out(multiplexer_3_out), .sel(RD_RT));  // open: en
  register register_2 (
    .in_1(clock_1_out), .in_2(multiplexer_5_out), .RegWrite(R_W), .out_7(out_17), .RS(RS),
    .RD(multiplexer_3_out), .out_8(register_2_out_8), .RT(RT));
  Multiplexer #(.width(16)) multiplexer_4 (
    .in0(register_2_out_8), .in1(out_19), .out(multiplexer_4_out), .sel(in_12));  // open: en
  assign out_19 = {{12{1'b0}}, RD_Imm};  // Bit_Extender bit_extender_1
  Adder #(.width(16)) adder_2 (.a(adder_1_out), .b(out_19), .out(adder_2_out));  // open: cin, cout
  // _16_bit_ALU 16_bit_alu_1: pin names not known; wires that end beside it: out_17, multiplexer_4_out, Sub, Sub, ALU_op, n16_bit_alu_1_p6, out_18
  and and_1 (and_1_out, in_2, out_18);
  RAM #(.addrWidth(16), .dataWidth(16), .bus("separate")) ram_1 (
    .addr(n16_bit_alu_1_p6), .din(register_2_out_8), .data(ram_1_data), .str(sw), .sel(Enable),
    .clk(clock_1_out), .ld(LW), .clr(Clear));
  assign bit_extender_2_out = {{4{1'b0}}, {RS, RT, RD_Imm}};  // Bit_Extender bit_extender_2
  Adder #(.width(16)) adder_3 (.a(bit_extender_2_out), .b(adder_1_out), .out(adder_3_out));  // open: cin, cout
  Multiplexer #(.width(16)) multiplexer_5 (
    .in0(n16_bit_alu_1_p6), .in1(ram_1_data), .out(multiplexer_5_out), .sel(ALU_Memory));  // open: en

  // Notes on the sheet:
  //   contents of rom_1 (hex, n*v repeats v):
  //   c127
  //   R/I-Type
  //   Branch
endmodule

module pipelined_2 (
  input  Branch,
  input  [1:0] in_2,
  input  in_3,
  input  in_4,
  input  RD_RT,
  input  Write_enable,
  input  R_I_type,
  input  [1:0] ALU_op,
  input  B_inv,
  input  lw,
  input  sw,
  input  Mem_Enable,
  input  in_13,
  input  beq,
  input  jump,
  output [15:0] out_16,
  output [15:0] Rs,
  output [3:0] opcode,
  output [3:0] RD,
  output [3:0] RS_2,
  output [3:0] RT,
  output out_22,
  output [15:0] out_23,
  output [15:0] out_24
);

  wire and_1_out, clock_1_out, xor_1_out;
  wire [3:0] bit_extender_2_out, rom_1_data;
  wire [15:0] adder_1_out, adder_2_out, adder_3_out, bit_extender_1_out, bit_extender_3_out,
       multiplexer_1_out, multiplexer_2_out, multiplexer_4_out, n16_bit_alu_1_result, ram_1_data,
       register_1_q, register_2_out_8;

  Register #(.width(16)) register_1 (.D(multiplexer_1_out), .Q(register_1_q), .clk(clock_1_out));  // open: en, clr
  Clock clock_1 (.out(clock_1_out));
  Multiplexer #(.width(16)) multiplexer_1 (
    .in0(multiplexer_2_out), .in1(adder_3_out), .out(multiplexer_1_out), .sel(jump));  // open: en
  Adder #(.width(16)) adder_1 (.a(register_1_q), .b(16'h1), .out(adder_1_out));  // open: cin, cout
  Multiplexer #(.width(16)) multiplexer_2 (
    .in0(adder_1_out), .in1(adder_2_out), .out(multiplexer_2_out), .sel(and_1_out));  // open: en
  ROM #(.addrWidth(16), .dataWidth(16)) rom_1 (
    .addr(register_1_q), .data({opcode, RD, RS_2, rom_1_data}));  // open: sel
  Multiplexer #(.width(4)) multiplexer_3 (.in0(rom_1_data), .in1(RD), .out(RT), .sel(RD_RT));  // open: en
  Multiplexer #(.select(2), .width(16)) multiplexer_4 (
    .in1(Rs), .in2(Rs), .out(multiplexer_4_out), .sel(in_2));  // open: in0, in3, en
  register register_2 (
    .in_1(clock_1_out), .in_2(out_24), .RegWrite(Write_enable), .out_7(Rs), .RS(RS_2), .RD(RD),
    .out_8(register_2_out_8), .RT(RT));
  assign bit_extender_1_out = {{12{1'b0}}, rom_1_data};  // Bit_Extender bit_extender_1
  Adder #(.width(16)) adder_2 (.a(adder_1_out), .b(bit_extender_1_out), .out(adder_2_out));  // open: cin, cout
  Multiplexer #(.width(16)) multiplexer_5 (
    .in0(register_2_out_8), .in1(bit_extender_1_out), .out(out_23), .sel(R_I_type));  // open: en
  _16_bit_ALU u_16_bit_alu_1 (
    .A_invert(in_4), .B_invert(B_inv), .Cin(B_inv), .in_4(Rs), .in_5(out_23), .Operation(ALU_op),
    .Result(n16_bit_alu_1_result), .out_8(out_22));  // open: out_9
  xor xor_1 (xor_1_out, Branch, out_22);
  Bit_Extender #(.in_width(16), .out_width(4)) bit_extender_2 (.in(out_23), .out(bit_extender_2_out));
  RAM #(.addrWidth(16), .dataWidth(16), .bus("separate")) ram_1 (
    .addr(n16_bit_alu_1_result), .din(register_2_out_8), .data(ram_1_data), .str(sw), .sel(Mem_Enable),
    .clk(clock_1_out), .ld(lw), .clr(in_3));
  assign bit_extender_3_out = {{4{1'b0}}, {RD, RS_2, RT}};  // Bit_Extender bit_extender_3
  and and_1 (and_1_out, beq, xor_1_out);
  Multiplexer #(.width(16)) multiplexer_6 (
    .in0(n16_bit_alu_1_result), .in1(ram_1_data), .out(out_24), .sel(in_13));  // open: en
  Adder #(.width(16)) adder_3 (.a(bit_extender_3_out), .b(adder_1_out), .out(adder_3_out));  // open: cin, cout
  Shifter_part #(.width(16)) shifter_1 (.in(multiplexer_4_out), .\dist (bit_extender_2_out), .out(out_16));
  Shifter_part #(.width(16), .shift("lr")) shifter_2 (
    .in(multiplexer_4_out), .\dist (bit_extender_2_out), .out(out_16));

  // Notes on the sheet:
  //   Result Mem/ ALU MUX
  //   contents of rom_1 (hex, n*v repeats v):
  //   342 1354 3123 5*0 2345 2456
  //   R/I-Type
  //   Rt
  //   ALU/Memory
  //   Sll
  //   Srl
endmodule

module Control_Unit (
  input  [3:0] Opcode,
  output RD_RT_mux,
  output WriteEnable,
  output R_I_MUX,
  output [1:0] AluOp,
  output Binv_Sub,
  output lw,
  output sw,
  output MemEnable,
  output Res_Mem_Alu_MUX,
  output beq,
  output jump
);

  wire and_1_out, and_2_out, and_3_out, and_4_out, and_5_out, and_6_out, and_7_out, and_8_out, and_9_out,
       and_10_out, and_11_out, and_12_out, and_13_out, and_14_out, and_15_out, and_16_out, and_19_out,
       and_20_out, not_1_out, not_2_out, not_3_out, not_4_out, not_5_out, not_6_out, not_7_out, not_8_out,
       not_9_out, not_10_out, not_11_out, not_12_out, not_13_out, not_14_out, not_15_out, not_16_out,
       not_17_out, not_18_out, not_19_out, not_20_out, not_21_out, not_22_out, not_23_out, not_24_out,
       not_25_out, not_26_out, not_27_out, not_28_out, not_29_out, not_30_out, not_31_out, not_32_out,
       not_33_out, not_34_out, not_35_out, not_36_out, not_37_out, not_38_out, not_39_out, not_40_out,
       not_41_out, not_42_out, or_3_out;

  not not_1 (not_1_out, Opcode[3]);
  not not_2 (not_2_out, Opcode[2]);
  not not_3 (not_3_out, Opcode[0]);
  not not_4 (not_4_out, Opcode[3]);
  not not_5 (not_5_out, Opcode[1]);
  not not_6 (not_6_out, Opcode[0]);
  not not_7 (not_7_out, Opcode[3]);
  not not_8 (not_8_out, Opcode[2]);
  not not_9 (not_9_out, Opcode[1]);
  not not_10 (not_10_out, Opcode[2]);
  not not_11 (not_11_out, Opcode[1]);
  not not_12 (not_12_out, Opcode[2]);
  not not_13 (not_13_out, Opcode[0]);
  not not_14 (not_14_out, Opcode[2]);
  not not_15 (not_15_out, Opcode[1]);
  not not_16 (not_16_out, Opcode[2]);
  not not_17 (not_17_out, Opcode[0]);
  not not_18 (not_18_out, Opcode[3]);
  not not_19 (not_19_out, Opcode[0]);
  not not_20 (not_20_out, Opcode[1]);
  not not_21 (not_21_out, Opcode[3]);
  not not_22 (not_22_out, Opcode[3]);
  not not_23 (not_23_out, Opcode[3]);
  not not_24 (not_24_out, Opcode[2]);
  not not_25 (not_25_out, Opcode[1]);
  not not_26 (not_26_out, Opcode[3]);
  not not_27 (not_27_out, Opcode[0]);
  not not_28 (not_28_out, Opcode[1]);
  not not_29 (not_29_out, Opcode[2]);
  not not_30 (not_30_out, Opcode[1]);
  not not_31 (not_31_out, Opcode[2]);
  not not_32 (not_32_out, Opcode[0]);
  not not_33 (not_33_out, Opcode[2]);
  not not_34 (not_34_out, Opcode[1]);
  not not_35 (not_35_out, Opcode[2]);
  not not_36 (not_36_out, Opcode[0]);
  not not_37 (not_37_out, Opcode[2]);
  not not_38 (not_38_out, Opcode[1]);
  not not_39 (not_39_out, Opcode[1]);
  and and_1 (and_1_out, not_1_out, not_2_out, Opcode[1], not_3_out);
  and and_2 (and_2_out, not_4_out, Opcode[2], not_5_out, not_6_out);
  and and_3 (and_3_out, not_7_out, Opcode[2], Opcode[1], Opcode[0]);
  not not_40 (not_40_out, Opcode[2]);
  and and_4 (and_4_out, Opcode[3], not_40_out, not_41_out);
  not not_41 (not_41_out, Opcode[1]);
  not not_42 (not_42_out, Opcode[3]);
  and and_5 (and_5_out, not_8_out, not_9_out);
  and and_6 (and_6_out, Opcode[3], not_10_out, not_11_out, Opcode[0]);
  and and_7 (and_7_out, Opcode[3], not_12_out, Opcode[1], not_13_out);
  and and_8 (and_8_out, not_14_out, not_15_out);
  and and_9 (and_9_out, not_16_out, not_17_out);
  and and_10 (and_10_out, not_18_out, Opcode[1], not_19_out);
  and and_11 (and_11_out, Opcode[3], not_20_out, Opcode[0]);
  and and_12 (and_12_out, not_21_out, Opcode[2], Opcode[0]);
  and and_13 (and_13_out, not_22_out, Opcode[2], Opcode[1]);
  and and_14 (and_14_out, not_23_out, not_24_out, not_25_out, Opcode[0]);
  and and_15 (and_15_out, not_26_out, Opcode[2], Opcode[1], not_27_out);
  and and_16 (and_16_out, Opcode[3], Opcode[2], not_28_out, Opcode[0]);
  and and_17 (lw, Opcode[3], not_29_out, not_30_out, Opcode[0]);
  and and_18 (sw, Opcode[3], not_31_out, Opcode[1], not_32_out);
  and and_19 (and_19_out, Opcode[3], not_33_out, not_34_out, Opcode[0]);
  and and_20 (and_20_out, Opcode[3], not_35_out, Opcode[1], not_36_out);
  and and_21 (Res_Mem_Alu_MUX, Opcode[3], not_37_out, not_38_out, Opcode[0]);
  and and_22 (beq, Opcode[3], Opcode[2], not_39_out, Opcode[0]);
  and and_23 (jump, Opcode[3], Opcode[2], Opcode[1], Opcode[0]);
  or or_1 (RD_RT_mux, and_1_out, and_2_out, and_3_out, and_4_out);
  or or_2 (WriteEnable, not_42_out, and_5_out);
  or or_3 (or_3_out, and_6_out, and_7_out);
  or or_4 (AluOp[1], and_8_out, and_9_out, and_10_out, and_11_out);
  or or_5 (AluOp[0], and_12_out, and_13_out);
  or or_6 (Binv_Sub, and_14_out, and_15_out, and_16_out);
  or or_7 (MemEnable, and_19_out, and_20_out);
  not not_43 (R_I_MUX, or_3_out);
endmodule

module Datapath_1 (
  input  _0,
  input  _1,
  input  _2,
  input  _3,
  input  blt_beq,
  input  _4,
  input  _5,
  input  in_8,
  input  _6,
  input  in_10,
  input  _7,
  input  in_12,
  input  Sift,
  input  _8,
  input  in_15,
  input  in_16,
  input  in_mem,
  input  in_18,
  input  [1:0] in_19,
  input  in_20,
  input  in_21,
  input  in_22,
  output [15:0] Rs,
  output [3:0] opcode,
  output [3:0] RD,
  output [3:0] RS_2,
  output [3:0] RT,
  output out_28,
  output [15:0] out_29,
  output [15:0] out_30,
  output [3:0] out_31
);

  wire and_1_out, and_2_out, bin_to_7segment_1_p2, bin_to_7segment_1_p3, bin_to_7segment_1_p4,
       bin_to_7segment_1_p5, bin_to_7segment_1_p6, bin_to_7segment_1_p7, bin_to_7segment_1_p8,
       bin_to_7segment_2_p3, bin_to_7segment_2_p4, bin_to_7segment_2_p5, bin_to_7segment_2_p6,
       bin_to_7segment_2_p7, bin_to_7segment_2_p8, bin_to_7segment_2_p9, bin_to_7segment_3_p2,
       bin_to_7segment_3_p3, bin_to_7segment_3_p4, bin_to_7segment_3_p5, bin_to_7segment_3_p6,
       bin_to_7segment_3_p7, bin_to_7segment_3_p8, bin_to_7segment_4_p2, bin_to_7segment_4_p3,
       bin_to_7segment_4_p4, bin_to_7segment_4_p5, bin_to_7segment_4_p6, bin_to_7segment_4_p7,
       bin_to_7segment_4_p8, bin_to_7segment_5_p2, bin_to_7segment_5_p3, bin_to_7segment_5_p4,
       bin_to_7segment_5_p5, bin_to_7segment_5_p6, bin_to_7segment_5_p7, bin_to_7segment_5_p8, blt_1_flag,
       clock_1_out, control_unit_1_p2, control_unit_1_p3, control_unit_1_p4, control_unit_1_p5,
       control_unit_1_p6, control_unit_1_p7, control_unit_1_p8, control_unit_1_p9, multiplexer_7_out,
       n16bit_to_bcd_1_p2, n16bit_to_bcd_1_p3, n16bit_to_bcd_1_p4, n16bit_to_bcd_1_p5, n16bit_to_bcd_1_p6;
  wire [3:0] multiplexer_4_out;
  wire [15:0] adder_1_out, adder_2_out, adder_3_out, bit_extender_1_out, bit_extender_2_out, input_1_out_11,
       multiplexer_1_out, multiplexer_2_out, multiplexer_3_out, multiplexer_6_out, multiplexer_9_out,
       n16_bit_alu_1_result, ram_1_data, register_1_q, register_2_q, register_3_out_8, shifter_1_output;

  \input  input_1 (
    ._0(_0), ._1(_1), ._2(_2), ._3(_3), ._4(_4), ._5(_5), ._6(_6), ._7(_7), ._8(_8), .in_10(in_16),
    .out_11(input_1_out_11));
  Register #(.width(16)) register_1 (.D(input_1_out_11), .Q(register_1_q), .clk(clock_1_out), .clr(in_8));  // open: en
  // demo_6_Control_Unit control_unit_1: pin names not known; wires that end beside it: opcode, control_unit_1_p2, control_unit_1_p3, control_unit_1_p4, control_unit_1_p5, control_unit_1_p6, control_unit_1_p7, control_unit_1_p8, control_unit_1_p9, in_19
  Register #(.width(16)) register_2 (.D(multiplexer_1_out), .Q(register_2_q), .clk(clock_1_out));  // open: en, clr
  Clock clock_1 (.out(clock_1_out));
  Multiplexer #(.width(16)) multiplexer_1 (
    .in0(multiplexer_2_out), .in1(adder_3_out), .out(multiplexer_1_out), .sel(control_unit_1_p9));  // open: en
  Multiplexer #(.width(16)) multiplexer_2 (
    .in0(adder_1_out), .in1(adder_2_out), .out(multiplexer_2_out), .sel(multiplexer_7_out));  // open: en
  Adder #(.width(16)) adder_1 (.a(register_2_q), .b(16'h1), .out(adder_1_out));  // open: cin, cout
  Multiplexer #(.width(16)) multiplexer_3 (
    .in0(out_30), .in1(register_1_q), .out(multiplexer_3_out), .sel(in_mem));  // open: en
  ROM #(.addrWidth(16), .dataWidth(16)) rom_1 (.addr(register_2_q), .data({opcode, RD, RS_2, out_31}));  // open: sel
  Multiplexer #(.width(4)) multiplexer_4 (.in0(RD), .in1(out_31), .out(multiplexer_4_out), .sel(in_15));  // open: en
  register register_3 (
    .in_1(clock_1_out), .in_2(multiplexer_3_out), .RegWrite(control_unit_1_p2), .out_7(Rs), .RS(RS_2),
    .RD(RD), .out_8(register_3_out_8), .RT(multiplexer_4_out));
  assign bit_extender_1_out = {{12{1'b0}}, out_31};  // Bit_Extender bit_extender_1
  Adder #(.width(16)) adder_2 (.a(adder_1_out), .b(bit_extender_1_out), .out(adder_2_out));  // open: cin, cout
  _16_bit_ALU u_16_bit_alu_1 (
    .A_invert(in_22), .B_invert(control_unit_1_p4), .Cin(control_unit_1_p4), .in_4(Rs), .in_5(out_29),
    .Operation(in_19), .Result(n16_bit_alu_1_result), .out_8(out_28));  // open: out_9
  Multiplexer #(.width(16)) multiplexer_5 (
    .in0(register_3_out_8), .in1(bit_extender_1_out), .out(out_29), .sel(control_unit_1_p3));  // open: en
  Shifter shifter_1 (.Shift_Amount(out_31), .sll_srl(in_18), .Input(Rs), .Output(shifter_1_output));
  Blt blt_1 (.A(out_29), .B(Rs), .Flag(blt_1_flag));
  RAM #(.addrWidth(16), .dataWidth(16), .bus("separate")) ram_1 (
    .addr(n16_bit_alu_1_result), .din(register_3_out_8), .data(ram_1_data), .str(control_unit_1_p6),
    .sel(control_unit_1_p7), .clk(clock_1_out), .ld(control_unit_1_p5), .clr(in_10));
  assign bit_extender_2_out = {{4{1'b0}}, {RD, RS_2, out_31}};  // Bit_Extender bit_extender_2
  and and_1 (and_1_out, in_20, out_28);
  and and_2 (and_2_out, in_20, blt_1_flag);
  Multiplexer #(.width(16)) multiplexer_6 (
    .in0(n16_bit_alu_1_result), .in1(ram_1_data), .out(multiplexer_6_out), .sel(control_unit_1_p8));  // open: en
  Adder #(.width(16)) adder_3 (.a(bit_extender_2_out), .b(adder_1_out), .out(adder_3_out));  // open: cin, cout
  Multiplexer multiplexer_7 (.in0(and_1_out), .in1(and_2_out), .out(multiplexer_7_out), .sel(blt_beq));  // open: en
  Multiplexer #(.width(16)) multiplexer_8 (
    .in0(multiplexer_6_out), .in1(shifter_1_output), .out(out_30), .sel(Sift));  // open: en
  Multiplexer #(.width(16)) multiplexer_9 (
    .in1(multiplexer_6_out), .out(multiplexer_9_out), .sel(in_12));  // open: in0, en
  // _16bit_to_BCD 16bit_to_bcd_1: pin names not known; wires that end beside it: multiplexer_9_out, n16bit_to_bcd_1_p2, n16bit_to_bcd_1_p3, n16bit_to_bcd_1_p4, n16bit_to_bcd_1_p5, n16bit_to_bcd_1_p6
  // Bin_to_7Segment bin_to_7segment_1: pin names not known; wires that end beside it: n16bit_to_bcd_1_p2, bin_to_7segment_1_p2, bin_to_7segment_1_p3, bin_to_7segment_1_p4, bin_to_7segment_1_p5, bin_to_7segment_1_p6, bin_to_7segment_1_p7, bin_to_7segment_1_p8
  _7_Segment_Display u_7_segment_display_1 (
    .g(bin_to_7segment_1_p8), .f(bin_to_7segment_1_p7), .a(bin_to_7segment_1_p2), .b(bin_to_7segment_1_p3),
    .e(bin_to_7segment_1_p6), .d(bin_to_7segment_1_p5), .c(bin_to_7segment_1_p4));  // open: dp
  // Bin_to_7Segment bin_to_7segment_2: pin names not known; wires that end beside it: n16bit_to_bcd_1_p3, n16bit_to_bcd_1_p3, bin_to_7segment_2_p3, bin_to_7segment_2_p4, bin_to_7segment_2_p5, bin_to_7segment_2_p6, bin_to_7segment_2_p7, bin_to_7segment_2_p8, bin_to_7segment_2_p9
  _7_Segment_Display u_7_segment_display_2 (
    .g(bin_to_7segment_2_p9), .f(bin_to_7segment_2_p8), .a(bin_to_7segment_2_p3), .b(bin_to_7segment_2_p4),
    .e(bin_to_7segment_2_p7), .d(bin_to_7segment_2_p6), .c(bin_to_7segment_2_p5));  // open: dp
  // Bin_to_7Segment bin_to_7segment_3: pin names not known; wires that end beside it: n16bit_to_bcd_1_p4, bin_to_7segment_3_p2, bin_to_7segment_3_p3, bin_to_7segment_3_p4, bin_to_7segment_3_p5, bin_to_7segment_3_p6, bin_to_7segment_3_p7, bin_to_7segment_3_p8
  _7_Segment_Display u_7_segment_display_3 (
    .g(bin_to_7segment_3_p8), .f(bin_to_7segment_3_p7), .a(bin_to_7segment_3_p2), .b(bin_to_7segment_3_p3),
    .e(bin_to_7segment_3_p6), .d(bin_to_7segment_3_p5), .c(bin_to_7segment_3_p4));  // open: dp
  // Bin_to_7Segment bin_to_7segment_4: pin names not known; wires that end beside it: n16bit_to_bcd_1_p5, bin_to_7segment_4_p2, bin_to_7segment_4_p3, bin_to_7segment_4_p4, bin_to_7segment_4_p5, bin_to_7segment_4_p6, bin_to_7segment_4_p7, bin_to_7segment_4_p8
  // Bin_to_7Segment bin_to_7segment_5: pin names not known; wires that end beside it: n16bit_to_bcd_1_p6, bin_to_7segment_5_p2, bin_to_7segment_5_p3, bin_to_7segment_5_p4, bin_to_7segment_5_p5, bin_to_7segment_5_p6, bin_to_7segment_5_p7, bin_to_7segment_5_p8
  _7_Segment_Display u_7_segment_display_4 (
    .g(bin_to_7segment_4_p8), .f(bin_to_7segment_4_p7), .a(bin_to_7segment_4_p2), .b(bin_to_7segment_4_p3),
    .e(bin_to_7segment_4_p6), .d(bin_to_7segment_4_p5), .c(bin_to_7segment_4_p4));  // open: dp
  _7_Segment_Display u_7_segment_display_5 (
    .g(bin_to_7segment_5_p8), .f(bin_to_7segment_5_p7), .a(bin_to_7segment_5_p2), .b(bin_to_7segment_5_p3),
    .e(bin_to_7segment_5_p6), .d(bin_to_7segment_5_p5), .c(bin_to_7segment_5_p4));  // open: dp

  assign RT = out_31;

  // Notes on the sheet:
  //   9
  //   contents of rom_1 (hex, n*v repeats v):
  //   c346 2456 0 0 0 3456 0 c445 2345 231 3423
  //   R/I-Type
  //   Branch
  //   Rt
  //   ALU/Memory
  //   Group 8 Datapath
endmodule

module Datapath_2 (
  output [1:0] Op_code,
  output [1:0] RD,
  output [1:0] RS,
  output [1:0] RT
);

  Register #(.width(16)) register_1 ();  // open: D, en, Q, clk, clr
  ROM #(.addrWidth(16)) rom_1 (.data({Op_code, RD, RS, RT}));  // open: addr, sel

  // Notes on the sheet:
  //   contents of rom_1 (hex, n*v repeats v):
  //   42 54 23 5*0 45 56
endmodule

module Shifter (
  input  [3:0] Shift_Amount,
  input  sll_srl,
  input  [15:0] Input,
  output [15:0] Output
);

  wire multiplexer_1_out, multiplexer_2_out, multiplexer_3_out, multiplexer_4_out, multiplexer_5_out,
       multiplexer_6_out, multiplexer_7_out, multiplexer_8_out, multiplexer_9_out, multiplexer_10_out,
       multiplexer_11_out, multiplexer_12_out, multiplexer_13_out, multiplexer_14_out, multiplexer_15_out,
       multiplexer_16_out, multiplexer_17_out, multiplexer_18_out, multiplexer_19_out, multiplexer_20_out,
       multiplexer_21_out, multiplexer_22_out, multiplexer_23_out, multiplexer_24_out, multiplexer_25_out,
       multiplexer_26_out, multiplexer_27_out, multiplexer_28_out, multiplexer_29_out, multiplexer_30_out,
       multiplexer_31_out, multiplexer_32_out, multiplexer_33_out, multiplexer_34_out, multiplexer_35_out,
       multiplexer_36_out, multiplexer_37_out, multiplexer_38_out, multiplexer_39_out, multiplexer_40_out,
       multiplexer_41_out, multiplexer_42_out, multiplexer_43_out, multiplexer_44_out, multiplexer_45_out,
       multiplexer_46_out, multiplexer_47_out, multiplexer_48_out, multiplexer_49_out, multiplexer_50_out,
       multiplexer_51_out, multiplexer_52_out, multiplexer_53_out, multiplexer_54_out, multiplexer_55_out,
       multiplexer_56_out, multiplexer_57_out, multiplexer_58_out, multiplexer_59_out, multiplexer_60_out,
       multiplexer_61_out, multiplexer_62_out, multiplexer_63_out, multiplexer_64_out, multiplexer_65_out,
       multiplexer_66_out, multiplexer_67_out, multiplexer_68_out, multiplexer_69_out, multiplexer_70_out,
       multiplexer_71_out, multiplexer_72_out, multiplexer_73_out, multiplexer_74_out, multiplexer_75_out,
       multiplexer_76_out, multiplexer_77_out, multiplexer_78_out, multiplexer_79_out, multiplexer_80_out,
       multiplexer_81_out, multiplexer_82_out, multiplexer_83_out, multiplexer_84_out, multiplexer_85_out,
       multiplexer_86_out, multiplexer_87_out, multiplexer_88_out, multiplexer_89_out, multiplexer_90_out,
       multiplexer_91_out, multiplexer_92_out, multiplexer_93_out, multiplexer_94_out, multiplexer_95_out,
       multiplexer_96_out;
  wire [15:0] multiplexer_112_out, multiplexer_113_out;

  Multiplexer multiplexer_1 (
    .in0(Input[15]), .in1(Input[14]), .out(multiplexer_1_out), .sel(Shift_Amount[0]));  // open: en
  Multiplexer multiplexer_2 (
    .in0(Input[14]), .in1(Input[13]), .out(multiplexer_2_out), .sel(Shift_Amount[0]));  // open: en
  Multiplexer multiplexer_3 (
    .in0(Input[13]), .in1(Input[12]), .out(multiplexer_3_out), .sel(Shift_Amount[0]));  // open: en
  Multiplexer multiplexer_4 (
    .in0(Input[12]), .in1(Input[11]), .out(multiplexer_4_out), .sel(Shift_Amount[0]));  // open: en
  Multiplexer multiplexer_5 (
    .in0(Input[11]), .in1(Input[10]), .out(multiplexer_5_out), .sel(Shift_Amount[0]));  // open: en
  Multiplexer multiplexer_6 (
    .in0(Input[10]), .in1(Input[9]), .out(multiplexer_6_out), .sel(Shift_Amount[0]));  // open: en
  Multiplexer multiplexer_7 (
    .in0(Input[9]), .in1(Input[8]), .out(multiplexer_7_out), .sel(Shift_Amount[0]));  // open: en
  Multiplexer multiplexer_8 (
    .in0(Input[8]), .in1(Input[7]), .out(multiplexer_8_out), .sel(Shift_Amount[0]));  // open: en
  Multiplexer multiplexer_9 (
    .in0(Input[7]), .in1(Input[6]), .out(multiplexer_9_out), .sel(Shift_Amount[0]));  // open: en
  Multiplexer multiplexer_10 (
    .in0(Input[6]), .in1(Input[5]), .out(multiplexer_10_out), .sel(Shift_Amount[0]));  // open: en
  Multiplexer multiplexer_11 (
    .in0(Input[5]), .in1(Input[4]), .out(multiplexer_11_out), .sel(Shift_Amount[0]));  // open: en
  Multiplexer multiplexer_12 (
    .in0(Input[4]), .in1(Input[3]), .out(multiplexer_12_out), .sel(Shift_Amount[0]));  // open: en
  Multiplexer multiplexer_13 (
    .in0(Input[3]), .in1(Input[2]), .out(multiplexer_13_out), .sel(Shift_Amount[0]));  // open: en
  Multiplexer multiplexer_14 (
    .in0(Input[2]), .in1(Input[1]), .out(multiplexer_14_out), .sel(Shift_Amount[0]));  // open: en
  Multiplexer multiplexer_15 (
    .in0(Input[1]), .in1(Input[0]), .out(multiplexer_15_out), .sel(Shift_Amount[0]));  // open: en
  Multiplexer multiplexer_16 (.in0(Input[0]), .in1(1'b0), .out(multiplexer_16_out), .sel(Shift_Amount[0]));  // open: en
  Multiplexer multiplexer_17 (
    .in0(Input[0]), .in1(Input[8]), .out(multiplexer_17_out), .sel(Shift_Amount[3]));  // open: en
  Multiplexer multiplexer_18 (
    .in0(Input[1]), .in1(Input[9]), .out(multiplexer_18_out), .sel(Shift_Amount[3]));  // open: en
  Multiplexer multiplexer_19 (
    .in0(Input[2]), .in1(Input[10]), .out(multiplexer_19_out), .sel(Shift_Amount[3]));  // open: en
  Multiplexer multiplexer_20 (
    .in0(Input[3]), .in1(Input[11]), .out(multiplexer_20_out), .sel(Shift_Amount[3]));  // open: en
  Multiplexer multiplexer_21 (
    .in0(Input[4]), .in1(Input[12]), .out(multiplexer_21_out), .sel(Shift_Amount[3]));  // open: en
  Multiplexer multiplexer_22 (
    .in0(Input[5]), .in1(Input[13]), .out(multiplexer_22_out), .sel(Shift_Amount[3]));  // open: en
  Multiplexer multiplexer_23 (
    .in0(Input[6]), .in1(Input[14]), .out(multiplexer_23_out), .sel(Shift_Amount[3]));  // open: en
  Multiplexer multiplexer_24 (
    .in0(Input[7]), .in1(Input[15]), .out(multiplexer_24_out), .sel(Shift_Amount[3]));  // open: en
  Multiplexer multiplexer_25 (.in0(Input[8]), .in1(1'b0), .out(multiplexer_25_out), .sel(Shift_Amount[3]));  // open: en
  Multiplexer multiplexer_26 (.in0(Input[9]), .in1(1'b0), .out(multiplexer_26_out), .sel(Shift_Amount[3]));  // open: en
  Multiplexer multiplexer_27 (
    .in0(Input[10]), .in1(1'b0), .out(multiplexer_27_out), .sel(Shift_Amount[3]));  // open: en
  Multiplexer multiplexer_28 (
    .in0(Input[11]), .in1(1'b0), .out(multiplexer_28_out), .sel(Shift_Amount[3]));  // open: en
  Multiplexer multiplexer_29 (
    .in0(Input[12]), .in1(1'b0), .out(multiplexer_29_out), .sel(Shift_Amount[3]));  // open: en
  Multiplexer multiplexer_30 (
    .in0(Input[13]), .in1(1'b0), .out(multiplexer_30_out), .sel(Shift_Amount[3]));  // open: en
  Multiplexer multiplexer_31 (
    .in0(Input[14]), .in1(1'b0), .out(multiplexer_31_out), .sel(Shift_Amount[3]));  // open: en
  Multiplexer multiplexer_32 (
    .in0(Input[15]), .in1(1'b0), .out(multiplexer_32_out), .sel(Shift_Amount[3]));  // open: en
  Multiplexer multiplexer_33 (
    .in0(multiplexer_1_out), .in1(multiplexer_3_out), .out(multiplexer_33_out), .sel(Shift_Amount[1]));  // open: en
  Multiplexer multiplexer_34 (
    .in0(multiplexer_2_out), .in1(multiplexer_4_out), .out(multiplexer_34_out), .sel(Shift_Amount[1]));  // open: en
  Multiplexer multiplexer_35 (
    .in0(multiplexer_3_out), .in1(multiplexer_5_out), .out(multiplexer_35_out), .sel(Shift_Amount[1]));  // open: en
  Multiplexer multiplexer_36 (
    .in0(multiplexer_4_out), .in1(multiplexer_6_out), .out(multiplexer_36_out), .sel(Shift_Amount[1]));  // open: en
  Multiplexer multiplexer_37 (
    .in0(multiplexer_5_out), .in1(multiplexer_7_out), .out(multiplexer_37_out), .sel(Shift_Amount[1]));  // open: en
  Multiplexer multiplexer_38 (
    .in0(multiplexer_6_out), .in1(multiplexer_8_out), .out(multiplexer_38_out), .sel(Shift_Amount[1]));  // open: en
  Multiplexer multiplexer_39 (
    .in0(multiplexer_7_out), .in1(multiplexer_9_out), .out(multiplexer_39_out), .sel(Shift_Amount[1]));  // open: en
  Multiplexer multiplexer_40 (
    .in0(multiplexer_8_out), .in1(multiplexer_10_out), .out(multiplexer_40_out), .sel(Shift_Amount[1]));  // open: en
  Multiplexer multiplexer_41 (
    .in0(multiplexer_9_out), .in1(multiplexer_11_out), .out(multiplexer_41_out), .sel(Shift_Amount[1]));  // open: en
  Multiplexer multiplexer_42 (
    .in0(multiplexer_10_out), .in1(multiplexer_12_out), .out(multiplexer_42_out), .sel(Shift_Amount[1]));  // open: en
  Multiplexer multiplexer_43 (
    .in0(multiplexer_11_out), .in1(multiplexer_13_out), .out(multiplexer_43_out), .sel(Shift_Amount[1]));  // open: en
  Multiplexer multiplexer_44 (
    .in0(multiplexer_12_out), .in1(multiplexer_14_out), .out(multiplexer_44_out), .sel(Shift_Amount[1]));  // open: en
  Multiplexer multiplexer_45 (
    .in0(multiplexer_13_out), .in1(multiplexer_15_out), .out(multiplexer_45_out), .sel(Shift_Amount[1]));  // open: en
  Multiplexer multiplexer_46 (
    .in0(multiplexer_14_out), .in1(multiplexer_16_out), .out(multiplexer_46_out), .sel(Shift_Amount[1]));  // open: en
  Multiplexer multiplexer_47 (
    .in0(multiplexer_15_out), .in1(1'b0), .out(multiplexer_47_out), .sel(Shift_Amount[1]));  // open: en
  Multiplexer multiplexer_48 (
    .in0(multiplexer_16_out), .in1(1'b0), .out(multiplexer_48_out), .sel(Shift_Amount[1]));  // open: en
  Multiplexer multiplexer_49 (
    .in0(multiplexer_17_out), .in1(multiplexer_21_out), .out(multiplexer_49_out), .sel(Shift_Amount[2]));  // open: en
  Multiplexer multiplexer_50 (
    .in0(multiplexer_18_out), .in1(multiplexer_22_out), .out(multiplexer_50_out), .sel(Shift_Amount[2]));  // open: en
  Multiplexer multiplexer_51 (
    .in0(multiplexer_19_out), .in1(multiplexer_23_out), .out(multiplexer_51_out), .sel(Shift_Amount[2]));  // open: en
  Multiplexer multiplexer_52 (
    .in0(multiplexer_20_out), .in1(multiplexer_24_out), .out(multiplexer_52_out), .sel(Shift_Amount[2]));  // open: en
  Multiplexer multiplexer_53 (
    .in0(multiplexer_21_out), .in1(multiplexer_25_out), .out(multiplexer_53_out), .sel(Shift_Amount[2]));  // open: en
  Multiplexer multiplexer_54 (
    .in0(multiplexer_22_out), .in1(multiplexer_26_out), .out(multiplexer_54_out), .sel(Shift_Amount[2]));  // open: en
  Multiplexer multiplexer_55 (
    .in0(multiplexer_23_out), .in1(multiplexer_27_out), .out(multiplexer_55_out), .sel(Shift_Amount[2]));  // open: en
  Multiplexer multiplexer_56 (
    .in0(multiplexer_24_out), .in1(multiplexer_28_out), .out(multiplexer_56_out), .sel(Shift_Amount[2]));  // open: en
  Multiplexer multiplexer_57 (
    .in0(multiplexer_25_out), .in1(multiplexer_29_out), .out(multiplexer_57_out), .sel(Shift_Amount[2]));  // open: en
  Multiplexer multiplexer_58 (
    .in0(multiplexer_26_out), .in1(multiplexer_30_out), .out(multiplexer_58_out), .sel(Shift_Amount[2]));  // open: en
  Multiplexer multiplexer_59 (
    .in0(multiplexer_27_out), .in1(multiplexer_31_out), .out(multiplexer_59_out), .sel(Shift_Amount[2]));  // open: en
  Multiplexer multiplexer_60 (
    .in0(multiplexer_28_out), .in1(multiplexer_32_out), .out(multiplexer_60_out), .sel(Shift_Amount[2]));  // open: en
  Multiplexer multiplexer_61 (
    .in0(multiplexer_29_out), .in1(1'b0), .out(multiplexer_61_out), .sel(Shift_Amount[2]));  // open: en
  Multiplexer multiplexer_62 (
    .in0(multiplexer_30_out), .in1(1'b0), .out(multiplexer_62_out), .sel(Shift_Amount[2]));  // open: en
  Multiplexer multiplexer_63 (
    .in0(multiplexer_31_out), .in1(1'b0), .out(multiplexer_63_out), .sel(Shift_Amount[2]));  // open: en
  Multiplexer multiplexer_64 (
    .in0(multiplexer_32_out), .in1(1'b0), .out(multiplexer_64_out), .sel(Shift_Amount[2]));  // open: en
  Multiplexer multiplexer_65 (
    .in0(multiplexer_33_out), .in1(multiplexer_37_out), .out(multiplexer_65_out), .sel(Shift_Amount[2]));  // open: en
  Multiplexer multiplexer_66 (
    .in0(multiplexer_34_out), .in1(multiplexer_38_out), .out(multiplexer_66_out), .sel(Shift_Amount[2]));  // open: en
  Multiplexer multiplexer_67 (
    .in0(multiplexer_35_out), .in1(multiplexer_39_out), .out(multiplexer_67_out), .sel(Shift_Amount[2]));  // open: en
  Multiplexer multiplexer_68 (
    .in0(multiplexer_36_out), .in1(multiplexer_40_out), .out(multiplexer_68_out), .sel(Shift_Amount[2]));  // open: en
  Multiplexer multiplexer_69 (
    .in0(multiplexer_37_out), .in1(multiplexer_41_out), .out(multiplexer_69_out), .sel(Shift_Amount[2]));  // open: en
  Multiplexer multiplexer_70 (
    .in0(multiplexer_38_out), .in1(multiplexer_42_out), .out(multiplexer_70_out), .sel(Shift_Amount[2]));  // open: en
  Multiplexer multiplexer_71 (
    .in0(multiplexer_39_out), .in1(multiplexer_43_out), .out(multiplexer_71_out), .sel(Shift_Amount[2]));  // open: en
  Multiplexer multiplexer_72 (
    .in0(multiplexer_40_out), .in1(multiplexer_44_out), .out(multiplexer_72_out), .sel(Shift_Amount[2]));  // open: en
  Multiplexer multiplexer_73 (
    .in0(multiplexer_41_out), .in1(multiplexer_45_out), .out(multiplexer_73_out), .sel(Shift_Amount[2]));  // open: en
  Multiplexer multiplexer_74 (
    .in0(multiplexer_42_out), .in1(multiplexer_46_out), .out(multiplexer_74_out), .sel(Shift_Amount[2]));  // open: en
  Multiplexer multiplexer_75 (
    .in0(multiplexer_43_out), .in1(multiplexer_47_out), .out(multiplexer_75_out), .sel(Shift_Amount[2]));  // open: en
  Multiplexer multiplexer_76 (
    .in0(multiplexer_44_out), .in1(multiplexer_48_out), .out(multiplexer_76_out), .sel(Shift_Amount[2]));  // open: en
  Multiplexer multiplexer_77 (
    .in0(multiplexer_45_out), .in1(1'b0), .out(multiplexer_77_out), .sel(Shift_Amount[2]));  // open: en
  Multiplexer multiplexer_78 (
    .in0(multiplexer_46_out), .in1(1'b0), .out(multiplexer_78_out), .sel(Shift_Amount[2]));  // open: en
  Multiplexer multiplexer_79 (
    .in0(multiplexer_47_out), .in1(1'b0), .out(multiplexer_79_out), .sel(Shift_Amount[2]));  // open: en
  Multiplexer multiplexer_80 (
    .in0(multiplexer_48_out), .in1(1'b0), .out(multiplexer_80_out), .sel(Shift_Amount[2]));  // open: en
  Multiplexer multiplexer_81 (
    .in0(multiplexer_49_out), .in1(multiplexer_51_out), .out(multiplexer_81_out), .sel(Shift_Amount[1]));  // open: en
  Multiplexer multiplexer_82 (
    .in0(multiplexer_50_out), .in1(multiplexer_52_out), .out(multiplexer_82_out), .sel(Shift_Amount[1]));  // open: en
  Multiplexer multiplexer_83 (
    .in0(multiplexer_51_out), .in1(multiplexer_53_out), .out(multiplexer_83_out), .sel(Shift_Amount[1]));  // open: en
  Multiplexer multiplexer_84 (
    .in0(multiplexer_52_out), .in1(multiplexer_54_out), .out(multiplexer_84_out), .sel(Shift_Amount[1]));  // open: en
  Multiplexer multiplexer_85 (
    .in0(multiplexer_53_out), .in1(multiplexer_55_out), .out(multiplexer_85_out), .sel(Shift_Amount[1]));  // open: en
  Multiplexer multiplexer_86 (
    .in0(multiplexer_54_out), .in1(multiplexer_56_out), .out(multiplexer_86_out), .sel(Shift_Amount[1]));  // open: en
  Multiplexer multiplexer_87 (
    .in0(multiplexer_55_out), .in1(multiplexer_57_out), .out(multiplexer_87_out), .sel(Shift_Amount[1]));  // open: en
  Multiplexer multiplexer_88 (
    .in0(multiplexer_56_out), .in1(multiplexer_58_out), .out(multiplexer_88_out), .sel(Shift_Amount[1]));  // open: en
  Multiplexer multiplexer_89 (
    .in0(multiplexer_57_out), .in1(multiplexer_59_out), .out(multiplexer_89_out), .sel(Shift_Amount[1]));  // open: en
  Multiplexer multiplexer_90 (
    .in0(multiplexer_58_out), .in1(multiplexer_60_out), .out(multiplexer_90_out), .sel(Shift_Amount[1]));  // open: en
  Multiplexer multiplexer_91 (
    .in0(multiplexer_59_out), .in1(multiplexer_61_out), .out(multiplexer_91_out), .sel(Shift_Amount[1]));  // open: en
  Multiplexer multiplexer_92 (
    .in0(multiplexer_60_out), .in1(multiplexer_62_out), .out(multiplexer_92_out), .sel(Shift_Amount[1]));  // open: en
  Multiplexer multiplexer_93 (
    .in0(multiplexer_61_out), .in1(multiplexer_63_out), .out(multiplexer_93_out), .sel(Shift_Amount[1]));  // open: en
  Multiplexer multiplexer_94 (
    .in0(multiplexer_62_out), .in1(multiplexer_64_out), .out(multiplexer_94_out), .sel(Shift_Amount[1]));  // open: en
  Multiplexer multiplexer_95 (
    .in0(multiplexer_63_out), .in1(1'b0), .out(multiplexer_95_out), .sel(Shift_Amount[1]));  // open: en
  Multiplexer multiplexer_96 (
    .in0(multiplexer_64_out), .in1(1'b0), .out(multiplexer_96_out), .sel(Shift_Amount[1]));  // open: en
  Multiplexer multiplexer_97 (
    .in0(multiplexer_65_out), .in1(multiplexer_73_out), .out(multiplexer_112_out[15]), .sel(Shift_Amount[3]));  // open: en
  Multiplexer multiplexer_98 (
    .in0(multiplexer_66_out), .in1(multiplexer_74_out), .out(multiplexer_112_out[14]), .sel(Shift_Amount[3]));  // open: en
  Multiplexer multiplexer_99 (
    .in0(multiplexer_67_out), .in1(multiplexer_75_out), .out(multiplexer_112_out[13]), .sel(Shift_Amount[3]));  // open: en
  Multiplexer multiplexer_100 (
    .in0(multiplexer_68_out), .in1(multiplexer_76_out), .out(multiplexer_112_out[12]), .sel(Shift_Amount[3]));  // open: en
  Multiplexer multiplexer_101 (
    .in0(multiplexer_69_out), .in1(multiplexer_77_out), .out(multiplexer_112_out[11]), .sel(Shift_Amount[3]));  // open: en
  Multiplexer multiplexer_102 (
    .in0(multiplexer_70_out), .in1(multiplexer_78_out), .out(multiplexer_112_out[10]), .sel(Shift_Amount[3]));  // open: en
  Multiplexer multiplexer_103 (
    .in0(multiplexer_71_out), .in1(multiplexer_79_out), .out(multiplexer_112_out[9]), .sel(Shift_Amount[3]));  // open: en
  Multiplexer multiplexer_104 (
    .in0(multiplexer_72_out), .in1(multiplexer_80_out), .out(multiplexer_112_out[8]), .sel(Shift_Amount[3]));  // open: en
  Multiplexer multiplexer_105 (
    .in0(multiplexer_73_out), .in1(1'b0), .out(multiplexer_112_out[7]), .sel(Shift_Amount[3]));  // open: en
  Multiplexer multiplexer_106 (
    .in0(multiplexer_74_out), .in1(1'b0), .out(multiplexer_112_out[6]), .sel(Shift_Amount[3]));  // open: en
  Multiplexer multiplexer_107 (
    .in0(multiplexer_75_out), .in1(1'b0), .out(multiplexer_112_out[5]), .sel(Shift_Amount[3]));  // open: en
  Multiplexer multiplexer_108 (
    .in0(multiplexer_76_out), .in1(1'b0), .out(multiplexer_112_out[4]), .sel(Shift_Amount[3]));  // open: en
  Multiplexer multiplexer_109 (
    .in0(multiplexer_77_out), .in1(1'b0), .out(multiplexer_112_out[3]), .sel(Shift_Amount[3]));  // open: en
  Multiplexer multiplexer_110 (
    .in0(multiplexer_78_out), .in1(1'b0), .out(multiplexer_112_out[2]), .sel(Shift_Amount[3]));  // open: en
  Multiplexer multiplexer_111 (
    .in0(multiplexer_79_out), .in1(1'b0), .out(multiplexer_112_out[1]), .sel(Shift_Amount[3]));  // open: en
  Multiplexer multiplexer_112 (
    .in0(multiplexer_80_out), .in1(1'b0), .out(multiplexer_112_out[0]), .sel(Shift_Amount[3]));  // open: en
  Multiplexer multiplexer_113 (
    .in0(multiplexer_81_out), .in1(multiplexer_82_out), .out(multiplexer_113_out[0]), .sel(Shift_Amount[0]));  // open: en
  Multiplexer multiplexer_114 (
    .in0(multiplexer_82_out), .in1(multiplexer_83_out), .out(multiplexer_113_out[1]), .sel(Shift_Amount[0]));  // open: en
  Multiplexer multiplexer_115 (
    .in0(multiplexer_83_out), .in1(multiplexer_84_out), .out(multiplexer_113_out[2]), .sel(Shift_Amount[0]));  // open: en
  Multiplexer multiplexer_116 (
    .in0(multiplexer_84_out), .in1(multiplexer_85_out), .out(multiplexer_113_out[3]), .sel(Shift_Amount[0]));  // open: en
  Multiplexer multiplexer_117 (
    .in0(multiplexer_85_out), .in1(multiplexer_86_out), .out(multiplexer_113_out[4]), .sel(Shift_Amount[0]));  // open: en
  Multiplexer multiplexer_118 (
    .in0(multiplexer_86_out), .in1(multiplexer_87_out), .out(multiplexer_113_out[5]), .sel(Shift_Amount[0]));  // open: en
  Multiplexer multiplexer_119 (
    .in0(multiplexer_87_out), .in1(multiplexer_88_out), .out(multiplexer_113_out[6]), .sel(Shift_Amount[0]));  // open: en
  Multiplexer multiplexer_120 (
    .in0(multiplexer_88_out), .in1(multiplexer_89_out), .out(multiplexer_113_out[7]), .sel(Shift_Amount[0]));  // open: en
  Multiplexer multiplexer_121 (
    .in0(multiplexer_89_out), .in1(multiplexer_90_out), .out(multiplexer_113_out[8]), .sel(Shift_Amount[0]));  // open: en
  Multiplexer multiplexer_122 (
    .in0(multiplexer_90_out), .in1(multiplexer_91_out), .out(multiplexer_113_out[9]), .sel(Shift_Amount[0]));  // open: en
  Multiplexer multiplexer_123 (
    .in0(multiplexer_91_out), .in1(multiplexer_92_out), .out(multiplexer_113_out[10]), .sel(Shift_Amount[0]));  // open: en
  Multiplexer multiplexer_124 (
    .in0(multiplexer_92_out), .in1(multiplexer_93_out), .out(multiplexer_113_out[11]), .sel(Shift_Amount[0]));  // open: en
  Multiplexer multiplexer_125 (
    .in0(multiplexer_93_out), .in1(multiplexer_94_out), .out(multiplexer_113_out[12]), .sel(Shift_Amount[0]));  // open: en
  Multiplexer multiplexer_126 (
    .in0(multiplexer_94_out), .in1(multiplexer_95_out), .out(multiplexer_113_out[13]), .sel(Shift_Amount[0]));  // open: en
  Multiplexer multiplexer_127 (
    .in0(multiplexer_95_out), .in1(multiplexer_96_out), .out(multiplexer_113_out[14]), .sel(Shift_Amount[0]));  // open: en
  Multiplexer multiplexer_128 (
    .in0(multiplexer_96_out), .in1(1'b0), .out(multiplexer_113_out[15]), .sel(Shift_Amount[0]));  // open: en
  Multiplexer #(.width(16)) multiplexer_129 (
    .in0(multiplexer_112_out), .in1(multiplexer_113_out), .out(Output), .sel(sll_srl));  // open: en
endmodule

module Blt (
  input  [15:0] A,
  input  [15:0] B,
  output Flag
);

  wire and_1_out, and_2_out, and_3_out, and_4_out, and_5_out, and_6_out, and_7_out, and_8_out, and_9_out,
       and_10_out, and_11_out, and_12_out, and_13_out, and_14_out, and_15_out, and_16_out, not_1_out,
       not_2_out, not_3_out, not_4_out, not_5_out, not_6_out, not_7_out, not_8_out, not_9_out, not_10_out,
       not_11_out, not_12_out, not_13_out, not_14_out, not_15_out, not_16_out, or_1_out, or_2_out, or_3_out,
       or_4_out, or_5_out, or_6_out, xnor_1_out, xnor_2_out, xnor_3_out, xnor_4_out, xnor_5_out, xnor_6_out,
       xnor_7_out, xnor_8_out, xnor_9_out, xnor_10_out, xnor_11_out, xnor_12_out, xnor_13_out, xnor_14_out,
       xnor_15_out, xnor_16_out, xnor_17_out, xnor_18_out, xnor_19_out, xnor_20_out, xnor_21_out,
       xnor_22_out, xnor_23_out, xnor_24_out;

  xnor xnor_1 (xnor_1_out, A[15], B[15]);
  xnor xnor_2 (xnor_2_out, A[14], B[14]);
  not not_1 (not_1_out, A[13]);
  xnor xnor_3 (xnor_3_out, A[15], B[15]);
  xnor xnor_4 (xnor_4_out, A[14], B[14]);
  xnor xnor_5 (xnor_5_out, A[13], B[13]);
  not not_2 (not_2_out, A[12]);
  xnor xnor_6 (xnor_6_out, A[11], B[11]);
  xnor xnor_7 (xnor_7_out, A[10], B[10]);
  not not_3 (not_3_out, A[9]);
  xnor xnor_8 (xnor_8_out, A[11], B[11]);
  xnor xnor_9 (xnor_9_out, A[10], B[10]);
  xnor xnor_10 (xnor_10_out, A[9], B[9]);
  not not_4 (not_4_out, A[8]);
  not not_5 (not_5_out, A[7]);
  xnor xnor_11 (xnor_11_out, A[7], B[7]);
  not not_6 (not_6_out, A[6]);
  xnor xnor_12 (xnor_12_out, A[7], B[7]);
  xnor xnor_13 (xnor_13_out, A[6], B[6]);
  not not_7 (not_7_out, A[5]);
  xnor xnor_14 (xnor_14_out, A[7], B[7]);
  xnor xnor_15 (xnor_15_out, A[6], B[6]);
  xnor xnor_16 (xnor_16_out, A[5], B[5]);
  not not_8 (not_8_out, A[4]);
  not not_9 (not_9_out, A[3]);
  xnor xnor_17 (xnor_17_out, A[3], B[3]);
  not not_10 (not_10_out, A[2]);
  xnor xnor_18 (xnor_18_out, A[3], B[3]);
  xnor xnor_19 (xnor_19_out, A[2], B[2]);
  not not_11 (not_11_out, A[1]);
  xnor xnor_20 (xnor_20_out, A[3], B[3]);
  xnor xnor_21 (xnor_21_out, A[2], B[2]);
  xnor xnor_22 (xnor_22_out, A[1], B[1]);
  not not_12 (not_12_out, A[0]);
  not not_13 (not_13_out, A[15]);
  and and_1 (and_1_out, not_13_out, B[15]);
  xnor xnor_23 (xnor_23_out, A[15], B[15]);
  not not_14 (not_14_out, A[14]);
  and and_2 (and_2_out, xnor_23_out, not_14_out, B[14]);
  and and_3 (and_3_out, xnor_1_out, xnor_2_out, not_1_out, B[13]);
  and and_4 (and_4_out, xnor_3_out, xnor_4_out, xnor_5_out, not_2_out, B[12]);
  not not_15 (not_15_out, A[11]);
  and and_5 (and_5_out, not_15_out, B[11]);
  xnor xnor_24 (xnor_24_out, A[11], B[11]);
  not not_16 (not_16_out, A[10]);
  and and_6 (and_6_out, xnor_24_out, not_16_out, B[10]);
  and and_7 (and_7_out, xnor_6_out, xnor_7_out, not_3_out, B[9]);
  and and_8 (and_8_out, xnor_8_out, xnor_9_out, xnor_10_out, not_4_out, B[8]);
  and and_9 (and_9_out, not_5_out, B[7]);
  and and_10 (and_10_out, xnor_11_out, not_6_out, B[6]);
  and and_11 (and_11_out, xnor_12_out, xnor_13_out, not_7_out, B[5]);
  and and_12 (and_12_out, xnor_14_out, xnor_15_out, xnor_16_out, not_8_out, B[4]);
  and and_13 (and_13_out, not_9_out, B[3]);
  and and_14 (and_14_out, xnor_17_out, not_10_out, B[2]);
  and and_15 (and_15_out, xnor_18_out, xnor_19_out, not_11_out, B[1]);
  and and_16 (and_16_out, xnor_20_out, xnor_21_out, xnor_22_out, not_12_out, B[0]);
  or or_1 (or_1_out, and_1_out, and_2_out, and_3_out, and_4_out);
  or or_2 (or_2_out, and_5_out, and_6_out, and_7_out, and_8_out);
  or or_3 (or_3_out, and_9_out, and_10_out, and_11_out, and_12_out);
  or or_4 (or_4_out, and_13_out, and_14_out, and_15_out, and_16_out);
  or or_5 (or_5_out, or_1_out, or_2_out);
  or or_6 (or_6_out, or_3_out, or_4_out);
  or or_7 (Flag, or_5_out, or_6_out);
endmodule

module \input  (
  input  _0,
  input  _1,
  input  _2,
  input  _3,
  input  _4,
  input  _5,
  input  _6,
  input  _7,
  input  _8,
  input  in_10,
  output [15:0] out_11
);

  wire [3:0] or_1_out;

  or or_1 (or_1_out[0], _1, _3, _5, _7, in_10);
  or or_2 (or_1_out[1], _3, _2, _6, _7);
  or or_3 (or_1_out[2], _4, _5, _6, _7);
  or or_4 (or_1_out[3], _8, in_10);
  assign out_11 = {{12{1'b0}}, or_1_out};  // Bit_Extender bit_extender_1
  Register #(.width(16)) register_1 ();  // open: D, en, Q, clk, clr

  // Notes on the sheet:
  //   9
endmodule

module input_1 (
  input  _0,
  input  _1,
  input  _2,
  input  _3,
  input  _4,
  input  _5,
  input  _6,
  input  _7,
  input  _8,
  input  in_10,
  output out_11,
  output out_12,
  output out_13,
  output out_14
);

  or or_1 (out_11, _1, _3, _5, _7, in_10);
  or or_2 (out_12, _3, _2, _6, _7);
  or or_3 (out_13, _4, _5, _6, _7);
  or or_4 (out_14, _8, in_10);
  Register #(.width(16)) register_1 ();  // open: D, en, Q, clk, clr

  // Notes on the sheet:
  //   9
  //   0
  //   9
endmodule

module test (
  input  _0,
  input  _1,
  input  _2,
  input  _3,
  input  _4,
  input  in_6,
  input  _5,
  input  _6,
  input  _7,
  input  _8,
  input  in_11
);

  wire input_1_1_out_11, input_1_1_out_12, input_1_1_out_13, input_1_1_out_14, input_1_2_out_12,
       input_1_2_out_13, input_1_2_out_14;

  input_1 input_1_1 (
    ._0(_0), ._1(_1), ._2(_2), ._3(_3), ._4(_4), ._5(_5), ._6(_6), ._7(_7), ._8(_8), .in_10(in_11),
    .out_11(input_1_1_out_11), .out_12(input_1_1_out_12), .out_13(input_1_1_out_13), .out_14(input_1_1_out_14));
  input_1 input_1_2 (
    ._0(_0), ._1(_1), ._2(_2), ._3(_3), ._4(_4), ._5(_5), ._6(_6), ._7(_7), ._8(_8), .in_10(in_11),
    .out_11(input_1_1_out_14), .out_12(input_1_2_out_12), .out_13(input_1_2_out_13), .out_14(input_1_2_out_14));
  input_1 input_1_3 (
    ._0(_0), ._1(_1), ._2(_2), ._3(_3), ._4(_4), ._5(_5), ._6(_6), ._7(_7), ._8(_8), .in_10(in_11));  // open: out_11, out_12, out_13, out_14
  input_1 input_1_4 (
    ._0(_0), ._1(_1), ._2(_2), ._3(_3), ._4(_4), ._5(_5), ._6(_6), ._7(_7), ._8(_8), .in_10(in_11));  // open: out_11, out_12, out_13, out_14
  Multiplexer #(.select(4)) multiplexer_1 (
    .in0(input_1_1_out_11), .in1(input_1_1_out_12), .in2(input_1_1_out_13), .in3(input_1_1_out_14),
    .in4(input_1_1_out_14), .in5(input_1_2_out_12), .in6(input_1_2_out_13), .in7(input_1_2_out_14), .out(in_6));  // open: in8, in9, in10, in11, in12, in13, in14, in15, sel, en

  // Notes on the sheet:
  //   9
endmodule

module Datapath_Final (
  input  _0,
  input  _1,
  input  _2,
  input  _3,
  input  _4,
  input  _5,
  input  _6,
  input  in_8,
  input  ALU_Memory,
  input  _7,
  input  _8,
  input  in_12,
  output [15:0] out_13,
  output [15:0] out_14,
  output [3:0] out_15,
  output [15:0] Rs,
  output [15:0] out_17,
  output [3:0] opcode,
  output [3:0] RD,
  output [3:0] RS_2,
  output [3:0] RT,
  output out_22,
  output [15:0] out_23,
  output [3:0] out_24,
  output [15:0] out_25,
  output [3:0] out_26,
  output [15:0] out_27,
  output [3:0] out_28,
  output [3:0] out_29,
  output [15:0] out_30
);

  wire and_1_out, and_2_out, bin_to_7segment_1_p2, bin_to_7segment_1_p3, bin_to_7segment_1_p4,
       bin_to_7segment_1_p5, bin_to_7segment_1_p6, bin_to_7segment_1_p7, bin_to_7segment_1_p8,
       bin_to_7segment_2_p2, bin_to_7segment_2_p3, bin_to_7segment_2_p4, bin_to_7segment_2_p5,
       bin_to_7segment_2_p6, bin_to_7segment_2_p7, bin_to_7segment_2_p8, bin_to_7segment_3_p2,
       bin_to_7segment_3_p3, bin_to_7segment_3_p4, bin_to_7segment_3_p5, bin_to_7segment_3_p6,
       bin_to_7segment_3_p7, bin_to_7segment_3_p8, bin_to_7segment_4_p2, bin_to_7segment_4_p3,
       bin_to_7segment_4_p4, bin_to_7segment_4_p5, bin_to_7segment_4_p6, bin_to_7segment_4_p7,
       bin_to_7segment_4_p8, bin_to_7segment_5_p2, bin_to_7segment_5_p3, bin_to_7segment_5_p4,
       bin_to_7segment_5_p5, bin_to_7segment_5_p6, bin_to_7segment_5_p7, bin_to_7segment_5_p8, blt_1_flag,
       button_1_out, clock_1_out, control_unit_for_datapth_1_b_inv, control_unit_for_datapth_1_blt_beq,
       control_unit_for_datapth_1_branch, control_unit_for_datapth_1_in, control_unit_for_datapth_1_jump,
       control_unit_for_datapth_1_l_r, control_unit_for_datapth_1_lw, control_unit_for_datapth_1_mem_enable,
       control_unit_for_datapth_1_out, control_unit_for_datapth_1_out_17,
       control_unit_for_datapth_1_r_i_type, control_unit_for_datapth_1_rd_rt,
       control_unit_for_datapth_1_shift, control_unit_for_datapth_1_sw,
       control_unit_for_datapth_1_write_enable, controlled_buffer_1_out, multiplexer_9_out, not_1_out,
       or_1_out, or_2_out;
  wire [1:0] control_unit_for_datapth_1_alu_op;
  wire [3:0] multiplexer_5_out;
  wire [15:0] adder_1_out, adder_2_out, adder_3_out, bit_extender_1_out, bit_extender_2_out,
       bit_extender_3_out, bit_extender_4_out, input_1_out_11, multiplexer_1_out, multiplexer_3_out,
       multiplexer_4_out, multiplexer_6_out, multiplexer_8_out, n16_bit_alu_1_result, negator_2_out,
       ram_1_data, register_1_q, shifter_1_output;

  Button button_1 (.out(button_1_out));
  or or_1 (or_1_out, multiplexer_9_out, control_unit_for_datapth_1_jump);
  \input  input_1 (
    ._0(_0), ._1(_1), ._2(_2), ._3(_3), ._4(_4), ._5(_5), ._6(_6), ._7(_7), ._8(_8), .in_10(in_12),
    .out_11(input_1_out_11));
  not not_1 (not_1_out, control_unit_for_datapth_1_in);
  assign controlled_buffer_1_out = or_2_out ? clock_1_out : 1'bz;  // Controlled_Buffer controlled_buffer_1
  Clock clock_1 (.out(clock_1_out));
  or or_2 (or_2_out, button_1_out, not_1_out);
  control_unit_for_datapth control_unit_for_datapth_1 (
    .in_1(opcode), .RD_RT(control_unit_for_datapth_1_rd_rt),
    .Write_enable(control_unit_for_datapth_1_write_enable), .R_I_Type(control_unit_for_datapth_1_r_i_type),
    .ALU_OP(control_unit_for_datapth_1_alu_op), .B_inv(control_unit_for_datapth_1_b_inv),
    .lw(control_unit_for_datapth_1_lw), .sw(control_unit_for_datapth_1_sw),
    .Mem_Enable(control_unit_for_datapth_1_mem_enable), .Branch(control_unit_for_datapth_1_branch),
    .Jump(control_unit_for_datapth_1_jump), .L_R(control_unit_for_datapth_1_l_r),
    .Shift(control_unit_for_datapth_1_shift), .BLT_BEQ(control_unit_for_datapth_1_blt_beq),
    .In(control_unit_for_datapth_1_in), .Out(control_unit_for_datapth_1_out),
    .out_17(control_unit_for_datapth_1_out_17));
  Multiplexer #(.width(16)) multiplexer_1 (
    .in0(16'h1), .in1({16{1'b0}}), .out(multiplexer_1_out), .sel(or_1_out));  // open: en
  Register #(.width(16)) register_1 (.D(out_14), .Q(register_1_q), .clk(controlled_buffer_1_out));  // open: en, clr
  Multiplexer #(.width(16)) multiplexer_2 (
    .in0(multiplexer_3_out), .in1(adder_3_out), .out(out_14), .sel(control_unit_for_datapth_1_jump));  // open: en
  Multiplexer #(.width(16)) multiplexer_3 (
    .in0(adder_1_out), .in1(adder_2_out), .out(multiplexer_3_out), .sel(multiplexer_9_out));  // open: en
  Adder #(.width(16)) adder_1 (.a(register_1_q), .b(multiplexer_1_out), .out(adder_1_out));  // open: cin, cout
  Multiplexer #(.width(16)) multiplexer_4 (
    .in0(out_25), .in1(input_1_out_11), .out(multiplexer_4_out), .sel(control_unit_for_datapth_1_in));  // open: en
  ROM #(.addrWidth(16), .dataWidth(16)) rom_1 (.addr(register_1_q), .data({opcode, RD, RS_2, RT}));  // open: sel
  Multiplexer #(.width(4)) multiplexer_5 (
    .in0(RD), .in1(RT), .out(multiplexer_5_out), .sel(control_unit_for_datapth_1_rd_rt));  // open: en
  assign bit_extender_1_out = {{12{1'b0}}, RT};  // Bit_Extender bit_extender_1
  Multiplexer #(.width(16)) multiplexer_6 (
    .in0(bit_extender_1_out), .in1(out_30), .out(multiplexer_6_out), .sel(RT[3]));  // open: en
  register register_2 (
    .in_1(controlled_buffer_1_out), .in_2(multiplexer_4_out),
    .RegWrite(control_unit_for_datapth_1_write_enable), .out_7(Rs), .RS(RS_2), .RD(RD), .out_8(out_27),
    .RT(multiplexer_5_out));
  assign bit_extender_2_out = {{12{1'b0}}, {1'b0, RT[2:0]}};  // Bit_Extender bit_extender_2
  Adder #(.width(16)) adder_2 (.a(adder_1_out), .b(multiplexer_6_out), .out(adder_2_out));  // open: cin, cout
  _16_bit_ALU u_16_bit_alu_1 (
    .A_invert(in_8), .B_invert(control_unit_for_datapth_1_b_inv), .Cin(control_unit_for_datapth_1_b_inv),
    .in_4(Rs), .in_5(out_23), .Operation(control_unit_for_datapth_1_alu_op), .Result(n16_bit_alu_1_result),
    .out_8(out_22));  // open: out_9
  Multiplexer #(.width(16)) multiplexer_7 (
    .in0(out_27), .in1(multiplexer_6_out), .out(out_23), .sel(control_unit_for_datapth_1_r_i_type));  // open: en
  Negator #(.width(16)) negator_1 (.in(bit_extender_2_out), .out(out_30));
  Shifter shifter_1 (
    .Shift_Amount(RT), .sll_srl(control_unit_for_datapth_1_l_r), .Input(Rs), .Output(shifter_1_output));
  Blt blt_1 (.A(out_23), .B(Rs), .Flag(blt_1_flag));
  RAM #(.addrWidth(16), .dataWidth(16), .bus("separate")) ram_1 (
    .addr(n16_bit_alu_1_result), .din(out_27), .data(ram_1_data), .str(control_unit_for_datapth_1_sw),
    .sel(control_unit_for_datapth_1_mem_enable), .clk(controlled_buffer_1_out),
    .ld(control_unit_for_datapth_1_lw), .clr(ALU_Memory));
  assign bit_extender_3_out = {{4{1'b0}}, {RD, RS_2, RT}};  // Bit_Extender bit_extender_3
  and and_1 (and_1_out, control_unit_for_datapth_1_branch, out_22);
  and and_2 (and_2_out, control_unit_for_datapth_1_branch, blt_1_flag);
  Multiplexer #(.width(16)) multiplexer_8 (
    .in0(n16_bit_alu_1_result), .in1(ram_1_data), .out(multiplexer_8_out),
    .sel(control_unit_for_datapth_1_out_17));  // open: en
  assign bit_extender_4_out = {{4{1'b0}}, {1'b0, RD[2:0], RS_2, RT}};  // Bit_Extender bit_extender_4
  Multiplexer multiplexer_9 (
    .in0(and_1_out), .in1(and_2_out), .out(multiplexer_9_out), .sel(control_unit_for_datapth_1_blt_beq));  // open: en
  Negator #(.width(16)) negator_2 (.in(bit_extender_4_out), .out(negator_2_out));
  Multiplexer #(.width(16)) multiplexer_10 (
    .in0(multiplexer_8_out), .in1(shifter_1_output), .out(out_25), .sel(control_unit_for_datapth_1_shift));  // open: en
  Multiplexer #(.width(16)) multiplexer_11 (
    .in1(Rs), .out(out_17), .sel(control_unit_for_datapth_1_out));  // open: in0, en
  Adder #(.width(16)) adder_3 (.a(out_13), .b(adder_1_out), .out(adder_3_out));  // open: cin, cout
  // _16bit_to_BCD 16bit_to_bcd_1: pin names not known; wires that end beside it: out_17, out_15, out_24, out_26, out_28, out_29
  Multiplexer #(.width(16)) multiplexer_12 (
    .in0(bit_extender_3_out), .in1(negator_2_out), .out(out_13), .sel(RD[3]));  // open: en
  // Bin_to_7Segment bin_to_7segment_1: pin names not known; wires that end beside it: out_15, bin_to_7segment_1_p2, bin_to_7segment_1_p3, bin_to_7segment_1_p4, bin_to_7segment_1_p5, bin_to_7segment_1_p6, bin_to_7segment_1_p7, bin_to_7segment_1_p8
  _7_Segment_Display u_7_segment_display_1 (
    .g(bin_to_7segment_1_p8), .f(bin_to_7segment_1_p7), .a(bin_to_7segment_1_p2), .b(bin_to_7segment_1_p3),
    .e(bin_to_7segment_1_p6), .d(bin_to_7segment_1_p5), .c(bin_to_7segment_1_p4));  // open: dp
  // Bin_to_7Segment bin_to_7segment_2: pin names not known; wires that end beside it: out_24, bin_to_7segment_2_p2, bin_to_7segment_2_p3, bin_to_7segment_2_p4, bin_to_7segment_2_p5, bin_to_7segment_2_p6, bin_to_7segment_2_p7, bin_to_7segment_2_p8
  _7_Segment_Display u_7_segment_display_2 (
    .g(bin_to_7segment_2_p8), .f(bin_to_7segment_2_p7), .a(bin_to_7segment_2_p2), .b(bin_to_7segment_2_p3),
    .e(bin_to_7segment_2_p6), .d(bin_to_7segment_2_p5), .c(bin_to_7segment_2_p4));  // open: dp
  // Bin_to_7Segment bin_to_7segment_3: pin names not known; wires that end beside it: out_26, bin_to_7segment_3_p2, bin_to_7segment_3_p3, bin_to_7segment_3_p4, bin_to_7segment_3_p5, bin_to_7segment_3_p6, bin_to_7segment_3_p7, bin_to_7segment_3_p8
  _7_Segment_Display u_7_segment_display_3 (
    .g(bin_to_7segment_3_p8), .f(bin_to_7segment_3_p7), .a(bin_to_7segment_3_p2), .b(bin_to_7segment_3_p3),
    .e(bin_to_7segment_3_p6), .d(bin_to_7segment_3_p5), .c(bin_to_7segment_3_p4));  // open: dp
  // Bin_to_7Segment bin_to_7segment_4: pin names not known; wires that end beside it: out_28, bin_to_7segment_4_p2, bin_to_7segment_4_p3, bin_to_7segment_4_p4, bin_to_7segment_4_p5, bin_to_7segment_4_p6, bin_to_7segment_4_p7, bin_to_7segment_4_p8
  // Bin_to_7Segment bin_to_7segment_5: pin names not known; wires that end beside it: out_29, bin_to_7segment_5_p2, bin_to_7segment_5_p3, bin_to_7segment_5_p4, bin_to_7segment_5_p5, bin_to_7segment_5_p6, bin_to_7segment_5_p7, bin_to_7segment_5_p8
  _7_Segment_Display u_7_segment_display_4 (
    .g(bin_to_7segment_4_p8), .f(bin_to_7segment_4_p7), .a(bin_to_7segment_4_p2), .b(bin_to_7segment_4_p3),
    .e(bin_to_7segment_4_p6), .d(bin_to_7segment_4_p5), .c(bin_to_7segment_4_p4));  // open: dp
  _7_Segment_Display u_7_segment_display_5 (
    .g(bin_to_7segment_5_p8), .f(bin_to_7segment_5_p7), .a(bin_to_7segment_5_p2), .b(bin_to_7segment_5_p3),
    .e(bin_to_7segment_5_p6), .d(bin_to_7segment_5_p5), .c(bin_to_7segment_5_p4));  // open: dp

  // Notes on the sheet:
  //   Enter
  //   9
  //   contents of rom_1 (hex, n*v repeats v):
  //   b200 c020 b300 c030 1423 c040 200 c020 300 c030 400 c040
  //   in/mem
  //   R/I-Type
  //   Branch
  //   Rt
  //   blt/beq
  //   Sift
endmodule

module control_unit_for_datapth (
  input  [3:0] in_1,
  output RD_RT,
  output Write_enable,
  output R_I_Type,
  output [1:0] ALU_OP,
  output B_inv,
  output lw,
  output sw,
  output Mem_Enable,
  output Branch,
  output Jump,
  output L_R,
  output Shift,
  output BLT_BEQ,
  output In,
  output Out,
  output out_17
);

  wire and_1_out, and_2_out, and_3_out, and_4_out, and_5_out, and_6_out, and_7_out, and_8_out, and_9_out,
       and_10_out, and_11_out, and_12_out, and_13_out, and_14_out, and_17_out, and_18_out, and_19_out,
       and_20_out, and_23_out, and_24_out, not_1_out, not_2_out, not_3_out, not_4_out;

  not not_1 (not_1_out, in_1[3]);
  not not_2 (not_2_out, in_1[2]);
  not not_3 (not_3_out, in_1[1]);
  not not_4 (not_4_out, in_1[0]);
  and and_1 (and_1_out, not_2_out, not_3_out);
  and and_2 (and_2_out, not_2_out, not_3_out);
  and and_3 (and_3_out, not_2_out, in_1[0]);
  and and_4 (and_4_out, not_2_out, in_1[1], not_4_out);
  and and_5 (and_5_out, not_1_out, in_1[2], not_3_out, not_4_out);
  and and_6 (and_6_out, in_1[3], not_2_out, not_3_out, in_1[0]);
  and and_7 (and_7_out, in_1[1], not_4_out);
  and and_8 (and_8_out, not_2_out, not_3_out);
  and and_9 (and_9_out, in_1[2], in_1[1]);
  and and_10 (and_10_out, in_1[3], in_1[2], in_1[0]);
  and and_11 (and_11_out, not_1_out, in_1[2], not_3_out, in_1[0]);
  and and_12 (and_12_out, not_1_out, in_1[2], in_1[1], not_4_out);
  and and_13 (and_13_out, not_1_out, not_2_out, not_3_out, in_1[0]);
  and and_14 (and_14_out, in_1[3], in_1[2], not_3_out, in_1[0]);
  and and_15 (lw, in_1[3], not_2_out, not_3_out, in_1[0]);
  and and_16 (sw, in_1[3], not_2_out, in_1[1], not_4_out);
  and and_17 (and_17_out, in_1[3], not_2_out, not_3_out, in_1[0]);
  and and_18 (and_18_out, in_1[3], not_2_out, in_1[1], not_4_out);
  and and_19 (and_19_out, in_1[3], in_1[2], not_3_out, in_1[0]);
  and and_20 (and_20_out, in_1[3], in_1[2], in_1[1], not_4_out);
  and and_21 (Jump, in_1[3], in_1[2], in_1[1], in_1[0]);
  and and_22 (L_R, in_1[3], not_2_out, not_3_out, not_4_out);
  and and_23 (and_23_out, not_1_out, in_1[2], in_1[1], in_1[0]);
  and and_24 (and_24_out, in_1[3], not_2_out, not_3_out, not_4_out);
  and and_25 (BLT_BEQ, in_1[3], in_1[2], in_1[1], not_4_out);
  and and_26 (In, in_1[3], not_2_out, in_1[1], in_1[0]);
  and and_27 (Out, in_1[3], in_1[2], not_3_out, not_4_out);
  and and_28 (out_17, in_1[3], not_2_out, not_3_out, in_1[0]);
  or or_1 (ALU_OP[0], and_11_out, and_12_out);
  or or_2 (B_inv, and_13_out, and_14_out);
  or or_3 (Mem_Enable, and_17_out, and_18_out);
  or or_4 (Branch, and_19_out, and_20_out);
  or or_5 (Shift, and_23_out, and_24_out);
  or or_6 (RD_RT, and_1_out, not_1_out);
  or or_7 (Write_enable, not_1_out, and_2_out, and_3_out);
  or or_8 (R_I_Type, and_4_out, and_5_out, and_6_out);
  or or_9 (ALU_OP[1], and_7_out, and_8_out, and_9_out, and_10_out);

  // Notes on the sheet:
  //   A
  //   B
  //   C
  //   D
  //   Rsult Mem/AlU Mux
endmodule
